// Logisim project adder_4bit.circ as structural Verilog
module adder_4bit (
  input  A0,
  input  B0,
  input  A1,
  input  B1,
  input  A2,
  input  B2,
  input  A3,
  input  B3,
  input  Cin,
  output S0,
  output S1,
  output S2,
  output S3,
  output Cout
);

  wire FA1O2_out, FA2G1_out, FA2G2_out, FA2G3_out, FA2O1_out, FA2O2_out, FA2X1_out, FA3G1_out, FA3G2_out,
       FA3G3_out, FA3O1_out, FA3X1_out, TQ9, TQb, TQc, TQd, TQe, TQf, TQg, TQi, TQj, TQk, TQl;

  xor FA0X1 (TQ9, A0, B0);
  xor FA0X2 (S0, TQ9, Cin);
  and FA0G1 (TQb, B0, A0);
  and FA0G2 (TQc, A0, Cin);
  and FA0G3 (TQd, Cin, B0);
  or FA0O1 (TQe, TQb, TQc);
  or FA0O2 (TQf, TQe, TQd);
  xor FA1X1 (TQg, A1, B1);
  xor FA1X2 (S1, TQg, TQf);
  and FA1G1 (TQi, B1, A1);
  and FA1G2 (TQj, A1, TQf);
  and FA1G3 (TQk, TQf, B1);
  or FA1O1 (TQl, TQi, TQj);
  or FA1O2 (FA1O2_out, TQl, TQk);
  xor FA2X1 (FA2X1_out, A2, B2);
  xor FA2X2 (S2, FA2X1_out, FA1O2_out);
  and FA2G1 (FA2G1_out, B2, A2);
  and FA2G2 (FA2G2_out, A2, FA1O2_out);
  and FA2G3 (FA2G3_out, FA1O2_out, B2);
  or FA2O1 (FA2O1_out, FA2G1_out, FA2G2_out);
  or FA2O2 (FA2O2_out, FA2O1_out, FA2G3_out);
  xor FA3X1 (FA3X1_out, A3, B3);
  xor FA3X2 (S3, FA3X1_out, FA2O2_out);
  and FA3G1 (FA3G1_out, B3, A3);
  and FA3G2 (FA3G2_out, A3, FA2O2_out);
  and FA3G3 (FA3G3_out, FA2O2_out, B3);
  or FA3O1 (FA3O1_out, FA3G1_out, FA3G2_out);
  or FA3O2 (Cout, FA3O1_out, FA3G3_out);

  // Other names for the same wires on the sheet: TQ0 = A0; TQ1 = B0; TQ2 = A1; TQ3 = B1; TQ4 = A2; TQ5 = B2; TQ6 = A3;
  //   TQ7 = B3; TQ8 = Cin; TQa = S0; TQh = S1; TQm = S2; TQn = S3; TQo = Cout
endmodule
