// Logisim project adder_8bit.circ as structural Verilog
module adder_8bit (
  input  A0,
  input  B0,
  input  A1,
  input  B1,
  input  A2,
  input  B2,
  input  A3,
  input  B3,
  input  A4,
  input  B4,
  input  A5,
  input  B5,
  input  A6,
  input  B6,
  input  A7,
  input  B7,
  input  Cin,
  output S0,
  output S1,
  output S2,
  output S3,
  output S4,
  output S5,
  output S6,
  output S7,
  output Cout
);

  wire n18, n20, n21, n22, n23, n24, n25, n27, n28, n29, n30, n31, n32, n34, n35, n36, n37, n38, n39, n41,
       n42, n43, n44, n45, n46, n48, n49, n50, n51, n52, n53, n55, n56, n57, n58, n59, n60, n62, n63, n64,
       n65, n66, n67, n69, n70, n71, n72;

  xor FA0X1 (n18, A0, B0);
  xor FA0X2 (S0, n18, Cin);
  and FA0G1 (n20, B0, A0);
  and FA0G2 (n21, A0, Cin);
  and FA0G3 (n22, Cin, B0);
  or FA0O1 (n23, n20, n21);
  or FA0O2 (n24, n23, n22);
  xor FA1X1 (n25, A1, B1);
  xor FA1X2 (S1, n25, n24);
  and FA1G1 (n27, B1, A1);
  and FA1G2 (n28, A1, n24);
  and FA1G3 (n29, n24, B1);
  or FA1O1 (n30, n27, n28);
  or FA1O2 (n31, n30, n29);
  xor FA2X1 (n32, A2, B2);
  xor FA2X2 (S2, n32, n31);
  and FA2G1 (n34, B2, A2);
  and FA2G2 (n35, A2, n31);
  and FA2G3 (n36, n31, B2);
  or FA2O1 (n37, n34, n35);
  or FA2O2 (n38, n37, n36);
  xor FA3X1 (n39, A3, B3);
  xor FA3X2 (S3, n39, n38);
  and FA3G1 (n41, B3, A3);
  and FA3G2 (n42, A3, n38);
  and FA3G3 (n43, n38, B3);
  or FA3O1 (n44, n41, n42);
  or FA3O2 (n45, n44, n43);
  xor FA4X1 (n46, A4, B4);
  xor FA4X2 (S4, n46, n45);
  and FA4G1 (n48, B4, A4);
  and FA4G2 (n49, A4, n45);
  and FA4G3 (n50, n45, B4);
  or FA4O1 (n51, n48, n49);
  or FA4O2 (n52, n51, n50);
  xor FA5X1 (n53, A5, B5);
  xor FA5X2 (S5, n53, n52);
  and FA5G1 (n55, B5, A5);
  and FA5G2 (n56, A5, n52);
  and FA5G3 (n57, n52, B5);
  or FA5O1 (n58, n55, n56);
  or FA5O2 (n59, n58, n57);
  xor FA6X1 (n60, A6, B6);
  xor FA6X2 (S6, n60, n59);
  and FA6G1 (n62, B6, A6);
  and FA6G2 (n63, A6, n59);
  and FA6G3 (n64, n59, B6);
  or FA6O1 (n65, n62, n63);
  or FA6O2 (n66, n65, n64);
  xor FA7X1 (n67, A7, B7);
  xor FA7X2 (S7, n67, n66);
  and FA7G1 (n69, B7, A7);
  and FA7G2 (n70, A7, n66);
  and FA7G3 (n71, n66, B7);
  or FA7O1 (n72, n69, n70);
  or FA7O2 (Cout, n72, n71);

  // Other names for the same wires on the sheet: n1 = A0; n2 = B0; n3 = A1; n4 = B1; n5 = A2; n6 = B2; n7 = A3;
  //   n8 = B3; n9 = A4; n10 = B4; n11 = A5; n12 = B5; n13 = A6; n14 = B6; n15 = A7; n16 = B7; n17 = Cin; n19 = S0;
  //   n26 = S1; n33 = S2; n40 = S3; n47 = S4; n54 = S5; n61 = S6; n68 = S7; n73 = Cout
endmodule
