// Logisim project alu_1bit.circ as structural Verilog
module alu_1bit (
  input  A0,
  input  B0,
  input  S1,
  input  S0,
  input  Cin,
  output R0,
  output Cout,
  output Z
);

  wire ALU0CS_out, ALU0CSN_out, ALU0M1_out, ALU0M1A_out, ALU0M2_out, ALU0M2A_out, ALU0M3_out, ALU0MO1_out,
       ALU0N1_out, ALU0N2_out, ALU0SS_out, TQ3, TQ4, TQ5, TQ6, TQ7, TQ8, TQ9, TQa, TQb, TQc;

  and ALU0A (TQb, A0, B0);
  or ALU0O (TQc, B0, A0);
  xor ALU0X1 (TQ3, A0, TQ9);
  xor ALU0X2 (TQa, TQ3, TQ4);
  and ALU0G1 (TQ5, A0, TQ9);
  and ALU0G2 (TQ6, A0, TQ4);
  and ALU0G3 (TQ7, TQ3, TQ4);
  or ALU0C1 (TQ8, TQ5, TQ6);
  or ALU0C2 (Cout, TQ8, TQ7);
  and ALU0SS (ALU0SS_out, S1, S0);
  xor ALU0BX (TQ9, ALU0SS_out, B0);
  not ALU0N1 (ALU0N1_out, S1);
  not ALU0N2 (ALU0N2_out, S0);
  and ALU0M1A (ALU0M1A_out, TQb, ALU0N1_out);
  and ALU0M2A (ALU0M2A_out, TQc, ALU0N1_out);
  and ALU0M1 (ALU0M1_out, ALU0M1A_out, ALU0N2_out);
  and ALU0M2 (ALU0M2_out, ALU0M2A_out, S0);
  and ALU0M3 (ALU0M3_out, TQa, S1);
  or ALU0MO1 (ALU0MO1_out, ALU0M1_out, ALU0M2_out);
  or ALU0MO2 (R0, ALU0MO1_out, ALU0M3_out);
  and ALU0CS (ALU0CS_out, ALU0CSN_out, Cin);
  not ALU0CSN (ALU0CSN_out, ALU0SS_out);
  or ALU0CSO (TQ4, ALU0CS_out, ALU0SS_out);
  not ALU0ZO (Z, R0);

  // Other names for the same wires on the sheet: TQ0 = A0; TQ1 = B0; TQ2 = Cin; TQd = S0; TQe = S1; TQf = R0; TQg = Z;
  //   TQh = Cout
endmodule
