// Logisim project alu_4bit.circ as structural Verilog
module alu_4bit (
  input  A0,
  input  B0,
  input  A1,
  input  B1,
  input  A2,
  input  B2,
  input  A3,
  input  B3,
  input  S1,
  input  S0,
  input  Cin,
  output R0,
  output R1,
  output R2,
  output R3,
  output Cout,
  output Z
);

  wire TQ1b, TQ1e, TQ1f, TQ1g, TQ1h, TQ1i, TQ1j, TQ1k, TQ1l, TQ1m, TQ1n, TQ1o, TQ1p, TQ1q, TQ1r, TQ1s, TQ1t,
       TQ1u, TQ1v, TQ1w, TQ1y, TQ2, TQ2a, TQ2b, TQ2c, TQ2d, TQ2e, TQ2f, TQ2g, TQ2h, TQ2i, TQ2j, TQ2l, TQ2m,
       TQ2p, TQ2q, TQ2r, TQ4, TQ5, TQ6, TQ7, TQ8, TQ9, TQ10, TQ11, TQ12, TQ13, TQ14, TQ15, TQ16, TQ17, TQ18,
       TQ19, TQ21, TQ22, TQ23, TQ24, TQ25, TQ26, TQ27, TQ28, TQ29, TQa, TQb, TQc, TQd, TQe, TQf, TQg, TQh,
       TQi, TQj, TQk, TQl, TQm, TQn, TQr, TQs, TQt, TQu, TQv, TQw, TQx, TQy, TQz;

  and ALU0A (TQe, A0, B0);
  not ALU0N2 (TQg, S0);
  and ALU1A (TQ10, A1, B1);
  not ALU1N2 (TQ12, S0);
  xor ALU2X2 (TQ1m, TQ1e, TQ1f);
  and ALU2M1 (TQ1t, TQ1o, TQ1p);
  and ALU3G3 (TQ25, TQ21, TQ22);
  or ALU3MO1 (TQ2i, TQ2g, TQ2h);
  or ALU0O (TQh, B0, A0);
  and ALU0M1A (TQf, TQe, TQi);
  or ALU1O (TQ13, B1, A1);
  and ALU1M1A (TQ11, TQ10, TQ14);
  and ALU2G1 (TQ1g, A2, TQ1l);
  and ALU2M2 (TQ1u, TQ1s, S0);
  or ALU3C1 (TQ26, TQ23, TQ24);
  or ALU3MO2 (R3, TQ2i, TQ2j);
  and ALU0M2A (TQj, TQh, TQi);
  and ALU1M2A (TQ15, TQ13, TQ14);
  xor ALU0X1 (TQ5, A0, TQc);
  xor ALU1X1 (TQr, A1, TQy);
  and ALU2G2 (TQ1h, A2, TQ1f);
  and ALU2M3 (TQ1w, TQ1m, S1);
  or ALU3C2 (TQ2p, TQ26, TQ25);
  or ALU3ZO (TQ2m, R3, TQ2l);
  xor ALU0X2 (TQd, TQ5, TQ6);
  and ALU0M1 (TQk, TQf, TQg);
  xor ALU1X2 (TQz, TQr, TQs);
  and ALU1M1 (TQ16, TQ11, TQ12);
  and ALU2G3 (TQ1i, TQ1e, TQ1f);
  or ALU2MO1 (TQ1v, TQ1t, TQ1u);
  and ALU3SS (TQ27, S1, S0);
  not ALUZ (Z, TQ2m);
  and ALU0M2 (TQl, TQj, S0);
  and ALU1M2 (TQ17, TQ15, S0);
  and ALUF (TQ2q, S1, S0);
  and ALU0G1 (TQ7, A0, TQc);
  and ALU1G1 (TQt, A1, TQy);
  or ALU2C1 (TQ1j, TQ1g, TQ1h);
  or ALU2MO2 (R2, TQ1v, TQ1w);
  xor ALU3BX (TQ28, TQ27, B3);
  and ALU0G2 (TQ8, A0, TQ6);
  and ALU0M3 (TQn, TQd, S1);
  and ALU1G2 (TQu, A1, TQs);
  and ALU1M3 (TQ19, TQz, S1);
  or ALU2C2 (TQ22, TQ1j, TQ1i);
  or ALU2ZO (TQ2l, R2, TQ1y);
  not ALU3N1 (TQ2e, S1);
  xor ALUCX (TQ2r, TQ2p, TQ2q);
  or ALU0MO1 (TQm, TQk, TQl);
  or ALU1MO1 (TQ18, TQ16, TQ17);
  not ALU3N2 (TQ2c, S0);
  and ALUCG (Cout, TQ2r, S1);
  and ALU0G3 (TQ9, TQ5, TQ6);
  and ALU1G3 (TQv, TQr, TQs);
  and ALU2SS (TQ1k, S1, S0);
  and ALU3A (TQ2a, A3, B3);
  or ALU0C1 (TQa, TQ7, TQ8);
  or ALU0MO2 (R0, TQm, TQn);
  or ALU1C1 (TQw, TQt, TQu);
  or ALU1MO2 (R1, TQ18, TQ19);
  xor ALU2BX (TQ1l, TQ1k, B2);
  or ALU3O (TQ2d, B3, A3);
  and ALU3M1A (TQ2b, TQ2a, TQ2e);
  and ALU0CS (TQ4, TQ2, Cin);
  or ALU1ZO (TQ1y, R1, TQ1b);
  and ALU3M2A (TQ2f, TQ2d, TQ2e);
  or ALU0C2 (TQs, TQa, TQ9);
  or ALU1C2 (TQ1f, TQw, TQv);
  not ALU2N1 (TQ1r, S1);
  xor ALU3X1 (TQ21, A3, TQ28);
  and ALU0SS (TQb, S1, S0);
  not ALU0CSN (TQ2, TQb);
  and ALU1SS (TQx, S1, S0);
  and ALU2A (TQ1n, A2, B2);
  not ALU2N2 (TQ1p, S0);
  xor ALU3X2 (TQ29, TQ21, TQ22);
  and ALU3M1 (TQ2g, TQ2b, TQ2c);
  or ALU0CSO (TQ6, TQ4, TQb);
  or ALU2O (TQ1q, B2, A2);
  and ALU2M1A (TQ1o, TQ1n, TQ1r);
  and ALU3M2 (TQ2h, TQ2f, S0);
  xor ALU0BX (TQc, TQb, B0);
  xor ALU1BX (TQy, TQx, B1);
  and ALU3G1 (TQ23, A3, TQ28);
  not ALU0N1 (TQi, S1);
  or ALU0ZO (TQ1b, R0, R1);
  not ALU1N1 (TQ14, S1);
  xor ALU2X1 (TQ1e, A2, TQ1l);
  and ALU2M2A (TQ1s, TQ1q, TQ1r);
  and ALU3G2 (TQ24, A3, TQ22);
  and ALU3M3 (TQ2j, TQ29, S1);

  // Other names for the same wires on the sheet: TQ0 = A0; TQ1 = B0; TQ1a = R1; TQ1c = A2; TQ1d = B2; TQ1x = R2;
  //   TQ1z = A3; TQ2k = R3; TQ2n = Z; TQ2o = S0; TQ2s = S1; TQ2t = Cout; TQ3 = Cin; TQ20 = B3; TQo = R0; TQp = A1;
  //   TQq = B1
endmodule
