// Logisim project automatic_door.circ as structural Verilog
module automatic_door (
  input  CLK,
  input  RST,
  input  SENSOR,
  input  LIM,
  input  CLOSED,
  output OPENV,
  output HOLD,
  output CLOSEV
);

  wire TQ0, TQ1, TQ1a, TQ2, TQ4, TQ6, TQ7, TQ8, TQ9, TQ10, TQ11, TQ12, TQ13, TQ14, TQ15, TQ17, TQ18, TQ19,
       TQa, TQb, TQc, TQd, TQe, TQf, TQg, TQh, TQi, TQj, TQk, TQm, TQp, TQq, TQr, TQs, TQu, TQv, TQw, TQx,
       TQy;

  D_Flip_Flop U1 (.D(TQ6), .clk(CLK), .Q(TQ0), .reset(RST));  // open: Qn, preset
  and M5 (OPENV, TQ0, TQp);
  and A17 (TQ10, TQy, CLOSED);
  or O27 (TQ6, TQ2, TQ4);
  and A6 (TQq, TQ0, TQp);
  and A18 (TQ12, TQ10, TQ11);
  or O28 (TQh, TQ7, TQ8);
  D_Flip_Flop U2 (.D(TQk), .clk(CLK), .Q(TQe), .reset(RST));  // open: Qn, preset
  and A7 (TQr, TQq, TQ14);
  and A19 (TQc, TQ12, TQ18);
  or O29 (TQb, TQ9, TQa);
  not N1 (TQu, TQ0);
  and A8 (TQs, TQr, TQ11);
  and A20 (TQ13, TQ0, TQe);
  or O30 (TQd, TQb, TQc);
  not N2 (TQp, TQe);
  not NIsensor (TQ11, SENSOR);
  and A9 (TQ7, TQs, LIM);
  and A21 (TQ15, TQ13, TQ14);
  not NC1 (TQf, TQd);
  not NIlim (TQ18, LIM);
  and M10 (HOLD, TQu, TQe);
  and A22 (TQ17, TQ15, SENSOR);
  and AH1 (TQi, TQe, TQf);
  not NIclosed (TQ14, CLOSED);
  or O31 (TQk, TQh, TQi);
  and A11 (TQv, TQu, TQe);
  and A23 (TQa, TQ17, TQ18);
  // AND_Gate M0 has open pins: in0=TQu, in1=TQp, out=open
  and A12 (TQw, TQv, TQ14);
  or O24 (TQ19, TQ9, TQa);
  and A1 (TQg, TQu, TQp);
  and A13 (TQx, TQw, TQ11);
  or O25 (TQ2, TQ19, TQ8);
  and A2 (TQj, TQg, TQ14);
  and A14 (TQ8, TQx, TQ18);
  or O26 (TQ1a, TQ7, TQc);
  and A3 (TQm, TQj, SENSOR);
  and M15 (CLOSEV, TQ0, TQe);
  not NC0 (TQ1, TQ1a);
  and A4 (TQ9, TQm, TQ18);
  and A16 (TQy, TQ0, TQe);
  and AH0 (TQ4, TQ0, TQ1);

  // Other names for the same wires on the sheet: TQ3 = CLK; TQ5 = RST; TQ16 = SENSOR; TQl = OPENV; TQn = HOLD;
  //   TQo = CLOSEV; TQt = LIM; TQz = CLOSED
endmodule
