// Logisim project barrel_shifter_2bit.circ as structural Verilog
module barrel_shifter_2bit (
  input  D0,
  input  D1,
  input  SH0,
  input  GND,
  output Y0,
  output Y1
);

  wire TQ1, TQ2, TQ5, TQ8, TQ9;

  not NS1 (TQ5, SH0);
  and SA1 (TQ1, D0, TQ5);
  and SA2 (TQ2, GND, SH0);
  or MO3 (Y0, TQ1, TQ2);
  and SA4 (TQ8, D1, TQ5);
  and SA5 (TQ9, D0, SH0);
  or MO6 (Y1, TQ8, TQ9);

  // Other names for the same wires on the sheet: TQ0 = GND; TQ3 = Y0; TQ4 = D1; TQ6 = D0; TQ7 = SH0; TQa = Y1
endmodule
