// Logisim project barrel_shifter_4bit.circ as structural Verilog
module barrel_shifter_4bit (
  input  D0,
  input  D1,
  input  D2,
  input  D3,
  input  SH0,
  input  SH1,
  input  GND,
  output Y0,
  output Y1,
  output Y2,
  output Y3
);

  wire TQ0, TQ1, TQ1a, TQ1b, TQ1c, TQ1d, TQ1e, TQ1f, TQ2, TQ3, TQ4, TQ5, TQ6, TQ7, TQ8, TQ9, TQ11, TQ12,
       TQ14, TQ15, TQ18, TQb, TQc, TQd, TQe, TQf, TQg, TQh, TQi, TQj, TQk, TQm, TQn, TQo, TQq, TQr, TQs, TQt,
       TQu, TQv, TQw, TQz;

  not NS1 (TQ14, SH0);
  or MO11 (Y0, TQ8, TQ9);
  and SA23 (TQm, D2, TQ14);
  and SB35 (TQ1a, TQz, TQ12);
  not NS2 (TQ12, SH1);
  and SA12 (TQb, D1, TQ14);
  and SB24 (TQr, TQm, TQ12);
  and SA36 (TQ11, D2, SH0);
  and SA1 (TQ0, D0, TQ14);
  and SB13 (TQf, TQb, TQ12);
  and SA25 (TQn, D1, SH0);
  and SB37 (TQ1b, TQ11, TQ12);
  and SB2 (TQ4, TQ0, TQ12);
  and SA14 (TQc, D0, SH0);
  and SB26 (TQs, TQn, TQ12);
  and SA38 (TQ15, D1, TQ14);
  and SA3 (TQ1, GND, SH0);
  and SB15 (TQg, TQc, TQ12);
  and SA27 (TQo, D0, TQ14);
  and SB39 (TQ1d, TQ15, SH1);
  and SB4 (TQ5, TQ1, TQ12);
  and SA16 (TQd, GND, TQ14);
  and SB28 (TQu, TQo, SH1);
  and SA40 (TQ18, D0, SH0);
  and SA5 (TQ2, GND, TQ14);
  and SB17 (TQi, TQd, SH1);
  and SA29 (TQq, GND, SH0);
  and SB41 (TQ1f, TQ18, SH1);
  and SB6 (TQ7, TQ2, SH1);
  and SA18 (TQe, GND, SH0);
  and SB30 (TQw, TQq, SH1);
  or MO42 (TQ1c, TQ1a, TQ1b);
  and SA7 (TQ3, GND, SH0);
  and SB19 (TQk, TQe, SH1);
  or MO31 (TQt, TQr, TQs);
  or MO43 (TQ1e, TQ1c, TQ1d);
  and SB8 (TQ9, TQ3, SH1);
  or MO20 (TQh, TQf, TQg);
  or MO32 (TQv, TQt, TQu);
  or MO44 (Y3, TQ1e, TQ1f);
  or MO9 (TQ6, TQ4, TQ5);
  or MO21 (TQj, TQh, TQi);
  or MO33 (Y2, TQv, TQw);
  or MO10 (TQ8, TQ6, TQ7);
  or MO22 (Y1, TQj, TQk);
  and SA34 (TQz, D3, TQ14);

  // Other names for the same wires on the sheet: TQ1g = Y3; TQ10 = D2; TQ13 = D1; TQ16 = D0; TQ17 = SH0; TQ19 = SH1;
  //   TQa = Y0; TQl = Y1; TQp = GND; TQx = Y2; TQy = D3
endmodule
