// Logisim project bcd_adder.circ as structural Verilog
module bcd_adder (
  input  A0,
  input  B0,
  input  A1,
  input  B1,
  input  A2,
  input  B2,
  input  A3,
  input  B3,
  input  Cin,
  input  Z,
  output S0,
  output S1,
  output S2,
  output S3,
  output Cout
);

  wire BA28_out, BA29_out, BB27_out, BB28_out, BB29_out, BG27_out, BG28_out, BO27_out, BO28_out, BO29_out,
       BX28_out, BX29_out, TQ3, TQ4, TQ5, TQ6, TQ9, TQ10, TQ11, TQ12, TQ13, TQ14, TQ15, TQa, TQb, TQc, TQd,
       TQg, TQh, TQi, TQj, TQk, TQn, TQo, TQp, TQq, TQr, TQs, TQt, TQu, TQv, TQw, TQx, TQy, TQz;

  xor BXA1 (TQ3, A0, B0);
  xor BXS1 (TQv, TQ3, Cin);
  and BAA1 (TQ4, A0, B0);
  and BAB1 (TQ5, Cin, TQ3);
  or BAO1 (TQ6, TQ4, TQ5);
  or BAG1 (TQ9, TQ6, Z);
  xor BXA2 (TQa, A1, B1);
  xor BXS2 (TQ10, TQa, TQ9);
  and BAA2 (TQb, A1, B1);
  and BAB2 (TQc, TQ9, TQa);
  or BAO2 (TQd, TQb, TQc);
  or BAG2 (TQg, TQd, Z);
  xor BXA3 (TQh, A2, B2);
  xor BXS3 (TQ14, TQh, TQg);
  and BAA3 (TQi, A2, B2);
  and BAB3 (TQj, TQg, TQh);
  or BAO3 (TQk, TQi, TQj);
  or BAG3 (TQn, TQk, Z);
  xor BXA4 (TQo, A3, B3);
  xor BXS4 (TQ15, TQo, TQn);
  and BAA4 (TQp, A3, B3);
  and BAB4 (TQq, TQn, TQo);
  or BAO4 (TQr, TQp, TQq);
  or BAG4 (TQt, TQr, Z);
  or BAJ5 (Cout, TQt, TQu);
  and BAK5 (TQu, TQs, TQ15);
  or BAL5 (TQs, TQ14, TQ10);
  xor BX26 (TQw, TQv, Z);
  xor BX36 (S0, TQw, Z);
  and BA26 (TQx, TQv, Z);
  and BB26 (TQy, Z, TQw);
  or BO26 (TQz, TQx, TQy);
  or BG26 (TQ11, TQz, Z);
  xor BX27 (TQ12, TQ10, Cout);
  xor BX37 (S1, TQ12, TQ11);
  and BA27 (TQ13, TQ10, Cout);
  and BB27 (BB27_out, TQ11, TQ12);
  or BO27 (BO27_out, TQ13, BB27_out);
  or BG27 (BG27_out, BO27_out, Z);
  xor BX28 (BX28_out, TQ14, Cout);
  xor BX38 (S2, BX28_out, BG27_out);
  and BA28 (BA28_out, TQ14, Cout);
  and BB28 (BB28_out, BG27_out, BX28_out);
  or BO28 (BO28_out, BA28_out, BB28_out);
  or BG28 (BG28_out, BO28_out, Z);
  xor BX29 (BX29_out, TQ15, Z);
  xor BX39 (S3, BX29_out, BG28_out);
  and BA29 (BA29_out, TQ15, Z);
  and BB29 (BB29_out, BG28_out, BX29_out);
  or BO29 (BO29_out, BA29_out, BB29_out);
  // OR_Gate BG29 has open pins: in0=BO29_out, in1=Z, out=open

  // Other names for the same wires on the sheet: TQ0 = A0; TQ1 = B0; TQ1a = S3; TQ1b = Cout; TQ2 = Cin; TQ7 = A1;
  //   TQ8 = B1; TQ16 = Z; TQ17 = S0; TQ18 = S1; TQ19 = S2; TQe = A2; TQf = B2; TQl = A3; TQm = B3
endmodule
