// Logisim project bcd_counter.circ as structural Verilog
module bcd_counter (
  input  CLK,
  input  EN,
  input  RST,
  output Q0,
  output Q1,
  output Q2,
  output Q3
);

  wire TQ1, TQ2, TQ3, TQ4, TQ5, TQ6, TQ7;

  T_Flip_Flop U1 (.T(EN), .clk(CLK), .Q(Q0), .reset(RST));  // open: Qn, preset
  T_Flip_Flop U2 (.T(TQ1), .clk(CLK), .Q(Q1), .reset(RST));  // open: Qn, preset
  T_Flip_Flop U3 (.T(TQ3), .clk(CLK), .Q(Q2), .reset(RST));  // open: Qn, preset
  T_Flip_Flop U4 (.T(TQ7), .clk(CLK), .Q(Q3), .reset(RST));  // open: Qn, preset
  not N1 (TQ2, Q3);
  and A1 (TQ1, Q0, TQ2);
  and A2 (TQ4, Q0, Q1);
  and A3 (TQ3, TQ4, TQ2);
  and A4 (TQ5, TQ4, Q2);
  and A5 (TQ6, Q0, Q3);
  or O1 (TQ7, TQ5, TQ6);

  // Other names for the same wires on the sheet: TQ0 = EN; TQ8 = Q0; TQ9 = Q1; TQa = Q2; TQb = CLK; TQc = RST;
  //   TQd = Q3
endmodule
