// Logisim project bcd_subtractor.circ as structural Verilog
module bcd_subtractor (
  input  A0,
  input  B0,
  input  A1,
  input  B1,
  input  A2,
  input  B2,
  input  A3,
  input  B3,
  input  GND,
  input  ONE,
  output D0,
  output D1,
  output D2,
  output D3,
  output Borrow
);

  wire A43_out, A44_out, B43_out, B44_out, C42_out, C43_out, C44_out, G42_out, G43_out, TQ0, TQ1a, TQ1c,
       TQ1d, TQ1e, TQ1f, TQ1g, TQ1h, TQ1i, TQ1j, TQ1k, TQ1l, TQ1m, TQ1n, TQ1o, TQ1p, TQ1q, TQ1r, TQ1s, TQ1t,
       TQ1u, TQ1v, TQ1w, TQ1x, TQ1y, TQ1z, TQ2, TQ3, TQ5, TQ6, TQ8, TQ9, TQ10, TQ11, TQ12, TQ14, TQ15, TQ16,
       TQ17, TQ18, TQ19, TQ20, TQ21, TQ22, TQ23, TQ24, TQ25, TQ26, TQ27, TQa, TQc, TQd, TQe, TQf, TQg, TQh,
       TQk, TQl, TQm, TQn, TQo, TQq, TQx, TQy, TQz, X43_out, X44_out;

  not N1 (TQc, B0);
  xor X2 (TQx, B2, B1);
  or O1 (TQ8, B2, B1);
  xor X3 (TQ9, B3, TQ8);
  not N2 (TQ14, TQ9);
  xor X11 (TQd, A0, TQc);
  xor S11 (TQ1a, TQd, GND);
  and A11 (TQe, A0, TQc);
  and B11 (TQf, GND, TQd);
  or C11 (TQg, TQe, TQf);
  or G11 (TQk, TQg, GND);
  xor X12 (TQl, A1, B1);
  xor S12 (TQ1g, TQl, TQk);
  and A12 (TQm, A1, B1);
  and B12 (TQn, TQk, TQl);
  or C12 (TQo, TQm, TQn);
  or G12 (TQy, TQo, GND);
  xor X13 (TQz, A2, TQx);
  xor S13 (TQ1m, TQz, TQy);
  and A13 (TQ10, A2, TQx);
  and B13 (TQ11, TQy, TQz);
  or C13 (TQ12, TQ10, TQ11);
  or G13 (TQ15, TQ12, GND);
  xor X14 (TQ16, A3, TQ14);
  xor S14 (TQ1s, TQ16, TQ15);
  and A14 (TQ17, A3, TQ14);
  and B14 (TQ18, TQ15, TQ16);
  or C14 (TQ19, TQ17, TQ18);
  or G14 (TQ1z, TQ19, GND);
  xor X31 (TQ1c, TQ1a, ONE);
  xor S31 (TQ23, TQ1c, GND);
  and A31 (TQ1d, TQ1a, ONE);
  and B31 (TQ1e, GND, TQ1c);
  or C31 (TQ1f, TQ1d, TQ1e);
  or G31 (TQ1h, TQ1f, GND);
  xor X32 (TQ1i, TQ1g, GND);
  xor S32 (TQ0, TQ1i, TQ1h);
  and A32 (TQ1j, TQ1g, GND);
  and B32 (TQ1k, TQ1h, TQ1i);
  or C32 (TQ1l, TQ1j, TQ1k);
  or G32 (TQ1n, TQ1l, GND);
  xor X33 (TQ1o, TQ1m, GND);
  xor S33 (TQa, TQ1o, TQ1n);
  and A33 (TQ1p, TQ1m, GND);
  and B33 (TQ1q, TQ1n, TQ1o);
  or C33 (TQ1r, TQ1p, TQ1q);
  or G33 (TQ1t, TQ1r, GND);
  xor X34 (TQ1u, TQ1s, GND);
  xor S34 (TQh, TQ1u, TQ1t);
  and A34 (TQ1v, TQ1s, GND);
  and B34 (TQ1w, TQ1t, TQ1u);
  or C34 (TQ1x, TQ1v, TQ1w);
  or G34 (TQ20, TQ1x, GND);
  or B2J9 (TQq, TQ21, TQ22);
  and B2K9 (TQ22, TQ1y, TQh);
  or B2L9 (TQ1y, TQa, TQ0);
  or B2T10 (TQ21, TQ1z, TQ20);
  xor X41 (TQ24, TQ23, GND);
  xor S41 (D0, TQ24, GND);
  and A41 (TQ25, TQ23, GND);
  and B41 (TQ26, GND, TQ24);
  or C41 (TQ27, TQ25, TQ26);
  or G41 (TQ2, TQ27, GND);
  xor X42 (TQ3, TQ0, TQq);
  xor S42 (D1, TQ3, TQ2);
  and A42 (TQ5, TQ0, TQq);
  and B42 (TQ6, TQ2, TQ3);
  or C42 (C42_out, TQ5, TQ6);
  or G42 (G42_out, C42_out, GND);
  xor X43 (X43_out, TQa, TQq);
  xor S43 (D2, X43_out, G42_out);
  and A43 (A43_out, TQa, TQq);
  and B43 (B43_out, G42_out, X43_out);
  or C43 (C43_out, A43_out, B43_out);
  or G43 (G43_out, C43_out, GND);
  xor X44 (X44_out, TQh, GND);
  xor S44 (D3, X44_out, G43_out);
  and A44 (A44_out, TQh, GND);
  and B44 (B44_out, G43_out, X44_out);
  or C44 (C44_out, A44_out, B44_out);
  // OR_Gate G44 has open pins: in0=C44_out, in1=GND, out=open
  not NB (Borrow, TQq);

  // Other names for the same wires on the sheet: TQ1 = B0; TQ1b = ONE; TQ4 = B2; TQ7 = B3; TQ13 = A3; TQb = A0;
  //   TQi = A1; TQj = B1; TQp = GND; TQr = D0; TQs = D1; TQt = D2; TQu = D3; TQv = A2; TQw = Borrow
endmodule
