// Logisim project bcd_subtractor_2digit.circ as structural Verilog
module bcd_subtractor_2digit (
  input  A0,
  input  B0,
  input  A1,
  input  B1,
  input  A2,
  input  B2,
  input  A3,
  input  B3,
  input  A4,
  input  B4,
  input  A5,
  input  B5,
  input  A6,
  input  B6,
  input  A7,
  input  B7,
  input  Bin,
  input  GND,
  output D0,
  output D1,
  output D2,
  output D3,
  output D4,
  output D5,
  output D6,
  output D7,
  output Borrow
);

  wire TQ1, TQ1a, TQ1b, TQ1d, TQ1e, TQ1f, TQ1g, TQ1h, TQ1i, TQ1j, TQ1k, TQ1l, TQ1m, TQ1n, TQ1p, TQ1q, TQ1r,
       TQ1s, TQ1t, TQ1u, TQ1v, TQ1w, TQ1x, TQ1y, TQ1z, TQ2c, TQ2e, TQ2f, TQ2g, TQ2h, TQ2i, TQ2j, TQ2k, TQ2l,
       TQ2m, TQ2n, TQ2o, TQ2p, TQ2q, TQ2r, TQ2s, TQ2t, TQ2u, TQ2v, TQ2w, TQ2x, TQ2y, TQ2z, TQ3, TQ3a, TQ3b,
       TQ3c, TQ3d, TQ3e, TQ3f, TQ3g, TQ3h, TQ3i, TQ3j, TQ3k, TQ3l, TQ3m, TQ3q, TQ3r, TQ3t, TQ3u, TQ3v, TQ3w,
       TQ3x, TQ4a, TQ4b, TQ4d, TQ4e, TQ4f, TQ4g, TQ4h, TQ4i, TQ4j, TQ4k, TQ4l, TQ4m, TQ4n, TQ4o, TQ4p, TQ4q,
       TQ4r, TQ4s, TQ4t, TQ4u, TQ4v, TQ4w, TQ4x, TQ4y, TQ4z, TQ5, TQ6, TQ7, TQ8, TQ9, TQ10, TQ11, TQ12, TQ13,
       TQ14, TQ15, TQ16, TQ17, TQ18, TQ19, TQ21, TQ22, TQ29, TQ30, TQ31, TQ32, TQ33, TQ34, TQ35, TQ36, TQ37,
       TQ38, TQ39, TQ40, TQ41, TQ42, TQ43, TQ44, TQ46, TQ47, TQ48, TQ49, TQ50, TQ51, TQa, TQc, TQd, TQe, TQf,
       TQg, TQh, TQi, TQj, TQk, TQl, TQm, TQp, TQq, TQr, TQs, TQt, TQu, TQv, TQw, TQx, TQy;

  not not_1 (TQd, B0);
  xor S12 (TQ29, TQs, TQq);
  xor xor_1 (TQ2o, TQ1i, TQ1g);
  xor xor_2 (TQ2e, TQ29, GND);
  xor X34 (TQ2q, TQ2o, GND);
  and A41 (TQ31, TQ2z, GND);
  and and_1 (TQ3d, TQ3a, TQ3m);
  xor X2 (TQ46, B6, B5);
  and and_2 (TQ42, A5, B5);
  and and_3 (TQ4g, A7, TQ4d);
  xor S32 (TQy, TQ4s, TQ4r);
  xor xor_3 (TQ1p, TQ5, TQ3);
  and B41 (TQt, GND, TQp);
  and and_4 (TQ1j, TQ1d, TQ1f);
  xor xor_4 (TQ11, B2, B1);
  and A12 (TQu, A1, B1);
  and A14 (TQ1k, A3, TQ1e);
  xor xor_5 (TQ34, TQ2e, TQ2c);
  xor S34 (TQ3g, TQ2q, TQ2p);
  and and_5 (TQ32, GND, TQ30);
  and B43 (TQ3e, TQ3b, TQ3c);
  or O1 (TQ3q, B6, B5);
  and B12 (TQ43, TQ40, TQ41);
  and and_6 (TQ4h, TQ4e, TQ4f);
  and and_7 (TQ4t, TQ4q, GND);
  and and_8 (TQ7, TQ1, GND);
  or C41 (TQv, TQr, TQt);
  or C43 (TQ1l, TQ1h, TQ1j);
  or or_1 (TQ6, B2, B1);
  and and_9 (TQw, TQq, TQs);
  and B14 (TQ1m, TQ1g, TQ1i);
  and A32 (TQ2f, TQ29, GND);
  and A34 (TQ2r, TQ2o, GND);
  or or_2 (TQ33, TQ31, TQ32);
  or or_3 (TQ3f, TQ3d, TQ3e);
  xor X3 (TQ3r, B7, TQ3q);
  or C12 (TQ44, TQ42, TQ43);
  or C14 (TQ4i, TQ4g, TQ4h);
  and and_10 (TQ4u, TQ4r, TQ4s);
  and and_11 (TQ9, TQ3, TQ5);
  or G41 (TQ10, TQv, GND);
  or or_4 (TQ1q, TQ1l, GND);
  xor xor_6 (TQ8, B3, TQ6);
  or or_5 (TQx, TQu, TQw);
  or or_6 (TQ1n, TQ1k, TQ1m);
  and B32 (TQ2g, TQ2c, TQ2e);
  and B34 (TQ2s, TQ2p, TQ2q);
  or or_7 (TQ35, TQ33, GND);
  or G43 (TQ3h, TQ3f, GND);
  not N2 (TQ4d, TQ3r);
  or or_8 (TQ47, TQ44, GND);
  or G14 (TQe, TQ4i, GND);
  or or_9 (TQ4v, TQ4t, TQ4u);
  or or_10 (TQa, TQ7, TQ9);
  xor xor_7 (TQ12, TQy, TQ21);
  xor X44 (TQ1s, TQ1p, GND);
  not not_2 (TQ1e, TQ8);
  xor xor_8 (TQ3u, A4, TQ3t);
  or G12 (TQ13, TQx, GND);
  or or_11 (TQ2v, TQ1n, GND);
  or C32 (TQ2h, TQ2f, TQ2g);
  or C34 (TQ2t, TQ2r, TQ2s);
  xor X42 (TQ36, TQ34, TQ3m);
  xor xor_9 (TQ3i, TQ3g, GND);
  xor X13 (TQ48, A6, TQ46);
  not not_3 (TQ4l, TQ4j);
  or G32 (TQ4x, TQ4v, GND);
  or G34 (TQg, TQa, GND);
  xor xor_10 (D5, TQ12, TQ10);
  xor S44 (D7, TQ1s, TQ1q);
  xor X11 (TQf, A0, TQd);
  xor xor_11 (TQ15, A2, TQ11);
  not NBIN (TQ1t, Bin);
  or or_12 (TQ2j, TQ2h, GND);
  or or_13 (TQ2w, TQ2t, GND);
  xor S42 (D1, TQ36, TQ35);
  xor xor_12 (D3, TQ3i, TQ3h);
  xor S11 (TQ4k, TQ3u, GND);
  xor xor_13 (TQ4w, TQ48, TQ47);
  xor xor_14 (TQ4m, TQ4k, TQ4l);
  xor xor_15 (TQ4y, TQ4w, GND);
  or B2J22 (TQ21, TQi, TQk);
  and A42 (TQ14, TQy, TQ21);
  and and_12 (TQ1u, TQ1p, GND);
  xor xor_16 (TQ1r, TQf, GND);
  xor X31 (TQ1w, TQ1r, TQ1t);
  and and_13 (TQ3v, A4, TQ3t);
  xor xor_17 (TQm, TQ4m, GND);
  xor S13 (TQ2i, TQ15, TQ13);
  xor X33 (TQ2k, TQ2i, GND);
  or B2J9 (TQ3m, TQ2x, TQ2y);
  and and_14 (TQ37, TQ34, TQ3m);
  and A44 (TQ3j, TQ3g, GND);
  and and_15 (TQ49, A6, TQ46);
  xor xor_18 (TQ1b, TQ4y, TQ4x);
  and B2K22 (TQk, TQc, TQ1p);
  and and_16 (TQ16, TQ10, TQ12);
  and B44 (TQ1v, TQ1q, TQ1s);
  and A11 (TQh, A0, TQd);
  and A13 (TQ17, A2, TQ11);
  xor S31 (TQ2z, TQ1w, GND);
  xor S33 (TQ3a, TQ2k, TQ2j);
  and B2K9 (TQ2y, TQ2u, TQ3g);
  and B42 (TQ38, TQ35, TQ36);
  and and_17 (TQ3k, TQ3h, TQ3i);
  and B11 (TQ3w, GND, TQ3u);
  and and_18 (TQ4a, TQ47, TQ48);
  and and_19 (TQ4n, TQ4k, TQ4l);
  and A33 (TQ4z, TQ4w, GND);
  or B2L22 (TQc, TQ1b, TQy);
  or or_14 (TQ18, TQ14, TQ16);
  or C44 (TQ1x, TQ1u, TQ1v);
  and and_20 (TQj, GND, TQf);
  and A31 (TQ1y, TQ1r, TQ1t);
  or C11 (TQ3x, TQ3v, TQ3w);
  and and_21 (TQ4o, GND, TQ4m);
  and B13 (TQ19, TQ13, TQ15);
  and and_22 (TQ2l, TQ2i, GND);
  or B2L9 (TQ2u, TQ3a, TQ34);
  or C42 (TQ39, TQ37, TQ38);
  or or_15 (TQ3l, TQ3j, TQ3k);
  or C13 (TQ4b, TQ49, TQ4a);
  and and_23 (TQ50, TQ4x, TQ4y);
  or B2T22 (TQi, TQe, TQg);
  or or_16 (TQ1d, TQ18, GND);
  // OR_Gate or_17 has open pins: in0=TQ1x, in1=GND, out=open
  or or_18 (TQl, TQh, TQj);
  or or_19 (TQ1a, TQ17, TQ19);
  and B31 (TQ1z, GND, TQ1w);
  and B33 (TQ2m, TQ2j, TQ2k);
  or B2T9 (TQ2x, TQ2v, TQ2w);
  or G42 (TQ3b, TQ39, GND);
  // OR_Gate G44 has open pins: in0=TQ3l, in1=GND, out=open
  or G11 (TQ40, TQ3x, GND);
  or G13 (TQ4e, TQ4b, GND);
  or or_20 (TQ4p, TQ4n, TQ4o);
  or or_21 (TQ51, TQ4z, TQ50);
  xor X41 (TQp, TQm, GND);
  xor xor_19 (TQ1f, TQ1b, TQ21);
  not not_4 (Borrow, TQ21);
  or or_22 (TQq, TQl, GND);
  or C31 (TQ22, TQ1y, TQ1z);
  xor xor_20 (TQ41, A5, B5);
  or or_23 (TQ4r, TQ4p, GND);
  or or_24 (TQ1g, TQ1a, GND);
  or C33 (TQ2n, TQ2l, TQ2m);
  xor xor_21 (TQ30, TQ2z, GND);
  xor X43 (TQ3c, TQ3a, TQ3m);
  not NB (TQ4j, TQ3m);
  xor X14 (TQ4f, A7, TQ4d);
  or or_25 (TQ3, TQ51, GND);
  xor S41 (D4, TQp, GND);
  xor xor_22 (D6, TQ1f, TQ1d);
  xor X12 (TQs, A1, B1);
  xor xor_23 (TQ1i, A3, TQ1e);
  or G31 (TQ2c, TQ22, GND);
  or G33 (TQ2p, TQ2n, GND);
  xor xor_24 (D0, TQ30, GND);
  xor S43 (D2, TQ3c, TQ3b);
  not N1 (TQ3t, B4);
  xor xor_25 (TQ4q, TQ41, TQ40);
  xor S14 (TQ1, TQ4f, TQ4e);
  xor X32 (TQ4s, TQ4q, GND);
  xor xor_26 (TQ5, TQ1, GND);
  and and_24 (TQr, TQm, GND);
  and A43 (TQ1h, TQ1b, TQ21);

  // Other names for the same wires on the sheet: TQ0 = B0; TQ1c = A3; TQ1o = Bin; TQ2 = B2; TQ2a = D3; TQ2b = D7;
  //   TQ2d = Borrow; TQ3n = B4; TQ3o = B6; TQ3p = B7; TQ3s = A4; TQ3y = A5; TQ3z = B5; TQ4 = B3; TQ4c = A7;
  //   TQ20 = GND; TQ23 = D0; TQ24 = D4; TQ25 = D1; TQ26 = D5; TQ27 = D2; TQ28 = D6; TQ45 = A6; TQb = A0; TQn = A1;
  //   TQo = B1; TQz = A2
endmodule
