// Logisim project bidirsreg_4bit.circ as structural Verilog
module bidirsreg_4bit (
  input  DIR,
  input  SIN,
  input  SINL,
  input  RST,
  output Q0,
  output Q1,
  output Q2,
  output Q3
);

  wire AL1_out, AL2_out, AL3_out, AL4_out, AR1_out, AR2_out, AR3_out, AR4_out, CLK_out, N1_out, OR1_out,
       OR2_out, OR3_out, OR4_out;

  Clock CLK (.out(CLK_out));
  not N1 (N1_out, DIR);
  D_Flip_Flop U1 (.D(OR1_out), .clk(CLK_out), .Q(Q0), .preset(RST), .reset(RST));  // open: Qn
  D_Flip_Flop U2 (.D(OR2_out), .clk(CLK_out), .Q(Q1), .preset(RST), .reset(RST));  // open: Qn
  D_Flip_Flop U3 (.D(OR3_out), .clk(CLK_out), .Q(Q2), .preset(RST), .reset(RST));  // open: Qn
  D_Flip_Flop U4 (.D(OR4_out), .clk(CLK_out), .Q(Q3), .preset(RST), .reset(RST));  // open: Qn
  and AR1 (AR1_out, N1_out, SIN);
  and AL1 (AL1_out, DIR, Q1);
  or OR1 (OR1_out, AR1_out, AL1_out);
  and AR2 (AR2_out, N1_out, Q0);
  and AL2 (AL2_out, DIR, Q2);
  or OR2 (OR2_out, AR2_out, AL2_out);
  and AR3 (AR3_out, N1_out, Q1);
  and AL3 (AL3_out, DIR, Q3);
  or OR3 (OR3_out, AR3_out, AL3_out);
  and AR4 (AR4_out, N1_out, Q2);
  and AL4 (AL4_out, DIR, SINL);
  or OR4 (OR4_out, AR4_out, AL4_out);
endmodule
