// Logisim project comparator_3bit.circ as structural Verilog
module comparator_3bit (
  input  A0,
  input  B0,
  input  A1,
  input  B1,
  input  A2,
  input  B2,
  output GT,
  output EQ,
  output LT
);

  wire TQ1, TQ3, TQ7, TQa, TQd, TQe, TQf, TQg, TQh, TQi, TQj, TQk, TQl, TQm, TQn;

  xnor CMP0E (TQk, A0, B0);
  or CMPG1 (GT, TQh, TQi);
  not CMP0N (TQ1, B0);
  // AND_Gate CMPE1 has open pins: in0=TQj, in1=TQk, out=open
  and CMP0G (TQg, A0, TQ1);
  and CMPA2 (TQf, TQn, TQd);
  xnor CMP1E (TQl, A1, B1);
  or CMPG2 (TQh, TQe, TQf);
  not CMP1N (TQ7, B1);
  and CMPE2 (TQj, TQn, TQl);
  and CMP1G (TQd, A1, TQ7);
  // AND_Gate CMPQ1 is placed but not wired
  xnor CMP2E (TQn, A2, B2);
  and CMPQ2 (TQm, TQk, TQl);
  not CMP2N (TQa, B2);
  and CMPQ3 (EQ, TQm, TQn);
  and CMP2G (TQe, A2, TQa);
  or CMPO (TQ3, GT, EQ);
  not CMPL (LT, TQ3);
  and CMPA1 (TQi, TQj, TQg);

  // Other names for the same wires on the sheet: TQ0 = GT; TQ2 = EQ; TQ4 = A0; TQ5 = LT; TQ6 = B0; TQ8 = A1; TQ9 = B1;
  //   TQb = A2; TQc = B2
endmodule
