// Logisim project comparator_4bit.circ as structural Verilog
module comparator_4bit (
  input  A0,
  input  B0,
  input  A1,
  input  B1,
  input  A2,
  input  B2,
  input  A3,
  input  B3,
  output LT,
  output GT,
  output EQ
);

  wire n2, n7, n12, n17, n21, n22, n23, n24, n26, n27, n28, n29, n30, n32, n33, n34, n35, n36, n38, n42, n44,
       n49;

  xnor CMP0E (n38, A0, B0);
  not CMP0N (n2, B0);
  and CMP0G (n34, A0, n2);
  xnor CMP1E (n32, A1, B1);
  not CMP1N (n7, B1);
  and CMP1G (n28, A1, n7);
  xnor CMP2E (n26, A2, B2);
  not CMP2N (n12, B2);
  and CMP2G (n22, A2, n12);
  xnor CMP3E (n21, A3, B3);
  not CMP3N (n17, B3);
  and CMP3G (n23, A3, n17);
  or CMPO (n49, GT, EQ);
  not CMPL (LT, n49);
  and CMPA1 (n36, n33, n34);
  or CMPG1 (GT, n35, n36);
  // AND_Gate CMPE1 has open pins: in0=n33, in1=n38, out=open
  // AND_Gate CMPQ1 is placed but not wired
  and CMPQ2 (n42, n38, n32);
  and CMPQ3 (n44, n42, n26);
  and CMPQ4 (EQ, n44, n21);
  and CMPA2 (n30, n27, n28);
  or CMPG2 (n35, n29, n30);
  and CMPE2 (n33, n27, n32);
  and CMPA3 (n24, n21, n22);
  or CMPG3 (n29, n23, n24);
  and CMPE3 (n27, n21, n26);

  // Other names for the same wires on the sheet: n3 = A0; n4 = A0; n1 = B0; n5 = B0; n6 = B1; n10 = B1; n8 = A1;
  //   n9 = A1; n13 = A2; n14 = A2; n11 = B2; n15 = B2; n18 = A3; n19 = A3; n16 = B3; n20 = B3; n31 = n27; n37 = n33;
  //   n40 = n38; n41 = n32; n43 = n26; n25 = n21; n45 = n21; n39 = GT; n47 = GT; n46 = EQ; n48 = EQ; n50 = LT
endmodule
