// Logisim project comparator_8bit.circ as structural Verilog
module comparator_8bit (
  input  A0,
  input  B0,
  input  A1,
  input  B1,
  input  A2,
  input  B2,
  input  A3,
  input  B3,
  input  A4,
  input  B4,
  input  A5,
  input  B5,
  input  A6,
  input  B6,
  input  A7,
  input  B7,
  output GT,
  output EQ,
  output LT
);

  wire TQ0, TQ1a, TQ1b, TQ1c, TQ1d, TQ1e, TQ1f, TQ1g, TQ1h, TQ1i, TQ1j, TQ1k, TQ1l, TQ1m, TQ1n, TQ1o, TQ1p,
       TQ1q, TQ1r, TQ1s, TQ1v, TQ3, TQ6, TQ9, TQ10, TQ11, TQ12, TQ13, TQ14, TQ15, TQ16, TQ17, TQ18, TQ19,
       TQc, TQf, TQi, TQl, TQo, TQp, TQq, TQr, TQs, TQt, TQu, TQv, TQw, TQx, TQy, TQz;

  xnor CMP0E (TQ1f, A0, B0);
  xnor CMP4E (TQ1m, A4, B4);
  or CMPO (TQ1v, GT, EQ);
  or CMPG4 (TQ14, TQ10, TQ11);
  and CMPQ2 (TQ1h, TQ1f, TQ1g);
  not CMP0N (TQ0, B0);
  not CMP4N (TQc, B4);
  not CMPL (LT, TQ1v);
  and CMPE4 (TQ16, TQ12, TQ1k);
  and CMPQ3 (TQ1j, TQ1h, TQ1i);
  and CMP0G (TQ1b, A0, TQ0);
  and CMP4G (TQv, A4, TQc);
  and CMPA1 (TQ1d, TQ1e, TQ1b);
  and CMPA5 (TQx, TQy, TQv);
  and CMPQ4 (TQ1l, TQ1j, TQ1k);
  xnor CMP1E (TQ1g, A1, B1);
  xnor CMP5E (TQ1o, A5, B5);
  or CMPG1 (GT, TQ1c, TQ1d);
  or CMPG5 (TQ10, TQw, TQx);
  and CMPQ5 (TQ1n, TQ1l, TQ1m);
  not CMP1N (TQ3, B1);
  not CMP5N (TQf, B5);
  // AND_Gate CMPE1 has open pins: in0=TQ1e, in1=TQ1f, out=open
  and CMPE5 (TQ12, TQy, TQ1m);
  and CMPQ6 (TQ1p, TQ1n, TQ1o);
  and CMP1G (TQ17, A1, TQ3);
  and CMP5G (TQr, A5, TQf);
  and CMPA2 (TQ19, TQ1a, TQ17);
  and CMPA6 (TQt, TQu, TQr);
  and CMPQ7 (TQ1r, TQ1p, TQ1q);
  xnor CMP2E (TQ1i, A2, B2);
  xnor CMP6E (TQ1q, A6, B6);
  or CMPG2 (TQ1c, TQ18, TQ19);
  or CMPG6 (TQw, TQs, TQt);
  and CMPQ8 (EQ, TQ1r, TQ1s);
  not CMP2N (TQ6, B2);
  not CMP6N (TQi, B6);
  and CMPE2 (TQ1e, TQ1a, TQ1g);
  and CMPE6 (TQy, TQu, TQ1o);
  and CMP2G (TQ13, A2, TQ6);
  and CMP6G (TQo, A6, TQi);
  and CMPA3 (TQ15, TQ16, TQ13);
  xnor CMP3E (TQ1k, A3, B3);
  xnor CMP7E (TQ1s, A7, B7);
  and CMPA7 (TQq, TQ1s, TQo);
  or CMPG3 (TQ18, TQ14, TQ15);
  or CMPG7 (TQs, TQp, TQq);
  not CMP3N (TQ9, B3);
  not CMP7N (TQl, B7);
  and CMPE3 (TQ1a, TQ16, TQ1i);
  and CMP3G (TQz, A3, TQ9);
  and CMP7G (TQp, A7, TQl);
  and CMPE7 (TQu, TQ1s, TQ1q);
  and CMPA4 (TQ11, TQ12, TQz);
  // AND_Gate CMPQ1 is placed but not wired

  // Other names for the same wires on the sheet: TQ1 = A0; TQ1t = GT; TQ1u = EQ; TQ1w = LT; TQ2 = B0; TQ4 = A1;
  //   TQ5 = B1; TQ7 = A2; TQ8 = B2; TQa = A3; TQb = B3; TQd = A4; TQe = B4; TQg = A5; TQh = B5; TQj = A6; TQk = B6;
  //   TQm = A7; TQn = B7
endmodule
