// Logisim project countdown_timer.circ as structural Verilog
module countdown_timer (
  input  LOAD,
  input  RST,
  input  D0,
  input  D1,
  input  D2,
  input  D3,
  output Q0,
  output Q1,
  output Q2,
  output Q3,
  output ZERO
);

  wire CTDA2_out, CTDA3_out, CTDB2_out, CTDB3_out, CTDC2_out, CTDC3_out, CTDM2_out, CTDM3_out, CTDX2_out,
       CTDX3_out, TQ0, TQ1, TQ2, TQ5, TQ6, TQ7, TQ9, TQa, TQb, TQf, TQi, TQk, TQn, TQo, TQp, TQq;

  Clock CLK (.out(TQf));
  not CTDL (TQn, LOAD);
  not CTDN0 (TQo, Q0);
  not CTDN1 (TQp, Q1);
  and CTDZ1 (TQ0, TQo, TQp);
  not CTDN2 (TQq, Q2);
  and CTDZ2 (TQ1, TQ0, TQq);
  not CTDN3 (TQ2, Q3);
  and CTDZ3 (ZERO, TQ1, TQ2);
  and CTDA0 (TQ5, LOAD, D0);
  and CTDB0 (TQ6, TQn, TQi);
  or CTDM0 (TQ7, TQ5, TQ6);
  xor CTDX0 (TQi, Q0, TQn);
  D_Flip_Flop CTDF0 (.D(TQ7), .clk(TQf), .Q(Q0), .reset(RST));  // open: Qn, preset
  and CTDA1 (TQ9, LOAD, D1);
  and CTDB1 (TQa, TQn, TQk);
  or CTDM1 (TQb, TQ9, TQa);
  xor CTDX1 (TQk, Q1, TQo);
  D_Flip_Flop CTDF1 (.D(TQb), .clk(TQf), .Q(Q1), .reset(RST));  // open: Qn, preset
  and CTDA2 (CTDA2_out, LOAD, D2);
  and CTDB2 (CTDB2_out, TQn, CTDX2_out);
  or CTDM2 (CTDM2_out, CTDA2_out, CTDB2_out);
  xor CTDX2 (CTDX2_out, Q2, CTDC2_out);
  D_Flip_Flop CTDF2 (.D(CTDM2_out), .clk(TQf), .Q(Q2), .reset(RST));  // open: Qn, preset
  and CTDA3 (CTDA3_out, LOAD, D3);
  and CTDB3 (CTDB3_out, TQn, CTDX3_out);
  or CTDM3 (CTDM3_out, CTDA3_out, CTDB3_out);
  xor CTDX3 (CTDX3_out, Q3, CTDC3_out);
  D_Flip_Flop CTDF3 (.D(CTDM3_out), .clk(TQf), .Q(Q3), .reset(RST));  // open: Qn, preset
  and CTDC2 (CTDC2_out, TQo, TQp);
  and CTDC3 (CTDC3_out, CTDC2_out, TQq);

  // Other names for the same wires on the sheet: TQ3 = ZERO; TQ4 = D0; TQ8 = D1; TQc = D2; TQd = LOAD; TQe = D3;
  //   TQg = RST; TQh = Q0; TQj = Q1; TQl = Q2; TQm = Q3
endmodule
