// Logisim project debouncer.circ as structural Verilog
module debouncer (
  input  IN,
  input  RST,
  output OUT
);

  wire A1_out, A2_out, A3_out, CLK_out, O1_out, U1_q, U2_q, U3_q;

  Clock CLK (.out(CLK_out));
  D_Flip_Flop U1 (.D(IN), .clk(CLK_out), .Q(U1_q), .preset(RST), .reset(RST));  // open: Qn
  D_Flip_Flop U2 (.D(U1_q), .clk(CLK_out), .Q(U2_q), .preset(RST), .reset(RST));  // open: Qn
  D_Flip_Flop U3 (.D(U2_q), .clk(CLK_out), .Q(U3_q), .preset(RST), .reset(RST));  // open: Qn
  and A1 (A1_out, U1_q, U2_q);
  and A2 (A2_out, U1_q, U3_q);
  and A3 (A3_out, U2_q, U3_q);
  or O1 (O1_out, A1_out, A2_out);
  or O2 (OUT, O1_out, A3_out);
endmodule
