// Logisim project decoder_2bit.circ as structural Verilog
module decoder_2bit (
  input  A0,
  input  A1,
  output Y0,
  output Y1,
  output Y2,
  output Y3
);

  wire DECN1_out, DECN2_out;

  not DECN1 (DECN1_out, A0);
  not DECN2 (DECN2_out, A1);
  and DEC0_1 (Y0, DECN1_out, DECN2_out);
  and DEC1_1 (Y1, A0, DECN2_out);
  and DEC2_1 (Y2, DECN1_out, A1);
  and DEC3_1 (Y3, A0, A1);
endmodule
