// Logisim project decoder_3bit.circ as structural Verilog
module decoder_3bit (
  input  A0,
  input  A1,
  input  A2,
  output Y0,
  output Y1,
  output Y2,
  output Y3,
  output Y4,
  output Y5,
  output Y6,
  output Y7
);

  wire DEC0_1_out, DEC1_1_out, DEC2_1_out, DEC3_1_out, DEC4_1_out, DEC5_1_out, DEC6_1_out, DEC7_1_out,
       DECN1_out, DECN2_out, DECN3_out;

  not DECN1 (DECN1_out, A0);
  not DECN2 (DECN2_out, A1);
  not DECN3 (DECN3_out, A2);
  and DEC0_1 (DEC0_1_out, DECN1_out, DECN2_out);
  and DEC0_2 (Y0, DEC0_1_out, DECN3_out);
  and DEC1_1 (DEC1_1_out, A0, DECN2_out);
  and DEC1_2 (Y1, DEC1_1_out, DECN3_out);
  and DEC2_1 (DEC2_1_out, DECN1_out, A1);
  and DEC2_2 (Y2, DEC2_1_out, DECN3_out);
  and DEC3_1 (DEC3_1_out, A0, A1);
  and DEC3_2 (Y3, DEC3_1_out, DECN3_out);
  and DEC4_1 (DEC4_1_out, DECN1_out, DECN2_out);
  and DEC4_2 (Y4, DEC4_1_out, A2);
  and DEC5_1 (DEC5_1_out, A0, DECN2_out);
  and DEC5_2 (Y5, DEC5_1_out, A2);
  and DEC6_1 (DEC6_1_out, DECN1_out, A1);
  and DEC6_2 (Y6, DEC6_1_out, A2);
  and DEC7_1 (DEC7_1_out, A0, A1);
  and DEC7_2 (Y7, DEC7_1_out, A2);
endmodule
