// Logisim project decoder_4to16.circ as structural Verilog
module decoder_4to16 (
  input  A0,
  input  A1,
  input  A2,
  input  A3,
  input  nG2,
  output Y0,
  output Y1,
  output Y2,
  output Y3,
  output Y4,
  output Y5,
  output Y6,
  output Y7,
  output Y8,
  output Y9,
  output Y10,
  output Y11,
  output Y12,
  output Y13,
  output Y14,
  output Y15
);

  _74138 U1 (
    .pin1(A0), .pin2(A1), .pin3(A1), .pin4(A1), .pin5(A1), .pin6(A1), .pin7(A1), .pin15(A1), .pin14(A1),
    .pin13(A1), .pin12(Y3), .pin11(Y4), .pin10(A1), .pin9(A1));
  _74138 U2 (
    .pin1(A0), .pin2(A1), .pin3(A1), .pin4(A1), .pin5(A1), .pin6(A1), .pin7(A1), .pin15(A1), .pin14(A1),
    .pin13(Y10), .pin12(Y11), .pin11(A1), .pin10(A1), .pin9(A1));
  not U3A (A1, A1);

  assign A2 = A1;
  assign A3 = A1;
  assign nG2 = A1;
  assign Y0 = A1;
  assign Y1 = A1;
  assign Y2 = A1;
  assign Y5 = A1;
  assign Y6 = A1;
  assign Y7 = A1;
  assign Y8 = A1;
  assign Y9 = A1;
  assign Y12 = A1;
  assign Y13 = A1;
  assign Y14 = A1;
  assign Y15 = A1;
endmodule
