// Logisim project digital_clock.circ as structural Verilog
module digital_clock (
  input  RST,
  output Q0,
  output Q1,
  output Q2,
  output Q3,
  output Q4,
  output Q5,
  output Q6,
  output Q7,
  output Q8,
  output Q9,
  output Q10,
  output Q11,
  output Q12,
  output Q13,
  output Q18,
  output Q19,
  output Q20,
  output Q21,
  output Q22
);

  wire HA3_out, HA4_out, HM1_out, HM2_out, HM4_out, HN3_out, HNW_out, HR2_out, HR3_out, HR4_out, HW_out, TQ0,
       TQ1, TQ1e, TQ1g, TQ1h, TQ1k, TQ1l, TQ1m, TQ1n, TQ1o, TQ1p, TQ1q, TQ1r, TQ1s, TQ1t, TQ1u, TQ1v, TQ1w,
       TQ1x, TQ2, TQ3, TQ4, TQ5, TQ6, TQ7, TQ8, TQ9, TQ10, TQ11, TQ12, TQ13, TQ14, TQ15, TQ16, TQ17, TQ22,
       TQ23, TQ24, TQ25, TQ26, TQ27, TQa, TQb, TQe, TQf, TQh, TQi, TQj, TQk, TQl, TQm, TQn, TQo, TQs, TQu,
       TQv, TQw, TQx, TQy, TQz;

  Clock CLK (.out(TQ1h));
  T_Flip_Flop D0F0 (.T(TQ9), .clk(TQ1h), .Q(Q0), .reset(RST));  // open: Qn, preset
  T_Flip_Flop D0F1 (.T(TQb), .clk(TQ1h), .Q(Q1), .reset(RST));  // open: Qn, preset
  T_Flip_Flop D0F2 (.T(TQe), .clk(TQ1h), .Q(Q2), .reset(RST));  // open: Qn, preset
  T_Flip_Flop D0F3 (.T(TQn), .clk(TQ1h), .Q(Q3), .reset(RST));  // open: Qn, preset
  not D0N1 (TQ1, Q1);
  and D0A1 (TQ2, Q0, TQ1);
  not D0N2 (TQ4, Q2);
  and D0A2 (TQ5, TQ2, TQ4);
  and D0A3 (TQ1e, TQ5, Q3);
  not D0NW (TQk, TQ1e);
  or D0T0 (TQ9, TQk, TQ1e);
  and D0M1 (TQb, Q0, TQk);
  and D0R2 (TQf, Q0, Q1);
  and D0M2 (TQe, TQf, TQk);
  and D0R3 (TQi, TQf, Q2);
  and D0M3 (TQl, TQi, TQk);
  or D0O3 (TQn, TQl, TQ1e);
  T_Flip_Flop D1F0 (.T(TQ10), .clk(TQ1h), .Q(Q4), .reset(RST));  // open: Qn, preset
  T_Flip_Flop D1F1 (.T(TQ12), .clk(TQ1h), .Q(Q5), .reset(RST));  // open: Qn, preset
  T_Flip_Flop D1F2 (.T(TQ17), .clk(TQ1h), .Q(Q6), .reset(RST));  // open: Qn, preset
  not D1N1 (TQv, Q5);
  and D1A1 (TQw, Q4, TQv);
  and D1A2 (TQx, TQw, Q6);
  and D1W (TQ1g, TQ1e, TQx);
  not D1NW (TQz, TQ1g);
  and D1TE (TQ14, TQ1e, TQz);
  or D1T0 (TQ10, TQ14, TQ1g);
  and D1M1 (TQ12, Q4, TQ14);
  and D1R2 (TQ13, Q4, Q5);
  and D1M2 (TQ15, TQ13, TQ14);
  or D1O2 (TQ17, TQ15, TQ1g);
  and D1EC (TQ22, TQ1e, TQ1g);
  T_Flip_Flop D2F0 (.T(TQ1q), .clk(TQ1h), .Q(Q7), .reset(RST));  // open: Qn, preset
  T_Flip_Flop D2F1 (.T(TQ1r), .clk(TQ1h), .Q(Q8), .reset(RST));  // open: Qn, preset
  T_Flip_Flop D2F2 (.T(TQ1s), .clk(TQ1h), .Q(Q9), .reset(RST));  // open: Qn, preset
  T_Flip_Flop D2F3 (.T(TQ1x), .clk(TQ1h), .Q(Q10), .reset(RST));  // open: Qn, preset
  not D2N1 (TQ1k, Q8);
  and D2A1 (TQ1l, Q7, TQ1k);
  not D2N2 (TQ1m, Q9);
  and D2A2 (TQ1n, TQ1l, TQ1m);
  and D2A3 (TQ1o, TQ1n, Q10);
  and D2W (TQ23, TQ22, TQ1o);
  not D2NW (TQ1p, TQ23);
  and D2TE (TQ1v, TQ22, TQ1p);
  or D2T0 (TQ1q, TQ1v, TQ23);
  and D2M1 (TQ1r, Q7, TQ1v);
  and D2R2 (TQ1t, Q7, Q8);
  and D2M2 (TQ1s, TQ1t, TQ1v);
  and D2R3 (TQ1u, TQ1t, Q9);
  and D2M3 (TQ1w, TQ1u, TQ1v);
  or D2O3 (TQ1x, TQ1w, TQ23);
  and D2EC (TQh, TQ22, TQ23);
  T_Flip_Flop D3F0 (.T(TQ0), .clk(TQ1h), .Q(Q11), .reset(RST));  // open: Qn, preset
  T_Flip_Flop D3F1 (.T(TQ3), .clk(TQ1h), .Q(Q12), .reset(RST));  // open: Qn, preset
  T_Flip_Flop D3F2 (.T(TQa), .clk(TQ1h), .Q(Q13), .reset(RST));  // open: Qn, preset
  not D3N1 (TQ24, Q12);
  and D3A1 (TQ25, Q11, TQ24);
  and D3A2 (TQ26, TQ25, Q13);
  and D3W (TQj, TQh, TQ26);
  not D3NW (TQ27, TQj);
  and D3TE (TQ7, TQh, TQ27);
  or D3T0 (TQ0, TQ7, TQj);
  and D3M1 (TQ3, Q11, TQ7);
  and D3R2 (TQ6, Q11, Q12);
  and D3M2 (TQ8, TQ6, TQ7);
  or D3O2 (TQa, TQ8, TQj);
  and D3EC (TQs, TQh, TQj);
  T_Flip_Flop DH0 (.T(TQs), .clk(TQ1h), .Q(Q18), .reset(RST));  // open: Qn, preset
  T_Flip_Flop DH1 (.T(TQu), .clk(TQ1h), .Q(Q19), .reset(RST));  // open: Qn, preset
  T_Flip_Flop DH2 (.T(TQy), .clk(TQ1h), .Q(Q20), .reset(RST));  // open: Qn, preset
  T_Flip_Flop DH3 (.T(TQ11), .clk(TQ1h), .Q(Q21), .reset(RST));  // open: Qn, preset
  T_Flip_Flop DH4 (.T(TQ16), .clk(TQ1h), .Q(Q22), .reset(RST));  // open: Qn, preset
  and HA1 (TQm, Q18, Q19);
  and HA2 (TQo, TQm, Q20);
  not HN3 (HN3_out, Q21);
  and HA3 (HA3_out, TQo, HN3_out);
  and HA4 (HA4_out, HA3_out, Q22);
  and HW (HW_out, TQs, HA4_out);
  not HNW (HNW_out, HW_out);
  and HM1 (HM1_out, Q18, HNW_out);
  or HO1 (TQu, HM1_out, HW_out);
  and HR2 (HR2_out, Q18, Q19);
  and HM2 (HM2_out, HR2_out, HNW_out);
  or HO2 (TQy, HM2_out, HW_out);
  and HR3 (HR3_out, HR2_out, Q20);
  and HM3 (TQ11, HR3_out, HNW_out);
  and HR4 (HR4_out, HR3_out, Q21);
  and HM4 (HM4_out, HR4_out, HNW_out);
  or HO4 (TQ16, HM4_out, HW_out);

  // Other names for the same wires on the sheet: TQ1a = Q19; TQ1b = Q5; TQ1c = Q20; TQ1d = Q6; TQ1f = Q21; TQ1i = RST;
  //   TQ1j = Q22; TQ1y = Q7; TQ1z = Q8; TQ18 = Q18; TQ19 = Q4; TQ20 = Q9; TQ21 = Q10; TQc = Q11; TQd = Q12; TQg = Q13;
  //   TQp = Q0; TQq = Q1; TQr = Q2; TQt = Q3
endmodule
