// Logisim project edge_detector.circ as structural Verilog
module edge_detector (
  input  CLK,
  input  IN,
  input  RST,
  output RISE,
  output FALL
);

  wire N1_out, N2_out, U1_q;

  D_Flip_Flop U1 (.D(IN), .clk(CLK), .Q(U1_q), .reset(RST));  // open: Qn, preset
  not N1 (N1_out, U1_q);
  not N2 (N2_out, IN);
  and A1 (RISE, IN, N1_out);
  and A2 (FALL, U1_q, N2_out);

  // Other names for the same wires on the sheet: TQ0 = CLK; TQ1 = RST; TQ2 = IN; TQ3 = RISE; TQ4 = FALL
endmodule
