// Logisim project encoder_4to2.circ as structural Verilog
module encoder_4to2 (
  input  I2,
  input  I3,
  input  I1,
  input  I0,
  output Y1,
  output Y0,
  output G
);

  wire TQ0, TQ4, TQ6;

  or enc4_g_o1 (Y1, I2, I3);
  or enc4_g_o2 (TQ0, Y1, I1);
  or enc4_g_o3 (G, TQ0, I0);
  not enc4_n2 (TQ4, I2);
  and enc4_p0 (TQ6, I1, TQ4);
  or enc4_y0_o1 (Y0, I3, TQ6);

  // Other names for the same wires on the sheet: TQ1 = I0; TQ2 = I2; TQ3 = I1; TQ5 = I3; TQ7 = Y1; TQ8 = Y0; TQ9 = G
endmodule
