// Logisim project excess3_adder.circ as structural Verilog
module excess3_adder (
  input  A0,
  input  B0,
  input  A1,
  input  B1,
  input  A2,
  input  B2,
  input  A3,
  input  B3,
  input  ONE,
  input  GND,
  output S0,
  output S1,
  output S2,
  output S3,
  output Cout
);

  wire TQ1a, TQ1b, TQ1c, TQ1d, TQ1e, TQ1f, TQ2, TQ3, TQ4, TQ5, TQ8, TQ9, TQ10, TQ11, TQ12, TQ13, TQ14, TQ15,
       TQ16, TQ17, TQ18, TQ19, TQa, TQb, TQc, TQf, TQg, TQh, TQi, TQj, TQm, TQn, TQo, TQp, TQq, TQr, TQt,
       TQu, TQv, TQw, TQx, TQy, TQz;

  xor E3X1 (TQ2, A0, B0);
  xor E3X3 (TQg, A2, B2);
  not E3N1 (TQ1a, Cout);
  or E3G26 (TQ14, TQ12, GND);
  // OR_Gate E3G28 has open pins: in0=TQ1f, in1=GND, out=open
  xor E3S1 (TQr, TQ2, GND);
  xor E3S3 (TQ13, TQg, TQf);
  xor E3X25 (TQt, TQr, ONE);
  xor E3X27 (TQ15, TQ13, TQ1a);
  xor E3S25 (S0, TQt, GND);
  and E3A1 (TQ3, A0, B0);
  and E3A3 (TQh, A2, B2);
  xor E3S27 (S2, TQ15, TQ14);
  and E3B1 (TQ4, GND, TQ2);
  and E3B3 (TQi, TQf, TQg);
  and E3A25 (TQu, TQr, ONE);
  and E3A27 (TQ16, TQ13, TQ1a);
  and E3B25 (TQv, GND, TQt);
  or E3O1 (TQ5, TQ3, TQ4);
  or E3O3 (TQj, TQh, TQi);
  and E3B27 (TQ17, TQ14, TQ15);
  or E3G1 (TQ8, TQ5, GND);
  or E3G3 (TQm, TQj, GND);
  or E3O25 (TQw, TQu, TQv);
  or E3O27 (TQ18, TQ16, TQ17);
  or E3G25 (TQy, TQw, GND);
  xor E3X2 (TQ9, A1, B1);
  xor E3X4 (TQn, A3, B3);
  or E3G27 (TQ1b, TQ18, GND);
  xor E3S2 (TQx, TQ9, TQ8);
  xor E3S4 (TQ19, TQn, TQm);
  xor E3X26 (TQz, TQx, Cout);
  xor E3X28 (TQ1c, TQ19, TQ1a);
  xor E3S26 (S1, TQz, TQy);
  and E3A2 (TQa, A1, B1);
  and E3A4 (TQo, A3, B3);
  xor E3S28 (S3, TQ1c, TQ1b);
  and E3B2 (TQb, TQ8, TQ9);
  and E3B4 (TQp, TQm, TQn);
  and E3A26 (TQ10, TQx, Cout);
  and E3A28 (TQ1d, TQ19, TQ1a);
  and E3B26 (TQ11, TQy, TQz);
  or E3O2 (TQc, TQa, TQb);
  or E3O4 (TQq, TQo, TQp);
  and E3B28 (TQ1e, TQ1b, TQ1c);
  or E3G2 (TQf, TQc, GND);
  or E3G4 (Cout, TQq, GND);
  or E3O26 (TQ12, TQ10, TQ11);
  or E3O28 (TQ1f, TQ1d, TQ1e);

  // Other names for the same wires on the sheet: TQ0 = A0; TQ1 = B0; TQ1g = GND; TQ1h = S0; TQ1i = S1; TQ1j = S2;
  //   TQ1k = S3; TQ1l = Cout; TQ6 = A1; TQ7 = B1; TQd = A2; TQe = B2; TQk = A3; TQl = B3; TQs = ONE
endmodule
