// Logisim project excess3tobcd.circ as structural Verilog
module excess3tobcd (
  input  E1,
  input  E2,
  input  E4,
  input  E8,
  output D1,
  output D2,
  output D4,
  output D8
);

  wire TQ5, TQ8, TQ9, TQb;

  not N1 (D1, E1);
  xor X1 (D2, E2, E1);
  and A1 (TQ5, E2, E1);
  not N2 (TQ9, TQ5);
  not N3 (TQ8, E4);
  xor X2 (D4, E4, TQ9);
  and A2 (TQb, TQ8, TQ9);
  xor X3 (D8, E8, TQb);

  // Other names for the same wires on the sheet: TQ0 = D8; TQ1 = D1; TQ2 = D2; TQ3 = E2; TQ4 = E1; TQ6 = E4; TQ7 = D4;
  //   TQa = E8
endmodule
