// Logisim project freq_meter.circ as structural Verilog
module freq_meter (
  input  SIG,
  input  RST,
  output F0,
  output F1,
  output F2,
  output F3,
  output WIN
);

  wire FLA1_out, FLA2_out, FLA3_out, FLB1_out, FLB2_out, FLB3_out, FLR2_out, FLR3_out, TQ0, TQ1, TQ2, TQ3,
       TQ4, TQ5, TQ6, TQ7, TQ8, TQ9, TQ10, TQ12, TQ14, TQ15, TQ16, TQb, TQc, TQd, TQe, TQf, TQg, TQh, TQi,
       TQj, TQk, TQl, TQm, TQn, TQo, TQq, TQr, TQs, TQt, TQu, TQv, TQx, TQy;

  Clock CLK (.out(TQ12));
  and FW1 (TQ5, TQ3, TQ4);
  and FW2 (TQ7, TQ5, TQ6);
  D_Flip_Flop FWC0 (.D(TQ0), .clk(TQ12), .Q(TQ3), .reset(RST));  // open: Qn, preset
  D_Flip_Flop FWC1 (.D(TQ1), .clk(TQ12), .Q(TQ4), .reset(RST));  // open: Qn, preset
  D_Flip_Flop FWC2 (.D(TQ2), .clk(TQ12), .Q(TQ6), .reset(RST));  // open: Qn, preset
  not FWN (TQ0, TQ3);
  xor FWX1 (TQ1, TQ4, TQ3);
  xor FWX2 (TQ2, TQ6, TQ5);
  D_Flip_Flop FWIN (.D(TQ8), .clk(TQ12), .Q(WIN), .reset(RST));  // open: Qn, preset
  xor FWNX (TQ8, WIN, TQ7);
  D_Flip_Flop FWND (.D(WIN), .clk(TQ12), .Q(TQr), .reset(RST));  // open: Qn, preset
  D_Flip_Flop FSP (.D(SIG), .clk(TQ12), .Q(TQ9), .reset(RST));  // open: Qn, preset
  not FSPN (TQb, TQ9);
  and FRIS (TQc, SIG, TQb);
  and FEN (TQf, WIN, TQc);
  D_Flip_Flop FCC0 (.D(TQe), .clk(TQ12), .Q(TQs), .reset(RST));  // open: Qn, preset
  xor FCX0 (TQd, TQs, TQf);
  and FCW0 (TQe, WIN, TQd);
  and FCN0 (TQi, TQf, TQs);
  D_Flip_Flop FCC1 (.D(TQh), .clk(TQ12), .Q(TQx), .reset(RST));  // open: Qn, preset
  xor FCX1 (TQg, TQx, TQi);
  and FCW1 (TQh, WIN, TQg);
  and FCN1 (TQl, TQi, TQx);
  D_Flip_Flop FCC2 (.D(TQk), .clk(TQ12), .Q(TQ10), .reset(RST));  // open: Qn, preset
  xor FCX2 (TQj, TQ10, TQl);
  and FCW2 (TQk, WIN, TQj);
  and FCN2 (TQm, TQl, TQ10);
  D_Flip_Flop FCC3 (.D(TQo), .clk(TQ12), .Q(TQ15), .reset(RST));  // open: Qn, preset
  xor FCX3 (TQn, TQ15, TQm);
  and FCW3 (TQo, WIN, TQn);
  not FNW (TQq, WIN);
  and FLN (TQ14, TQq, TQr);
  not FNL (TQ16, TQ14);
  D_Flip_Flop FLO0 (.D(TQv), .clk(TQ12), .Q(F0), .reset(RST));  // open: Qn, preset
  and FLA0 (TQt, TQ14, TQs);
  and FLB0 (TQu, TQ16, F0);
  or FLR0 (TQv, TQt, TQu);
  D_Flip_Flop FLO1 (.D(TQy), .clk(TQ12), .Q(F1), .reset(RST));  // open: Qn, preset
  and FLA1 (FLA1_out, TQ14, TQx);
  and FLB1 (FLB1_out, TQ16, F1);
  or FLR1 (TQy, FLA1_out, FLB1_out);
  D_Flip_Flop FLO2 (.D(FLR2_out), .clk(TQ12), .Q(F2), .reset(RST));  // open: Qn, preset
  and FLA2 (FLA2_out, TQ14, TQ10);
  and FLB2 (FLB2_out, TQ16, F2);
  or FLR2 (FLR2_out, FLA2_out, FLB2_out);
  D_Flip_Flop FLO3 (.D(FLR3_out), .clk(TQ12), .Q(F3), .reset(RST));  // open: Qn, preset
  and FLA3 (FLA3_out, TQ14, TQ15);
  and FLB3 (FLB3_out, TQ16, F3);
  or FLR3 (FLR3_out, FLA3_out, FLB3_out);

  // Other names for the same wires on the sheet: TQ11 = F2; TQ13 = RST; TQ17 = F3; TQa = SIG; TQp = WIN; TQw = F0;
  //   TQz = F1
endmodule
