// Logisim project from_json_full_adder.circ as structural Verilog
module full_adder (
  input  A,
  input  B,
  input  Cin,
  output SUM,
  output Cout
);

  wire n3, n6, n7;

  xor xor_1 (n3, A, B);
  and and_1 (n7, A, B);
  xor xor_2 (SUM, n3, Cin);
  and and_2 (n6, n3, Cin);
  or or_1 (Cout, n6, n7);

  // Other names for the same wires on the sheet: n1 = A; n2 = B; n4 = Cin; n5 = SUM; n8 = Cout
endmodule
