// Logisim project from_json_mux_4to1.circ as structural Verilog
module mux_4to1 (
  input  D0,
  input  S0,
  input  D1,
  input  S1,
  input  D2,
  input  D3,
  output Y
);

  wire nS0, nS1, O01, O23, P0, P0a, P1, P1a, P2, P2a, P3, P3a;

  not not_1 (nS0, S0);
  not not_2 (nS1, S1);
  and and_1 (P0a, D0, nS1);
  and and_2 (P1a, D1, nS1);
  and and_3 (P2a, D2, S1);
  and and_4 (P3a, D3, S1);
  and and_5 (P0, P0a, nS0);
  and and_6 (P1, P1a, S0);
  and and_7 (P2, P2a, nS0);
  and and_8 (P3, P3a, S0);
  or or_1 (O01, P0, P1);
  or or_2 (O23, P2, P3);
  or or_3 (Y, O01, O23);
endmodule
