// Logisim project full_adder.circ as structural Verilog
module full_adder (
  input  A,
  input  B,
  input  Cin,
  output SUM,
  output Cout
);

  wire AB, X1, XC;

  xor xor_1 (X1, A, B);
  and and_1 (AB, A, B);
  xor xor_2 (Cout, X1, B);
  and and_2 (XC, X1, B);
  or or_1 (Cout, AB, XC);

  assign Cin = B;
  assign SUM = Cout;
endmodule
