// Logisim project generic_fsm.circ as structural Verilog
module generic_fsm (
  input  CLK,
  input  RST,
  input  A,
  input  B,
  output Z
);

  wire TQ0, TQ1, TQ2, TQ4, TQ6, TQ7, TQ8, TQ9, TQ10, TQ11, TQ13, TQ14, TQ15, TQ16, TQ17, TQ18, TQa, TQb, TQc,
       TQd, TQe, TQf, TQg, TQh, TQi, TQj, TQk, TQl, TQn, TQo, TQp, TQq, TQr, TQs, TQu, TQv, TQw, TQx, TQy,
       TQz;

  D_Flip_Flop U1 (.D(TQ1), .clk(CLK), .Q(TQ16), .reset(RST));  // open: Qn, preset
  and A6 (TQo, TQn, A);
  and M18 (TQl, TQ16, TQd);
  or O28 (TQg, TQ6, TQ7);
  and A7 (TQ2, TQo, TQv);
  and A19 (TQz, TQ16, TQd);
  or O29 (TQa, TQ8, TQ9);
  D_Flip_Flop U2 (.D(TQj), .clk(CLK), .Q(TQd), .reset(RST));  // open: Qn, preset
  and A8 (TQq, TQ16, TQp);
  and A20 (TQ11, TQz, TQ10);
  or O30 (TQc, TQa, TQb);
  not N1 (TQw, TQ16);
  and A9 (TQr, TQq, TQ10);
  and A21 (TQ4, TQ11, B);
  not NC1 (TQe, TQc);
  not N2 (TQp, TQd);
  and AH1 (TQh, TQd, TQe);
  not NIa (TQ10, A);
  and A10 (TQb, TQr, B);
  or O22 (TQ13, TQ8, TQ9);
  not NIb (TQv, B);
  and M11 (TQk, TQw, TQd);
  or O23 (TQ18, TQ13, TQ7);
  or O31 (TQj, TQg, TQh);
  // AND_Gate M0 has open pins: in0=TQw, in1=TQp, out=open
  or Ofo32 (Z, TQk, TQl);
  and A12 (TQs, TQw, TQd);
  or O24 (TQ14, TQ2, TQ4);
  and A1 (TQf, TQw, TQp);
  and A13 (TQu, TQs, A);
  or O25 (TQ15, TQ14, TQb);
  and A2 (TQi, TQf, A);
  and A14 (TQ7, TQu, TQv);
  not NC0 (TQ17, TQ15);
  and A3 (TQ8, TQi, TQv);
  and A15 (TQx, TQw, TQd);
  and AH0 (TQ0, TQ16, TQ17);
  // AND_Gate M4 has open pins: in0=TQ16, in1=TQp, out=open
  or O26 (TQ1, TQ18, TQ0);
  and A16 (TQy, TQx, TQ10);
  and A5 (TQn, TQ16, TQp);
  and A17 (TQ9, TQy, B);
  or O27 (TQ6, TQ2, TQ4);

  // Other names for the same wires on the sheet: TQ3 = CLK; TQ5 = RST; TQ12 = B; TQm = Z; TQt = A
endmodule
