// Logisim project gray2bin_4bit.circ as structural Verilog
module gray2bin_4bit (
  input  G0,
  input  G1,
  input  G2,
  input  G3,
  output B0,
  output B1,
  output B2,
  output B3
);

  xor U3 (B2, G2, G3);
  xor U2 (B1, G1, B2);
  xor U1 (B0, G0, B1);

  assign B3 = G3;
endmodule
