// Logisim project graycnt_2bit_test.circ as structural Verilog
module graycnt_2bit_test (
  input  CLK,
  input  RST,
  output G0,
  output Q0,
  output G1,
  output Q1
);

  wire N1_out, X2_out;

  D_Flip_Flop U1 (.D(N1_out), .clk(CLK), .Q(Q0), .reset(RST));  // open: Qn, preset
  D_Flip_Flop U2 (.D(X2_out), .clk(CLK), .Q(G1), .reset(RST));  // open: Qn, preset
  not N1 (N1_out, Q0);
  xor X2 (X2_out, G1, Q0);
  xor G3 (G0, Q0, G1);

  assign Q1 = G1;

  // Other names for the same wires on the sheet: TQ0 = CLK; TQ1 = RST; TQ2 = G0; TQ3 = Q0; TQ4 = G1
endmodule
