// Logisim project graycnt_4bit.circ as structural Verilog
module graycnt_4bit (
  input  CLK,
  input  RST,
  output G0,
  output Q0,
  output G1,
  output Q1,
  output G2,
  output Q2,
  output G3,
  output Q3
);

  wire TQ1, TQ5, TQ6, TQ7, TQ8, TQ9;

  D_Flip_Flop U1 (.D(TQ1), .clk(CLK), .Q(Q0), .reset(RST));  // open: Qn, preset
  xor UG3 (G2, Q2, G3);
  D_Flip_Flop U2 (.D(TQ5), .clk(CLK), .Q(Q1), .reset(RST));  // open: Qn, preset
  D_Flip_Flop U3 (.D(TQ6), .clk(CLK), .Q(Q2), .reset(RST));  // open: Qn, preset
  D_Flip_Flop U4 (.D(TQ9), .clk(CLK), .Q(G3), .reset(RST));  // open: Qn, preset
  not N1 (TQ1, Q0);
  xor X2 (TQ5, Q1, Q0);
  and A3 (TQ7, Q0, Q1);
  xor X4 (TQ6, Q2, TQ7);
  and A5 (TQ8, TQ7, Q2);
  xor X6 (TQ9, G3, TQ8);
  xor UG1 (G0, Q0, Q1);
  xor UG2 (G1, Q1, Q2);

  assign Q3 = G3;

  // Other names for the same wires on the sheet: TQ0 = Q2; TQ2 = CLK; TQ3 = RST; TQ4 = G3; TQa = G0; TQb = G1;
  //   TQc = G2; TQd = Q0; TQe = Q1
endmodule
