// Logisim project graycnt_4bit_test.circ as structural Verilog
module graycnt_4bit_test (
  input  CLK,
  input  RST,
  output G0,
  output Q0,
  output G1,
  output Q1,
  output G2,
  output Q2,
  output G3,
  output Q3
);

  wire TQ6, TQ7, TQ8, TQ9, TQa, TQb;

  D_Flip_Flop U1 (.D(TQ6), .clk(CLK), .Q(Q0), .reset(RST));  // open: Qn, preset
  xor G9 (G2, Q2, G3);
  D_Flip_Flop U2 (.D(TQ7), .clk(CLK), .Q(Q1), .reset(RST));  // open: Qn, preset
  D_Flip_Flop U3 (.D(TQ8), .clk(CLK), .Q(Q2), .reset(RST));  // open: Qn, preset
  D_Flip_Flop U4 (.D(TQb), .clk(CLK), .Q(G3), .reset(RST));  // open: Qn, preset
  not N1 (TQ6, Q0);
  xor X2 (TQ7, Q1, Q0);
  and A3 (TQ9, Q0, Q1);
  xor X4 (TQ8, Q2, TQ9);
  and A5 (TQa, TQ9, Q2);
  xor X6 (TQb, G3, TQa);
  xor G7 (G0, Q0, Q1);
  xor G8 (G1, Q1, Q2);

  assign Q3 = G3;

  // Other names for the same wires on the sheet: TQ0 = Q0; TQ1 = Q1; TQ2 = Q2; TQ3 = G3; TQ4 = CLK; TQ5 = RST;
  //   TQc = G0; TQd = G1; TQe = G2
endmodule
