// Logisim project hex7seg.circ as structural Verilog
module hex7seg (
  input  B0,
  input  B1,
  input  B2,
  input  B3,
  output a,
  output b,
  output c,
  output d,
  output e,
  output f,
  output g
);

  wire B7O297_out, B7O301_out, B7O305_out, B7P296_out, B7P298_out, B7P299_out, B7P300_out, B7P302_out,
       B7P303_out, B7P304_out, B7P306_out, B7P307_out, B7P308_out, TQ0, TQ1, TQ1a, TQ1b, TQ1c, TQ1d, TQ1e,
       TQ1f, TQ1g, TQ1h, TQ1i, TQ1j, TQ1k, TQ1l, TQ1m, TQ1n, TQ1o, TQ1p, TQ1q, TQ1r, TQ1s, TQ1t, TQ1u, TQ1v,
       TQ1w, TQ1x, TQ1y, TQ1z, TQ2, TQ2a, TQ2b, TQ2c, TQ2d, TQ2e, TQ2f, TQ2g, TQ2h, TQ2i, TQ2j, TQ2k, TQ2l,
       TQ2n, TQ2o, TQ2p, TQ2q, TQ2s, TQ2u, TQ2w, TQ2y, TQ3, TQ3a, TQ3b, TQ3c, TQ3d, TQ3e, TQ3f, TQ3g, TQ3h,
       TQ3i, TQ3j, TQ3k, TQ3l, TQ3m, TQ3n, TQ3o, TQ3p, TQ3q, TQ3r, TQ3s, TQ3t, TQ3u, TQ3w, TQ3x, TQ3y, TQ3z,
       TQ4, TQ4a, TQ4b, TQ4c, TQ4d, TQ4e, TQ4f, TQ4g, TQ4h, TQ4i, TQ4j, TQ4k, TQ4l, TQ4m, TQ4n, TQ4o, TQ4p,
       TQ4q, TQ4r, TQ4s, TQ4t, TQ4u, TQ4v, TQ4w, TQ4x, TQ4y, TQ4z, TQ5, TQ5a, TQ5b, TQ5c, TQ5d, TQ5e, TQ5f,
       TQ5g, TQ5h, TQ5i, TQ5j, TQ5k, TQ5l, TQ5m, TQ5n, TQ5o, TQ5p, TQ5q, TQ5r, TQ5s, TQ5t, TQ5u, TQ5v, TQ5w,
       TQ5x, TQ5y, TQ5z, TQ6, TQ6a, TQ6b, TQ6c, TQ6d, TQ6e, TQ6f, TQ6g, TQ6i, TQ6j, TQ6k, TQ6l, TQ6m, TQ6n,
       TQ6o, TQ6p, TQ6q, TQ6r, TQ6s, TQ6t, TQ6u, TQ6v, TQ6w, TQ6x, TQ6y, TQ6z, TQ7, TQ7a, TQ7b, TQ7c, TQ7d,
       TQ7e, TQ7f, TQ7g, TQ7h, TQ7i, TQ7j, TQ7l, TQ7m, TQ7n, TQ7o, TQ7p, TQ7q, TQ7r, TQ7s, TQ7t, TQ7u, TQ7v,
       TQ7w, TQ7x, TQ7y, TQ7z, TQ8, TQ8a, TQ8b, TQ8c, TQ8d, TQ8e, TQ8f, TQ9, TQ10, TQ11, TQ12, TQ13, TQ14,
       TQ15, TQ16, TQ17, TQ18, TQ19, TQ20, TQ21, TQ22, TQ23, TQ24, TQ25, TQ26, TQ27, TQ28, TQ29, TQ30, TQ31,
       TQ32, TQ33, TQ34, TQ35, TQ36, TQ37, TQ38, TQ39, TQ40, TQ41, TQ42, TQ43, TQ44, TQ45, TQ46, TQ47, TQ48,
       TQ49, TQ50, TQ51, TQ52, TQ53, TQ54, TQ55, TQ57, TQ58, TQ59, TQ60, TQ61, TQ62, TQ63, TQ64, TQ65, TQ66,
       TQ67, TQ68, TQ69, TQ70, TQ71, TQ72, TQ73, TQ74, TQ75, TQ76, TQ77, TQ78, TQ79, TQ80, TQ81, TQ82, TQ83,
       TQ84, TQ85, TQ86, TQ87, TQ88, TQ89, TQa, TQb, TQc, TQd, TQe, TQf, TQg, TQh, TQj, TQk, TQl, TQm, TQn,
       TQo, TQp, TQq, TQr, TQs, TQt, TQu, TQv, TQw, TQx, TQy, TQz;

  not B7N1 (TQ2n, B0);
  not B7N2 (TQ2i, B1);
  not B7N3 (TQ2c, B2);
  not B7N4 (TQ1i, B3);
  and B7P1 (TQ3, TQ2n, TQ2i);
  and B7P2 (TQ5, TQ3, TQ2c);
  and B7P3 (TQc, TQ5, TQ1i);
  and B7P4 (TQ9, TQ2n, B1);
  and B7P5 (TQa, TQ9, TQ2c);
  and B7P6 (TQe, TQa, TQ1i);
  or B7O7 (TQl, TQc, TQe);
  and B7P8 (TQh, B0, B1);
  and B7P9 (TQj, TQh, TQ2c);
  and B7P10 (TQm, TQj, TQ1i);
  or B7O11 (TQs, TQl, TQm);
  and B7P12 (TQo, B0, TQ2i);
  and B7P13 (TQq, TQo, B2);
  and B7P14 (TQt, TQq, TQ1i);
  or B7O15 (TQ10, TQs, TQt);
  and B7P16 (TQw, TQ2n, B1);
  and B7P17 (TQy, TQw, B2);
  and B7P18 (TQ11, TQy, TQ1i);
  or B7O19 (TQ18, TQ10, TQ11);
  and B7P20 (TQ14, B0, B1);
  and B7P21 (TQ16, TQ14, B2);
  and B7P22 (TQ19, TQ16, TQ1i);
  or B7O23 (TQ1g, TQ18, TQ19);
  and B7P24 (TQ1c, TQ2n, TQ2i);
  and B7P25 (TQ1e, TQ1c, TQ2c);
  and B7P26 (TQ1h, TQ1e, B3);
  or B7O27 (TQ1p, TQ1g, TQ1h);
  and B7P28 (TQ1l, B0, TQ2i);
  and B7P29 (TQ1n, TQ1l, TQ2c);
  and B7P30 (TQ1q, TQ1n, B3);
  or B7O31 (TQ1x, TQ1p, TQ1q);
  and B7P32 (TQ1t, TQ2n, B1);
  and B7P33 (TQ1v, TQ1t, TQ2c);
  and B7P34 (TQ1y, TQ1v, B3);
  or B7O35 (TQ25, TQ1x, TQ1y);
  and B7P36 (TQ21, TQ2n, TQ2i);
  and B7P37 (TQ23, TQ21, B2);
  and B7P38 (TQ26, TQ23, B3);
  or B7O39 (TQ2e, TQ25, TQ26);
  and B7P40 (TQ29, TQ2n, B1);
  and B7P41 (TQ2b, TQ29, B2);
  and B7P42 (TQ2f, TQ2b, B3);
  or B7O43 (TQ2k, TQ2e, TQ2f);
  and B7P44 (TQ2h, B0, B1);
  and B7P45 (TQ2j, TQ2h, B2);
  and B7P46 (TQ2l, TQ2j, B3);
  or B7O47 (a, TQ2k, TQ2l);
  and B7P48 (TQ2o, TQ2n, TQ2i);
  and B7P49 (TQ2p, TQ2o, TQ2c);
  and B7P50 (TQ2u, TQ2p, TQ1i);
  and B7P51 (TQ2q, B0, TQ2i);
  and B7P52 (TQ2s, TQ2q, TQ2c);
  and B7P53 (TQ2w, TQ2s, TQ1i);
  or B7O54 (TQ31, TQ2u, TQ2w);
  and B7P55 (TQ2y, TQ2n, B1);
  and B7P56 (TQ30, TQ2y, TQ2c);
  and B7P57 (TQ32, TQ30, TQ1i);
  or B7O58 (TQ35, TQ31, TQ32);
  and B7P59 (TQ33, B0, B1);
  and B7P60 (TQ34, TQ33, TQ2c);
  and B7P61 (TQ36, TQ34, TQ1i);
  or B7O62 (TQ39, TQ35, TQ36);
  and B7P63 (TQ37, TQ2n, TQ2i);
  and B7P64 (TQ38, TQ37, B2);
  and B7P65 (TQ3a, TQ38, TQ1i);
  or B7O66 (TQ3d, TQ39, TQ3a);
  and B7P67 (TQ3b, B0, B1);
  and B7P68 (TQ3c, TQ3b, B2);
  and B7P69 (TQ3e, TQ3c, TQ1i);
  or B7O70 (TQ3h, TQ3d, TQ3e);
  and B7P71 (TQ3f, TQ2n, TQ2i);
  and B7P72 (TQ3g, TQ3f, TQ2c);
  and B7P73 (TQ3i, TQ3g, B3);
  or B7O74 (TQ3l, TQ3h, TQ3i);
  and B7P75 (TQ3j, B0, TQ2i);
  and B7P76 (TQ3k, TQ3j, TQ2c);
  and B7P77 (TQ3m, TQ3k, B3);
  or B7O78 (TQ3p, TQ3l, TQ3m);
  and B7P79 (TQ3n, TQ2n, B1);
  and B7P80 (TQ3o, TQ3n, TQ2c);
  and B7P81 (TQ3q, TQ3o, B3);
  or B7O82 (TQ3t, TQ3p, TQ3q);
  and B7P83 (TQ3r, B0, TQ2i);
  and B7P84 (TQ3s, TQ3r, B2);
  and B7P85 (TQ3u, TQ3s, B3);
  or B7O86 (b, TQ3t, TQ3u);
  and B7P87 (TQ3w, TQ2n, TQ2i);
  and B7P88 (TQ3x, TQ3w, TQ2c);
  and B7P89 (TQ40, TQ3x, TQ1i);
  and B7P90 (TQ3y, B0, TQ2i);
  and B7P91 (TQ3z, TQ3y, TQ2c);
  and B7P92 (TQ41, TQ3z, TQ1i);
  or B7O93 (TQ44, TQ40, TQ41);
  and B7P94 (TQ42, B0, B1);
  and B7P95 (TQ43, TQ42, TQ2c);
  and B7P96 (TQ45, TQ43, TQ1i);
  or B7O97 (TQ48, TQ44, TQ45);
  and B7P98 (TQ46, TQ2n, TQ2i);
  and B7P99 (TQ47, TQ46, B2);
  and B7P100 (TQ49, TQ47, TQ1i);
  or B7O101 (TQ4c, TQ48, TQ49);
  and B7P102 (TQ4a, B0, TQ2i);
  and B7P103 (TQ4b, TQ4a, B2);
  and B7P104 (TQ4d, TQ4b, TQ1i);
  or B7O105 (TQ4g, TQ4c, TQ4d);
  and B7P106 (TQ4e, TQ2n, B1);
  and B7P107 (TQ4f, TQ4e, B2);
  and B7P108 (TQ4h, TQ4f, TQ1i);
  or B7O109 (TQ4k, TQ4g, TQ4h);
  and B7P110 (TQ4i, B0, B1);
  and B7P111 (TQ4j, TQ4i, B2);
  and B7P112 (TQ4l, TQ4j, TQ1i);
  or B7O113 (TQ4o, TQ4k, TQ4l);
  and B7P114 (TQ4m, TQ2n, TQ2i);
  and B7P115 (TQ4n, TQ4m, TQ2c);
  and B7P116 (TQ4p, TQ4n, B3);
  or B7O117 (TQ4s, TQ4o, TQ4p);
  and B7P118 (TQ4q, B0, TQ2i);
  and B7P119 (TQ4r, TQ4q, TQ2c);
  and B7P120 (TQ4t, TQ4r, B3);
  or B7O121 (TQ4w, TQ4s, TQ4t);
  and B7P122 (TQ4u, TQ2n, B1);
  and B7P123 (TQ4v, TQ4u, TQ2c);
  and B7P124 (TQ4x, TQ4v, B3);
  or B7O125 (TQ50, TQ4w, TQ4x);
  and B7P126 (TQ4y, B0, B1);
  and B7P127 (TQ4z, TQ4y, TQ2c);
  and B7P128 (TQ51, TQ4z, B3);
  or B7O129 (TQ54, TQ50, TQ51);
  and B7P130 (TQ52, B0, TQ2i);
  and B7P131 (TQ53, TQ52, B2);
  and B7P132 (TQ55, TQ53, B3);
  or B7O133 (c, TQ54, TQ55);
  and B7P134 (TQ57, TQ2n, TQ2i);
  and B7P135 (TQ58, TQ57, TQ2c);
  and B7P136 (TQ5b, TQ58, TQ1i);
  and B7P137 (TQ59, TQ2n, B1);
  and B7P138 (TQ5a, TQ59, TQ2c);
  and B7P139 (TQ5c, TQ5a, TQ1i);
  or B7O140 (TQ5f, TQ5b, TQ5c);
  and B7P141 (TQ5d, B0, B1);
  and B7P142 (TQ5e, TQ5d, TQ2c);
  and B7P143 (TQ5g, TQ5e, TQ1i);
  or B7O144 (TQ5j, TQ5f, TQ5g);
  and B7P145 (TQ5h, B0, TQ2i);
  and B7P146 (TQ5i, TQ5h, B2);
  and B7P147 (TQ5k, TQ5i, TQ1i);
  or B7O148 (TQ5n, TQ5j, TQ5k);
  and B7P149 (TQ5l, TQ2n, B1);
  and B7P150 (TQ5m, TQ5l, B2);
  and B7P151 (TQ5o, TQ5m, TQ1i);
  or B7O152 (TQ5r, TQ5n, TQ5o);
  and B7P153 (TQ5p, TQ2n, TQ2i);
  and B7P154 (TQ5q, TQ5p, TQ2c);
  and B7P155 (TQ5s, TQ5q, B3);
  or B7O156 (TQ5v, TQ5r, TQ5s);
  and B7P157 (TQ5t, B0, TQ2i);
  and B7P158 (TQ5u, TQ5t, TQ2c);
  and B7P159 (TQ5w, TQ5u, B3);
  or B7O160 (TQ5z, TQ5v, TQ5w);
  and B7P161 (TQ5x, TQ2n, B1);
  and B7P162 (TQ5y, TQ5x, TQ2c);
  and B7P163 (TQ60, TQ5y, B3);
  or B7O164 (TQ63, TQ5z, TQ60);
  and B7P165 (TQ61, B0, B1);
  and B7P166 (TQ62, TQ61, TQ2c);
  and B7P167 (TQ64, TQ62, B3);
  or B7O168 (TQ67, TQ63, TQ64);
  and B7P169 (TQ65, TQ2n, TQ2i);
  and B7P170 (TQ66, TQ65, B2);
  and B7P171 (TQ68, TQ66, B3);
  or B7O172 (TQ6b, TQ67, TQ68);
  and B7P173 (TQ69, B0, TQ2i);
  and B7P174 (TQ6a, TQ69, B2);
  and B7P175 (TQ6c, TQ6a, B3);
  or B7O176 (TQ6f, TQ6b, TQ6c);
  and B7P177 (TQ6d, TQ2n, B1);
  and B7P178 (TQ6e, TQ6d, B2);
  and B7P179 (TQ6g, TQ6e, B3);
  or B7O180 (d, TQ6f, TQ6g);
  and B7P181 (TQ6i, TQ2n, TQ2i);
  and B7P182 (TQ6j, TQ6i, TQ2c);
  and B7P183 (TQ6m, TQ6j, TQ1i);
  and B7P184 (TQ6k, TQ2n, B1);
  and B7P185 (TQ6l, TQ6k, TQ2c);
  and B7P186 (TQ6n, TQ6l, TQ1i);
  or B7O187 (TQ6q, TQ6m, TQ6n);
  and B7P188 (TQ6o, TQ2n, B1);
  and B7P189 (TQ6p, TQ6o, B2);
  and B7P190 (TQ6r, TQ6p, TQ1i);
  or B7O191 (TQ6u, TQ6q, TQ6r);
  and B7P192 (TQ6s, TQ2n, TQ2i);
  and B7P193 (TQ6t, TQ6s, TQ2c);
  and B7P194 (TQ6v, TQ6t, B3);
  or B7O195 (TQ6y, TQ6u, TQ6v);
  and B7P196 (TQ6w, TQ2n, B1);
  and B7P197 (TQ6x, TQ6w, TQ2c);
  and B7P198 (TQ6z, TQ6x, B3);
  or B7O199 (TQ72, TQ6y, TQ6z);
  and B7P200 (TQ70, B0, B1);
  and B7P201 (TQ71, TQ70, TQ2c);
  and B7P202 (TQ73, TQ71, B3);
  or B7O203 (TQ76, TQ72, TQ73);
  and B7P204 (TQ74, TQ2n, TQ2i);
  and B7P205 (TQ75, TQ74, B2);
  and B7P206 (TQ77, TQ75, B3);
  or B7O207 (TQ7a, TQ76, TQ77);
  and B7P208 (TQ78, B0, TQ2i);
  and B7P209 (TQ79, TQ78, B2);
  and B7P210 (TQ7b, TQ79, B3);
  or B7O211 (TQ7e, TQ7a, TQ7b);
  and B7P212 (TQ7c, TQ2n, B1);
  and B7P213 (TQ7d, TQ7c, B2);
  and B7P214 (TQ7f, TQ7d, B3);
  or B7O215 (TQ7i, TQ7e, TQ7f);
  and B7P216 (TQ7g, B0, B1);
  and B7P217 (TQ7h, TQ7g, B2);
  and B7P218 (TQ7j, TQ7h, B3);
  or B7O219 (e, TQ7i, TQ7j);
  and B7P220 (TQ7l, TQ2n, TQ2i);
  and B7P221 (TQ7m, TQ7l, TQ2c);
  and B7P222 (TQ7p, TQ7m, TQ1i);
  and B7P223 (TQ7n, TQ2n, TQ2i);
  and B7P224 (TQ7o, TQ7n, B2);
  and B7P225 (TQ7q, TQ7o, TQ1i);
  or B7O226 (TQ7t, TQ7p, TQ7q);
  and B7P227 (TQ7r, B0, TQ2i);
  and B7P228 (TQ7s, TQ7r, B2);
  and B7P229 (TQ7u, TQ7s, TQ1i);
  or B7O230 (TQ7x, TQ7t, TQ7u);
  and B7P231 (TQ7v, TQ2n, B1);
  and B7P232 (TQ7w, TQ7v, B2);
  and B7P233 (TQ7y, TQ7w, TQ1i);
  or B7O234 (TQ81, TQ7x, TQ7y);
  and B7P235 (TQ7z, TQ2n, TQ2i);
  and B7P236 (TQ80, TQ7z, TQ2c);
  and B7P237 (TQ82, TQ80, B3);
  or B7O238 (TQ85, TQ81, TQ82);
  and B7P239 (TQ83, B0, TQ2i);
  and B7P240 (TQ84, TQ83, TQ2c);
  and B7P241 (TQ86, TQ84, B3);
  or B7O242 (TQ89, TQ85, TQ86);
  and B7P243 (TQ87, TQ2n, B1);
  and B7P244 (TQ88, TQ87, TQ2c);
  and B7P245 (TQ8a, TQ88, B3);
  or B7O246 (TQ8d, TQ89, TQ8a);
  and B7P247 (TQ8b, B0, B1);
  and B7P248 (TQ8c, TQ8b, TQ2c);
  and B7P249 (TQ8e, TQ8c, B3);
  or B7O250 (TQ1, TQ8d, TQ8e);
  and B7P251 (TQ8f, TQ2n, TQ2i);
  and B7P252 (TQ0, TQ8f, B2);
  and B7P253 (TQ2, TQ0, B3);
  or B7O254 (TQ7, TQ1, TQ2);
  and B7P255 (TQ4, TQ2n, B1);
  and B7P256 (TQ6, TQ4, B2);
  and B7P257 (TQ8, TQ6, B3);
  or B7O258 (TQf, TQ7, TQ8);
  and B7P259 (TQb, B0, B1);
  and B7P260 (TQd, TQb, B2);
  and B7P261 (TQg, TQd, B3);
  or B7O262 (f, TQf, TQg);
  and B7P263 (TQk, TQ2n, B1);
  and B7P264 (TQn, TQk, TQ2c);
  and B7P265 (TQu, TQn, TQ1i);
  and B7P266 (TQp, B0, B1);
  and B7P267 (TQr, TQp, TQ2c);
  and B7P268 (TQv, TQr, TQ1i);
  or B7O269 (TQ12, TQu, TQv);
  and B7P270 (TQx, TQ2n, TQ2i);
  and B7P271 (TQz, TQx, B2);
  and B7P272 (TQ13, TQz, TQ1i);
  or B7O273 (TQ1a, TQ12, TQ13);
  and B7P274 (TQ15, B0, TQ2i);
  and B7P275 (TQ17, TQ15, B2);
  and B7P276 (TQ1b, TQ17, TQ1i);
  or B7O277 (TQ1j, TQ1a, TQ1b);
  and B7P278 (TQ1d, TQ2n, B1);
  and B7P279 (TQ1f, TQ1d, B2);
  and B7P280 (TQ1k, TQ1f, TQ1i);
  or B7O281 (TQ1r, TQ1j, TQ1k);
  and B7P282 (TQ1m, TQ2n, TQ2i);
  and B7P283 (TQ1o, TQ1m, TQ2c);
  and B7P284 (TQ1s, TQ1o, B3);
  or B7O285 (TQ1z, TQ1r, TQ1s);
  and B7P286 (TQ1u, B0, TQ2i);
  and B7P287 (TQ1w, TQ1u, TQ2c);
  and B7P288 (TQ20, TQ1w, B3);
  or B7O289 (TQ27, TQ1z, TQ20);
  and B7P290 (TQ22, TQ2n, B1);
  and B7P291 (TQ24, TQ22, TQ2c);
  and B7P292 (TQ28, TQ24, B3);
  or B7O293 (TQ2g, TQ27, TQ28);
  and B7P294 (TQ2a, B0, B1);
  and B7P295 (TQ2d, TQ2a, TQ2c);
  and B7P296 (B7P296_out, TQ2d, B3);
  or B7O297 (B7O297_out, TQ2g, B7P296_out);
  and B7P298 (B7P298_out, B0, TQ2i);
  and B7P299 (B7P299_out, B7P298_out, B2);
  and B7P300 (B7P300_out, B7P299_out, B3);
  or B7O301 (B7O301_out, B7O297_out, B7P300_out);
  and B7P302 (B7P302_out, TQ2n, B1);
  and B7P303 (B7P303_out, B7P302_out, B2);
  and B7P304 (B7P304_out, B7P303_out, B3);
  or B7O305 (B7O305_out, B7O301_out, B7P304_out);
  and B7P306 (B7P306_out, B0, B1);
  and B7P307 (B7P307_out, B7P306_out, B2);
  and B7P308 (B7P308_out, B7P307_out, B3);
  or B7O309 (g, B7O305_out, B7P308_out);

  // Other names for the same wires on the sheet: TQ2m = a; TQ2r = B0; TQ2t = B1; TQ2v = B2; TQ2x = B3; TQ2z = g;
  //   TQ3v = b; TQ6h = d; TQ7k = e; TQ56 = c; TQi = f
endmodule
