// Logisim project jk_flipflop.circ as structural Verilog: 1 circuit, main circuit main
module main (
  input  PRE,
  input  J,
  input  K,
  input  CLK,
  input  CLR,
  output Q,
  output nQ
);

  J_K_Flip_Flop JK (.J(J), .K(K), .clk(CLK), .Q(Q), .Qn(nQ), .preset(PRE), .reset(CLR));
endmodule
