// Logisim project jkff.circ as structural Verilog
module jkff (
  input  CLK,
  input  J,
  input  K,
  input  RST,
  output Q,
  output nQ
);

  wire U2_out, U3_out, U4_out, U5_out;

  D_Flip_Flop U1 (.D(U5_out), .clk(CLK), .Q(Q), .Qn(nQ), .preset(RST), .reset(RST));
  not U2 (U2_out, K);
  and U3 (U3_out, J, nQ);
  and U4 (U4_out, U2_out, Q);
  or U5 (U5_out, U3_out, U4_out);
endmodule
