// Logisim project johnson_4stage.circ as structural Verilog
module johnson_4stage (
  input  RST,
  output Q0,
  output Q1,
  output Q2,
  output Q3
);

  wire CLK_out, JN_out;

  Clock CLK (.out(CLK_out));
  not JN (JN_out, Q3);
  D_Flip_Flop U1 (.D(JN_out), .clk(CLK_out), .Q(Q0), .preset(RST), .reset(RST));  // open: Qn
  D_Flip_Flop U2 (.D(Q0), .clk(CLK_out), .Q(Q1), .preset(RST), .reset(RST));  // open: Qn
  D_Flip_Flop U3 (.D(Q1), .clk(CLK_out), .Q(Q2), .preset(RST), .reset(RST));  // open: Qn
  D_Flip_Flop U4 (.D(Q2), .clk(CLK_out), .Q(Q3), .preset(RST), .reset(RST));  // open: Qn
endmodule
