// Logisim project lfsr_4bit.circ as structural Verilog
module lfsr_4bit (
  input  CLK,
  input  SEED,
  input  RST,
  output Q0,
  output Q1,
  output Q2,
  output Q3
);

  wire O1_out, X1_out;

  D_Flip_Flop U1 (.D(O1_out), .clk(CLK), .Q(Q0), .preset(RST), .reset(RST));  // open: Qn
  D_Flip_Flop U2 (.D(Q0), .clk(CLK), .Q(Q1), .preset(RST), .reset(RST));  // open: Qn
  D_Flip_Flop U3 (.D(Q1), .clk(CLK), .Q(Q2), .preset(RST), .reset(RST));  // open: Qn
  D_Flip_Flop U4 (.D(Q2), .clk(CLK), .Q(Q3), .preset(RST), .reset(RST));  // open: Qn
  xor X1 (X1_out, Q3, Q2);
  or O1 (O1_out, SEED, X1_out);
endmodule
