// Logisim project logic_f_abc.circ as structural Verilog
module logic_f_abc (
  input  A,
  input  B,
  input  C,
  output F
);

  wire n4, n5;

  or or_1 (n4, A, B);
  or or_2 (n5, n4, C);
  not not_1 (F, n5);

  // Other names for the same wires on the sheet: n1 = A; n2 = B; n3 = C; n6 = F
endmodule
