// Logisim project mac_4bit.circ as structural Verilog
module mac_4bit (
  input  RST,
  input  GND,
  input  A0,
  input  A1,
  input  A2,
  input  A3,
  input  B0,
  input  B1,
  input  B2,
  input  B3,
  output Q0,
  output Q1,
  output Q2,
  output Q3,
  output Q4,
  output Q5,
  output Q6,
  output Q7
);

  wire MACH41_out, MACH42_out, MACI40_out, MACI41_out, MACI42_out, MACJ40_out, MACJ41_out, MACJ42_out,
       MACK40_out, MACK41_out, MACY41_out, MACY42_out, TQ0, TQ1, TQ1a, TQ1b, TQ1c, TQ1d, TQ1e, TQ1f, TQ1g,
       TQ1h, TQ1i, TQ1j, TQ1k, TQ1l, TQ1m, TQ1n, TQ1o, TQ1p, TQ1q, TQ1r, TQ1s, TQ1t, TQ1u, TQ1v, TQ1w, TQ1y,
       TQ1z, TQ2, TQ2a, TQ2b, TQ2c, TQ2d, TQ2f, TQ2h, TQ2i, TQ2j, TQ2k, TQ2m, TQ2n, TQ2o, TQ2p, TQ2q, TQ2s,
       TQ2t, TQ2w, TQ2x, TQ2y, TQ2z, TQ3a, TQ3b, TQ3c, TQ3d, TQ3e, TQ3f, TQ3g, TQ3h, TQ3i, TQ3j, TQ3k, TQ3l,
       TQ3m, TQ3n, TQ3o, TQ3p, TQ3q, TQ3r, TQ3s, TQ3t, TQ3u, TQ3v, TQ3w, TQ3x, TQ3y, TQ3z, TQ4, TQ4a, TQ4b,
       TQ4c, TQ4d, TQ4e, TQ4f, TQ4g, TQ4h, TQ4i, TQ4j, TQ4k, TQ4l, TQ4m, TQ4n, TQ4o, TQ4p, TQ4q, TQ4r, TQ4s,
       TQ5, TQ6, TQ7, TQ8, TQ9, TQ10, TQ11, TQ12, TQ13, TQ14, TQ15, TQ16, TQ17, TQ18, TQ19, TQ20, TQ21, TQ23,
       TQ25, TQ26, TQ27, TQ29, TQ30, TQ31, TQ32, TQ33, TQ34, TQ35, TQ36, TQ37, TQ38, TQ39, TQ40, TQ41, TQ42,
       TQ43, TQ44, TQ45, TQ46, TQ47, TQ48, TQ49, TQb, TQc, TQd, TQf, TQh, TQi, TQn, TQo, TQp, TQq, TQr, TQs,
       TQt, TQu, TQv, TQw, TQx, TQy, TQz;

  Clock CLK (.out(TQ2t));
  D_Flip_Flop U1 (.D(TQ1y), .clk(TQ2t), .Q(Q0), .reset(RST));  // open: Qn, preset
  D_Flip_Flop U2 (.D(TQ23), .clk(TQ2t), .Q(Q1), .reset(RST));  // open: Qn, preset
  D_Flip_Flop U3 (.D(TQ25), .clk(TQ2t), .Q(Q2), .reset(RST));  // open: Qn, preset
  D_Flip_Flop U4 (.D(TQ2a), .clk(TQ2t), .Q(Q3), .reset(RST));  // open: Qn, preset
  D_Flip_Flop U5 (.D(TQ2f), .clk(TQ2t), .Q(Q4), .reset(RST));  // open: Qn, preset
  D_Flip_Flop U6 (.D(TQ2h), .clk(TQ2t), .Q(Q5), .reset(RST));  // open: Qn, preset
  D_Flip_Flop U7 (.D(TQ2n), .clk(TQ2t), .Q(Q6), .reset(RST));  // open: Qn, preset
  D_Flip_Flop U8 (.D(TQ2s), .clk(TQ2t), .Q(Q7), .reset(RST));  // open: Qn, preset
  and MACP1 (TQ4r, A0, B0);
  and MACP2 (TQr, A1, B0);
  and MACP3 (TQ13, A2, B0);
  and MACP4 (TQ1g, A3, B0);
  and MACP5 (TQt, A0, B1);
  and MACP6 (TQ15, A1, B1);
  and MACP7 (TQ1h, A2, B1);
  and MACP8 (TQ1o, A3, B1);
  and MACP9 (TQ27, A0, B2);
  and MACP10 (TQ2j, A1, B2);
  and MACP11 (TQ2x, A2, B2);
  and MACP12 (TQ34, A3, B2);
  and MACP13 (TQ3l, A0, B3);
  and MACP14 (TQ3r, A1, B3);
  and MACP15 (TQ3y, A2, B3);
  and MACP16 (TQ45, A3, B3);
  xor MACX17 (TQv, TQr, TQt);
  xor MACS17 (TQ4, TQv, GND);
  and MACA17 (TQw, TQr, TQt);
  and MACB17 (TQx, GND, TQv);
  or MACO17 (TQy, TQw, TQx);
  or MACG17 (TQ17, TQy, GND);
  xor MACX18 (TQ18, TQ13, TQ15);
  xor MACS18 (TQ26, TQ18, TQ17);
  and MACA18 (TQ19, TQ13, TQ15);
  and MACB18 (TQ1a, TQ17, TQ18);
  or MACO18 (TQ1b, TQ19, TQ1a);
  or MACG18 (TQ1i, TQ1b, GND);
  xor MACX19 (TQ1j, TQ1g, TQ1h);
  xor MACS19 (TQ2i, TQ1j, TQ1i);
  and MACA19 (TQ1k, TQ1g, TQ1h);
  and MACB19 (TQ1l, TQ1i, TQ1j);
  or MACO19 (TQ1m, TQ1k, TQ1l);
  or MACG19 (TQ1p, TQ1m, GND);
  xor MACX20 (TQ1q, GND, TQ1o);
  xor MACS20 (TQ2w, TQ1q, TQ1p);
  and MACA20 (TQ1r, GND, TQ1o);
  and MACB20 (TQ1s, TQ1p, TQ1q);
  or MACO20 (TQ1t, TQ1r, TQ1s);
  or MACG20 (TQ1v, TQ1t, GND);
  xor MACX21 (TQ1w, GND, GND);
  xor MACS21 (TQ33, TQ1w, TQ1v);
  and MACA21 (TQ1z, GND, GND);
  and MACB21 (TQ20, TQ1v, TQ1w);
  or MACO21 (TQ21, TQ1z, TQ20);
  // OR_Gate MACG21 has open pins: in0=TQ21, in1=GND, out=open
  xor MACX22 (TQ29, TQ26, TQ27);
  xor MACS22 (TQb, TQ29, GND);
  and MACA22 (TQ2b, TQ26, TQ27);
  and MACB22 (TQ2c, GND, TQ29);
  or MACO22 (TQ2d, TQ2b, TQ2c);
  or MACG22 (TQ2k, TQ2d, GND);
  xor MACX23 (TQ2m, TQ2i, TQ2j);
  xor MACS23 (TQ3k, TQ2m, TQ2k);
  and MACA23 (TQ2o, TQ2i, TQ2j);
  and MACB23 (TQ2p, TQ2k, TQ2m);
  or MACO23 (TQ2q, TQ2o, TQ2p);
  or MACG23 (TQ2y, TQ2q, GND);
  xor MACX24 (TQ2z, TQ2w, TQ2x);
  xor MACS24 (TQ3q, TQ2z, TQ2y);
  and MACA24 (TQ30, TQ2w, TQ2x);
  and MACB24 (TQ31, TQ2y, TQ2z);
  or MACO24 (TQ32, TQ30, TQ31);
  or MACG24 (TQ35, TQ32, GND);
  xor MACX25 (TQ36, TQ33, TQ34);
  xor MACS25 (TQ3x, TQ36, TQ35);
  and MACA25 (TQ37, TQ33, TQ34);
  and MACB25 (TQ38, TQ35, TQ36);
  or MACO25 (TQ39, TQ37, TQ38);
  or MACG25 (TQ3a, TQ39, GND);
  xor MACX26 (TQ3b, GND, GND);
  xor MACS26 (TQ44, TQ3b, TQ3a);
  and MACA26 (TQ3c, GND, GND);
  and MACB26 (TQ3d, TQ3a, TQ3b);
  or MACO26 (TQ3e, TQ3c, TQ3d);
  or MACG26 (TQ3f, TQ3e, GND);
  xor MACX27 (TQ3g, GND, GND);
  xor MACS27 (TQ4b, TQ3g, TQ3f);
  and MACA27 (TQ3h, GND, GND);
  and MACB27 (TQ3i, TQ3f, TQ3g);
  or MACO27 (TQ3j, TQ3h, TQ3i);
  // OR_Gate MACG27 has open pins: in0=TQ3j, in1=GND, out=open
  xor MACX28 (TQ3m, TQ3k, TQ3l);
  xor MACS28 (TQn, TQ3m, GND);
  and MACA28 (TQ3n, TQ3k, TQ3l);
  and MACB28 (TQ3o, GND, TQ3m);
  or MACO28 (TQ3p, TQ3n, TQ3o);
  or MACG28 (TQ3s, TQ3p, GND);
  xor MACX29 (TQ3t, TQ3q, TQ3r);
  xor MACS29 (TQz, TQ3t, TQ3s);
  and MACA29 (TQ3u, TQ3q, TQ3r);
  and MACB29 (TQ3v, TQ3s, TQ3t);
  or MACO29 (TQ3w, TQ3u, TQ3v);
  or MACG29 (TQ3z, TQ3w, GND);
  xor MACX30 (TQ40, TQ3x, TQ3y);
  xor MACS30 (TQ1c, TQ40, TQ3z);
  and MACA30 (TQ41, TQ3x, TQ3y);
  and MACB30 (TQ42, TQ3z, TQ40);
  or MACO30 (TQ43, TQ41, TQ42);
  or MACG30 (TQ46, TQ43, GND);
  xor MACX31 (TQ47, TQ44, TQ45);
  xor MACS31 (TQ1n, TQ47, TQ46);
  and MACA31 (TQ48, TQ44, TQ45);
  and MACB31 (TQ49, TQ46, TQ47);
  or MACO31 (TQ4a, TQ48, TQ49);
  or MACG31 (TQ4c, TQ4a, GND);
  xor MACX32 (TQ4d, TQ4b, GND);
  xor MACS32 (TQ1u, TQ4d, TQ4c);
  and MACA32 (TQ4e, TQ4b, GND);
  and MACB32 (TQ4f, TQ4c, TQ4d);
  or MACO32 (TQ4g, TQ4e, TQ4f);
  or MACG32 (TQ4h, TQ4g, GND);
  xor MACX33 (TQ4i, GND, GND);
  // XOR_Gate MACS33 has open pins: in0=TQ4i, in1=TQ4h, out=open
  and MACA33 (TQ4j, GND, GND);
  and MACB33 (TQ4k, TQ4h, TQ4i);
  or MACO33 (TQ4l, TQ4j, TQ4k);
  or MACG33 (TQ4m, TQ4l, GND);
  xor MACX34 (TQ4n, GND, GND);
  // XOR_Gate MACS34 has open pins: in0=TQ4n, in1=TQ4m, out=open
  and MACA34 (TQ4o, GND, GND);
  and MACB34 (TQ4p, TQ4m, TQ4n);
  or MACO34 (TQ4q, TQ4o, TQ4p);
  // OR_Gate MACG34 has open pins: in0=TQ4q, in1=GND, out=open
  xor MACY35 (TQ4s, TQ4r, Q0);
  xor MACT35 (TQ1y, TQ4s, GND);
  and MACH35 (TQ0, TQ4r, Q0);
  and MACI35 (TQ1, GND, TQ4s);
  or MACJ35 (TQ2, TQ0, TQ1);
  or MACK35 (TQ5, TQ2, GND);
  xor MACY36 (TQ6, TQ4, Q1);
  xor MACT36 (TQ23, TQ6, TQ5);
  and MACH36 (TQ7, TQ4, Q1);
  and MACI36 (TQ8, TQ5, TQ6);
  or MACJ36 (TQ9, TQ7, TQ8);
  or MACK36 (TQc, TQ9, GND);
  xor MACY37 (TQd, TQb, Q2);
  xor MACT37 (TQ25, TQd, TQc);
  and MACH37 (TQf, TQb, Q2);
  and MACI37 (TQh, TQc, TQd);
  or MACJ37 (TQi, TQf, TQh);
  or MACK37 (TQo, TQi, GND);
  xor MACY38 (TQp, TQn, Q3);
  xor MACT38 (TQ2a, TQp, TQo);
  and MACH38 (TQq, TQn, Q3);
  and MACI38 (TQs, TQo, TQp);
  or MACJ38 (TQu, TQq, TQs);
  or MACK38 (TQ10, TQu, GND);
  xor MACY39 (TQ11, TQz, Q4);
  xor MACT39 (TQ2f, TQ11, TQ10);
  and MACH39 (TQ12, TQz, Q4);
  and MACI39 (TQ14, TQ10, TQ11);
  or MACJ39 (TQ16, TQ12, TQ14);
  or MACK39 (TQ1d, TQ16, GND);
  xor MACY40 (TQ1e, TQ1c, Q5);
  xor MACT40 (TQ2h, TQ1e, TQ1d);
  and MACH40 (TQ1f, TQ1c, Q5);
  and MACI40 (MACI40_out, TQ1d, TQ1e);
  or MACJ40 (MACJ40_out, TQ1f, MACI40_out);
  or MACK40 (MACK40_out, MACJ40_out, GND);
  xor MACY41 (MACY41_out, TQ1n, Q6);
  xor MACT41 (TQ2n, MACY41_out, MACK40_out);
  and MACH41 (MACH41_out, TQ1n, Q6);
  and MACI41 (MACI41_out, MACK40_out, MACY41_out);
  or MACJ41 (MACJ41_out, MACH41_out, MACI41_out);
  or MACK41 (MACK41_out, MACJ41_out, GND);
  xor MACY42 (MACY42_out, TQ1u, Q7);
  xor MACT42 (TQ2s, MACY42_out, MACK41_out);
  and MACH42 (MACH42_out, TQ1u, Q7);
  and MACI42 (MACI42_out, MACK41_out, MACY42_out);
  or MACJ42 (MACJ42_out, MACH42_out, MACI42_out);
  // OR_Gate MACK42 has open pins: in0=MACJ42_out, in1=GND, out=open

  // Other names for the same wires on the sheet: TQ1x = GND; TQ2e = Q3; TQ2g = Q4; TQ2l = Q5; TQ2r = Q6; TQ2u = RST;
  //   TQ2v = Q7; TQ3 = B0; TQ22 = Q0; TQ24 = Q1; TQ28 = Q2; TQa = B1; TQe = B2; TQg = A0; TQj = A1; TQk = A2;
  //   TQl = A3; TQm = B3
endmodule
