// Logisim project mod100_counter.circ as structural Verilog
module mod100_counter (
  input  CLK,
  input  RST,
  output Q0,
  output Q1,
  output Q2,
  output Q3,
  output Q4,
  output Q5,
  output Q6,
  output TC
);

  wire TQ1, TQ3, TQ4, TQ6, TQ9, TQb, TQc, TQd, TQe, TQf, TQg, TQh, TQi, TQj, TQk, TQl, TQm, TQn, TQo, TQp,
       TQq, TQr, TQs, TQu;

  T_Flip_Flop U1 (.T(TQe), .clk(CLK), .Q(Q0), .reset(RST));  // open: Qn, preset
  not N5 (TQb, Q4);
  and NR4 (TQm, TQk, Q3);
  and AT5 (TQc, TQ9, TQb);
  and TM4 (TQl, TQm, TQr);
  T_Flip_Flop U2 (.T(TQg), .clk(CLK), .Q(Q1), .reset(RST));  // open: Qn, preset
  and AT6 (TQd, TQc, Q5);
  and NR5 (TQp, TQm, Q4);
  T_Flip_Flop U3 (.T(TQh), .clk(CLK), .Q(Q2), .reset(RST));  // open: Qn, preset
  and AT7 (TC, TQd, Q6);
  and TM5 (TQn, TQp, TQr);
  not NA (TQr, TC);
  T_Flip_Flop U4 (.T(TQj), .clk(CLK), .Q(Q3), .reset(RST));  // open: Qn, preset
  or TO5 (TQo, TQn, TC);
  or T0 (TQe, TQr, TC);
  and NR6 (TQq, TQp, Q5);
  T_Flip_Flop U5 (.T(TQl), .clk(CLK), .Q(Q4), .reset(RST));  // open: Qn, preset
  and TM1 (TQf, Q0, TQr);
  and TM6 (TQs, TQq, TQr);
  T_Flip_Flop U6 (.T(TQo), .clk(CLK), .Q(Q5), .reset(RST));  // open: Qn, preset
  or TO1 (TQg, TQf, TC);
  or TO6 (TQu, TQs, TC);
  and NR2 (TQi, Q0, Q1);
  T_Flip_Flop U7 (.T(TQu), .clk(CLK), .Q(Q6), .reset(RST));  // open: Qn, preset
  and TM2 (TQh, TQi, TQr);
  and AT2 (TQ1, Q0, Q1);
  and NR3 (TQk, TQi, Q2);
  not N3 (TQ3, Q2);
  and TM3 (TQj, TQk, TQr);
  and AT3 (TQ4, TQ1, TQ3);
  not N4 (TQ6, Q3);
  and AT4 (TQ9, TQ4, TQ6);

  // Other names for the same wires on the sheet: TQ0 = Q3; TQ2 = Q4; TQ5 = Q5; TQ7 = CLK; TQ8 = RST; TQa = Q6;
  //   TQt = TC; TQv = Q0; TQw = Q1; TQx = Q2
endmodule
