// Logisim project mod10_counter.circ as structural Verilog
module mod10_counter (
  input  RST,
  output Q0,
  output Q1,
  output Q2,
  output Q3,
  output TC
);

  wire AT2_out, AT3_out, CLK_out, N2_out, N3_out, NA_out, NR2_out, NR3_out, T0_out, TM1_out, TM2_out,
       TM3_out, TO3_out;

  Clock CLK (.out(CLK_out));
  T_Flip_Flop U1 (.T(T0_out), .clk(CLK_out), .Q(Q0), .reset(RST), .preset(RST));  // open: Qn
  T_Flip_Flop U2 (.T(TM1_out), .clk(CLK_out), .Q(Q1), .reset(RST), .preset(RST));  // open: Qn
  T_Flip_Flop U3 (.T(TM2_out), .clk(CLK_out), .Q(Q2), .reset(RST), .preset(RST));  // open: Qn
  T_Flip_Flop U4 (.T(TO3_out), .clk(CLK_out), .Q(Q3), .reset(RST), .preset(RST));  // open: Qn
  not N2 (N2_out, Q1);
  and AT2 (AT2_out, Q0, N2_out);
  not N3 (N3_out, Q2);
  and AT3 (AT3_out, AT2_out, N3_out);
  and AT4 (TC, AT3_out, Q3);
  not NA (NA_out, TC);
  or T0 (T0_out, NA_out, TC);
  and TM1 (TM1_out, Q0, NA_out);
  and NR2 (NR2_out, Q0, Q1);
  and TM2 (TM2_out, NR2_out, NA_out);
  and NR3 (NR3_out, NR2_out, Q2);
  and TM3 (TM3_out, NR3_out, NA_out);
  or TO3 (TO3_out, TM3_out, TC);
endmodule
