// Logisim project mod128_counter.circ as structural Verilog
module mod128_counter (
  input  CLK,
  input  RST,
  output Q0,
  output Q1,
  output Q2,
  output Q3,
  output Q4,
  output Q5,
  output Q6,
  output TC
);

  wire TQ1, TQ3, TQ4, TQ6, TQ7, TQc, TQd, TQe, TQf, TQg, TQh, TQi, TQj, TQk, TQl, TQm, TQn, TQo, TQp, TQq,
       TQr, TQs, TQt, TQv;

  T_Flip_Flop U1 (.T(TQc), .clk(CLK), .Q(Q0), .reset(RST));  // open: Qn, preset
  and AT7 (TC, TQ7, Q6);
  and TM4 (TQl, TQn, TQs);
  not NA (TQs, TC);
  or TO4 (TQm, TQl, TC);
  T_Flip_Flop U2 (.T(TQe), .clk(CLK), .Q(Q1), .reset(RST));  // open: Qn, preset
  or T0 (TQc, TQs, TC);
  and NR5 (TQq, TQn, Q4);
  T_Flip_Flop U3 (.T(TQg), .clk(CLK), .Q(Q2), .reset(RST));  // open: Qn, preset
  and TM1 (TQd, Q0, TQs);
  and TM5 (TQo, TQq, TQs);
  or TO1 (TQe, TQd, TC);
  T_Flip_Flop U4 (.T(TQj), .clk(CLK), .Q(Q3), .reset(RST));  // open: Qn, preset
  or TO5 (TQp, TQo, TC);
  and NR2 (TQh, Q0, Q1);
  and NR6 (TQr, TQq, Q5);
  T_Flip_Flop U5 (.T(TQm), .clk(CLK), .Q(Q4), .reset(RST));  // open: Qn, preset
  and TM2 (TQf, TQh, TQs);
  and TM6 (TQt, TQr, TQs);
  T_Flip_Flop U6 (.T(TQp), .clk(CLK), .Q(Q5), .reset(RST));  // open: Qn, preset
  or TO2 (TQg, TQf, TC);
  or TO6 (TQv, TQt, TC);
  and NR3 (TQk, TQh, Q2);
  T_Flip_Flop U7 (.T(TQv), .clk(CLK), .Q(Q6), .reset(RST));  // open: Qn, preset
  and TM3 (TQi, TQk, TQs);
  and AT2 (TQ1, Q0, Q1);
  or TO3 (TQj, TQi, TC);
  and AT3 (TQ3, TQ1, Q2);
  and NR4 (TQn, TQk, Q3);
  and AT4 (TQ4, TQ3, Q3);
  and AT5 (TQ6, TQ4, Q4);
  and AT6 (TQ7, TQ6, Q5);

  // Other names for the same wires on the sheet: TQ0 = Q2; TQ2 = Q3; TQ5 = Q4; TQ8 = Q5; TQ9 = CLK; TQa = RST;
  //   TQb = Q6; TQu = TC; TQw = Q0; TQx = Q1
endmodule
