// Logisim project mod5_counter.circ as structural Verilog
module mod5_counter (
  input  CLK,
  input  RST,
  output Q0,
  output Q1,
  output Q2,
  output Q3
);

  wire TQ1, TQ3, TQ5, TQ7, TQ8, TQ9, TQa, TQb, TQc, TQd, TQe, TQf, TQg;

  T_Flip_Flop U1 (.T(TQf), .clk(CLK), .Q(Q0), .reset(RST));  // open: Qn, preset
  and NR2 (TQd, Q0, Q1);
  and TM2 (TQa, TQd, TQf);
  T_Flip_Flop U2 (.T(TQ9), .clk(CLK), .Q(Q1), .reset(RST));  // open: Qn, preset
  or TO2 (TQc, TQa, TQb);
  T_Flip_Flop U3 (.T(TQc), .clk(CLK), .Q(Q2), .reset(RST));  // open: Qn, preset
  and NR3 (TQe, TQd, Q2);
  T_Flip_Flop U4 (.T(TQg), .clk(CLK), .Q(Q3), .reset(RST));  // open: Qn, preset
  and TM3 (TQg, TQe, TQf);
  not N1 (TQ1, Q0);
  not N2 (TQ3, Q1);
  and AT2 (TQ5, TQ1, TQ3);
  and AT3 (TQ7, TQ5, Q2);
  not N4 (TQ8, Q3);
  and AT4 (TQb, TQ7, TQ8);
  not NA (TQf, TQb);
  and TM1 (TQ9, Q0, TQf);

  // Other names for the same wires on the sheet: TQ0 = Q2; TQ2 = CLK; TQ4 = RST; TQ6 = Q3; TQh = Q0; TQi = Q1
endmodule
