// Logisim project mod60_counter.circ as structural Verilog
module mod60_counter (
  input  RST,
  output Q0,
  output Q1,
  output Q2,
  output Q3,
  output Q4,
  output Q5,
  output TC
);

  wire AT2_out, AT3_out, AT4_out, AT5_out, CLK_out, N3_out, NA_out, NR2_out, NR3_out, NR4_out, NR5_out,
       T0_out, TM1_out, TM2_out, TM3_out, TM4_out, TM5_out, TO1_out, TO3_out, TO4_out, TO5_out;

  Clock CLK (.out(CLK_out));
  T_Flip_Flop U1 (.T(T0_out), .clk(CLK_out), .Q(Q0), .reset(RST), .preset(RST));  // open: Qn
  T_Flip_Flop U2 (.T(TO1_out), .clk(CLK_out), .Q(Q1), .reset(RST), .preset(RST));  // open: Qn
  T_Flip_Flop U3 (.T(TM2_out), .clk(CLK_out), .Q(Q2), .reset(RST), .preset(RST));  // open: Qn
  T_Flip_Flop U4 (.T(TO3_out), .clk(CLK_out), .Q(Q3), .reset(RST), .preset(RST));  // open: Qn
  T_Flip_Flop U5 (.T(TO4_out), .clk(CLK_out), .Q(Q4), .reset(RST), .preset(RST));  // open: Qn
  T_Flip_Flop U6 (.T(TO5_out), .clk(CLK_out), .Q(Q5), .reset(RST), .preset(RST));  // open: Qn
  and AT2 (AT2_out, Q0, Q1);
  not N3 (N3_out, Q2);
  and AT3 (AT3_out, AT2_out, N3_out);
  and AT4 (AT4_out, AT3_out, Q3);
  and AT5 (AT5_out, AT4_out, Q4);
  and AT6 (TC, AT5_out, Q5);
  not NA (NA_out, TC);
  or T0 (T0_out, NA_out, TC);
  and TM1 (TM1_out, Q0, NA_out);
  or TO1 (TO1_out, TM1_out, TC);
  and NR2 (NR2_out, Q0, Q1);
  and TM2 (TM2_out, NR2_out, NA_out);
  and NR3 (NR3_out, NR2_out, Q2);
  and TM3 (TM3_out, NR3_out, NA_out);
  or TO3 (TO3_out, TM3_out, TC);
  and NR4 (NR4_out, NR3_out, Q3);
  and TM4 (TM4_out, NR4_out, NA_out);
  or TO4 (TO4_out, TM4_out, TC);
  and NR5 (NR5_out, NR4_out, Q4);
  and TM5 (TM5_out, NR5_out, NA_out);
  or TO5 (TO5_out, TM5_out, TC);
endmodule
