// Logisim project multiplier_4x4.circ as structural Verilog
module multiplier_4x4 (
  input  A0,
  input  A1,
  input  A2,
  input  A3,
  input  B0,
  input  B1,
  input  B2,
  input  B3,
  input  GND,
  output P0,
  output P1,
  output P2,
  output P3,
  output P4,
  output P5,
  output P6,
  output P7
);

  wire TQ1a, TQ1b, TQ1c, TQ1d, TQ1e, TQ1f, TQ1g, TQ1h, TQ1i, TQ1j, TQ1k, TQ1l, TQ1m, TQ1n, TQ1o, TQ1p, TQ1q,
       TQ1r, TQ1s, TQ1t, TQ1u, TQ1v, TQ1w, TQ1x, TQ1y, TQ1z, TQ2a, TQ2b, TQ2c, TQ2d, TQ2e, TQ2f, TQ2g, TQ2h,
       TQ2i, TQ2j, TQ2k, TQ2l, TQ2m, TQ2n, TQ2o, TQ2p, TQ2q, TQ2r, TQ2s, TQ2t, TQ2u, TQ2v, TQ2w, TQ2x, TQ2y,
       TQ2z, TQ3a, TQ8, TQ9, TQ10, TQ11, TQ12, TQ13, TQ14, TQ15, TQ16, TQ17, TQ18, TQ19, TQ20, TQ21, TQ22,
       TQ23, TQ24, TQ25, TQ26, TQ27, TQ28, TQ29, TQ30, TQ31, TQ32, TQ33, TQ34, TQ35, TQ36, TQ37, TQ38, TQ39,
       TQa, TQb, TQc, TQd, TQe, TQf, TQg, TQh, TQi, TQj, TQk, TQl, TQm, TQn, TQo, TQp, TQq, TQr, TQs, TQt,
       TQu, TQv, TQw, TQx, TQy, TQz;

  and MULP1 (P0, A0, B0);
  and MULP13 (TQ25, A0, B3);
  and MULA18 (TQi, TQe, TQf);
  and MULA20 (TQv, GND, TQs);
  and MULA22 (TQ16, TQ13, TQ14);
  and MULA24 (TQ1k, TQ1g, TQ1h);
  and MULA26 (TQ1w, GND, GND);
  and MULA28 (TQ27, TQ24, TQ25);
  and MULA30 (TQ2l, TQ2h, TQ2i);
  and MULA32 (TQ2y, TQ2v, GND);
  and MULA34 (TQ38, GND, GND);
  and MULP2 (TQ8, A1, B0);
  and MULP14 (TQ2b, A1, B3);
  and MULB18 (TQj, TQg, TQh);
  and MULB20 (TQw, TQt, TQu);
  and MULB22 (TQ17, GND, TQ15);
  and MULB24 (TQ1l, TQ1i, TQ1j);
  and MULB26 (TQ1x, TQ1u, TQ1v);
  and MULB28 (TQ28, GND, TQ26);
  and MULB30 (TQ2m, TQ2j, TQ2k);
  and MULB32 (TQ2z, TQ2w, TQ2x);
  and MULB34 (TQ39, TQ36, TQ37);
  and MULP3 (TQe, A2, B0);
  and MULP15 (TQ2i, A2, B3);
  or MULO18 (TQk, TQi, TQj);
  or MULO20 (TQx, TQv, TQw);
  or MULO22 (TQ18, TQ16, TQ17);
  or MULO24 (TQ1m, TQ1k, TQ1l);
  or MULO26 (TQ1y, TQ1w, TQ1x);
  or MULO28 (TQ29, TQ27, TQ28);
  or MULO30 (TQ2n, TQ2l, TQ2m);
  or MULO32 (TQ30, TQ2y, TQ2z);
  or MULO34 (TQ3a, TQ38, TQ39);
  and MULP4 (TQl, A3, B0);
  and MULP16 (TQ2p, A3, B3);
  or MULG18 (TQn, TQk, GND);
  or MULG20 (TQy, TQx, GND);
  or MULG22 (TQ1b, TQ18, GND);
  or MULG24 (TQ1p, TQ1m, GND);
  or MULG26 (TQ1z, TQ1y, GND);
  or MULG28 (TQ2c, TQ29, GND);
  or MULG30 (TQ2q, TQ2n, GND);
  or MULG32 (TQ31, TQ30, GND);
  // OR_Gate MULG34 has open pins: in0=TQ3a, in1=GND, out=open
  and MULP5 (TQ9, A0, B1);
  xor MULX17 (TQa, TQ8, TQ9);
  xor MULX19 (TQo, TQl, TQm);
  xor MULX21 (TQz, GND, GND);
  xor MULX23 (TQ1c, TQ19, TQ1a);
  xor MULX25 (TQ1q, TQ1n, TQ1o);
  xor MULX27 (TQ20, GND, GND);
  xor MULX29 (TQ2d, TQ2a, TQ2b);
  xor MULX31 (TQ2r, TQ2o, TQ2p);
  xor MULX33 (TQ32, GND, GND);
  and MULP6 (TQf, A1, B1);
  xor MULS17 (P1, TQa, GND);
  xor MULS19 (TQ19, TQo, TQn);
  xor MULS21 (TQ1n, TQz, TQy);
  xor MULS23 (TQ24, TQ1c, TQ1b);
  xor MULS25 (TQ2h, TQ1q, TQ1p);
  xor MULS27 (TQ2v, TQ20, TQ1z);
  xor MULS29 (P4, TQ2d, TQ2c);
  xor MULS31 (P6, TQ2r, TQ2q);
  // XOR_Gate MULS33 has open pins: in0=TQ32, in1=TQ31, out=open
  and MULP7 (TQm, A2, B1);
  and MULA17 (TQb, TQ8, TQ9);
  and MULA19 (TQp, TQl, TQm);
  and MULA21 (TQ10, GND, GND);
  and MULA23 (TQ1d, TQ19, TQ1a);
  and MULA25 (TQ1r, TQ1n, TQ1o);
  and MULA27 (TQ21, GND, GND);
  and MULA29 (TQ2e, TQ2a, TQ2b);
  and MULA31 (TQ2s, TQ2o, TQ2p);
  and MULA33 (TQ33, GND, GND);
  and MULP8 (TQs, A3, B1);
  and MULB17 (TQc, GND, TQa);
  and MULB19 (TQq, TQn, TQo);
  and MULB21 (TQ11, TQy, TQz);
  and MULB23 (TQ1e, TQ1b, TQ1c);
  and MULB25 (TQ1s, TQ1p, TQ1q);
  and MULB27 (TQ22, TQ1z, TQ20);
  and MULB29 (TQ2f, TQ2c, TQ2d);
  and MULB31 (TQ2t, TQ2q, TQ2r);
  and MULB33 (TQ34, TQ31, TQ32);
  and MULP9 (TQ14, A0, B2);
  or MULO17 (TQd, TQb, TQc);
  or MULO19 (TQr, TQp, TQq);
  or MULO21 (TQ12, TQ10, TQ11);
  or MULO23 (TQ1f, TQ1d, TQ1e);
  or MULO25 (TQ1t, TQ1r, TQ1s);
  or MULO27 (TQ23, TQ21, TQ22);
  or MULO29 (TQ2g, TQ2e, TQ2f);
  or MULO31 (TQ2u, TQ2s, TQ2t);
  or MULO33 (TQ35, TQ33, TQ34);
  and MULP10 (TQ1a, A1, B2);
  or MULG17 (TQg, TQd, GND);
  or MULG19 (TQt, TQr, GND);
  // OR_Gate MULG21 has open pins: in0=TQ12, in1=GND, out=open
  or MULG23 (TQ1i, TQ1f, GND);
  or MULG25 (TQ1u, TQ1t, GND);
  // OR_Gate MULG27 has open pins: in0=TQ23, in1=GND, out=open
  or MULG29 (TQ2j, TQ2g, GND);
  or MULG31 (TQ2w, TQ2u, GND);
  or MULG33 (TQ36, TQ35, GND);
  and MULP11 (TQ1h, A2, B2);
  xor MULX18 (TQh, TQe, TQf);
  xor MULX20 (TQu, GND, TQs);
  xor MULX22 (TQ15, TQ13, TQ14);
  xor MULX24 (TQ1j, TQ1g, TQ1h);
  xor MULX26 (TQ1v, GND, GND);
  xor MULX28 (TQ26, TQ24, TQ25);
  xor MULX30 (TQ2k, TQ2h, TQ2i);
  xor MULX32 (TQ2x, TQ2v, GND);
  xor MULX34 (TQ37, GND, GND);
  and MULP12 (TQ1o, A3, B2);
  xor MULS18 (TQ13, TQh, TQg);
  xor MULS20 (TQ1g, TQu, TQt);
  xor MULS22 (P2, TQ15, GND);
  xor MULS24 (TQ2a, TQ1j, TQ1i);
  xor MULS26 (TQ2o, TQ1v, TQ1u);
  xor MULS28 (P3, TQ26, GND);
  xor MULS30 (P5, TQ2k, TQ2j);
  xor MULS32 (P7, TQ2x, TQ2w);
  // XOR_Gate MULS34 has open pins: in0=TQ37, in1=TQ36, out=open

  // Other names for the same wires on the sheet: TQ0 = B0; TQ1 = B1; TQ2 = B2; TQ3 = A0; TQ3b = GND; TQ3c = P0;
  //   TQ3d = P1; TQ3e = P2; TQ3f = P3; TQ3g = P4; TQ3h = P5; TQ3i = P6; TQ3j = P7; TQ4 = A1; TQ5 = A2; TQ6 = A3;
  //   TQ7 = B3
endmodule
