// Logisim project mux_4to1.circ as structural Verilog
module mux_4to1 (
  input  D0,
  input  D1,
  input  D2,
  input  D3,
  input  S0,
  input  S1,
  output Y
);

  wire TQ0, TQ1, TQ2, TQ3, TQ4, TQ5, TQ9, TQb, TQd, TQf, TQg, TQh;

  and MUX0D (TQ9, D0, TQ0);
  not MUXN2 (TQ1, S1);
  and MUX0S1 (TQ0, TQ3, TQ1);
  and MUX1D (TQb, D1, TQ2);
  and MUX1S1 (TQ2, S0, TQ1);
  and MUX2D (TQd, D2, TQ4);
  and MUX2S1 (TQ4, TQ3, S1);
  and MUX3D (TQf, D3, TQ5);
  and MUX3S1 (TQ5, S0, S1);
  or MUXO1 (TQg, TQ9, TQb);
  or MUXO2 (TQh, TQg, TQd);
  or MUXO3 (Y, TQh, TQf);
  not MUXN1 (TQ3, S0);

  // Other names for the same wires on the sheet: TQ6 = S0; TQ7 = S1; TQ8 = D0; TQa = D1; TQc = D2; TQe = D3; TQi = Y
endmodule
