// Logisim project mux_8to1.circ as structural Verilog
module mux_8to1 (
  input  D0,
  input  D1,
  input  D2,
  input  D3,
  input  D4,
  input  D5,
  input  D6,
  input  D7,
  input  S0,
  input  S1,
  input  S2,
  output Y
);

  wire MUX6S1_out, MUX7D_out, MUX7S1_out, MUX7S2_out, MUXO1_out, MUXO2_out, MUXO3_out, MUXO4_out, MUXO5_out,
       MUXO6_out, TQ1, TQ2, TQ3, TQ4, TQ5, TQ6, TQ7, TQ8, TQ9, TQa, TQb, TQc, TQd, TQe, TQf, TQg, TQl, TQn,
       TQp, TQr, TQt, TQv, TQx;

  and MUX0D (TQl, D0, TQ2);
  and MUX0S1 (TQ1, TQf, TQc);
  and MUX0S2 (TQ2, TQ1, TQ8);
  and MUX1D (TQn, D1, TQ4);
  and MUX1S1 (TQ3, S0, TQc);
  and MUX1S2 (TQ4, TQ3, TQ8);
  and MUX2D (TQp, D2, TQ6);
  and MUX2S1 (TQ5, TQf, S1);
  and MUX2S2 (TQ6, TQ5, TQ8);
  and MUX3D (TQr, D3, TQ9);
  and MUX3S1 (TQ7, S0, S1);
  and MUX3S2 (TQ9, TQ7, TQ8);
  and MUX4D (TQt, D4, TQb);
  and MUX4S1 (TQa, TQf, TQc);
  and MUX4S2 (TQb, TQa, S2);
  and MUX5D (TQv, D5, TQe);
  and MUX5S1 (TQd, S0, TQc);
  and MUX5S2 (TQe, TQd, S2);
  and MUX6D (TQx, D6, TQg);
  and MUX6S1 (MUX6S1_out, TQf, S1);
  and MUX6S2 (TQg, MUX6S1_out, S2);
  and MUX7D (MUX7D_out, D7, MUX7S2_out);
  and MUX7S1 (MUX7S1_out, S0, S1);
  and MUX7S2 (MUX7S2_out, MUX7S1_out, S2);
  or MUXO1 (MUXO1_out, TQl, TQn);
  or MUXO2 (MUXO2_out, MUXO1_out, TQp);
  or MUXO3 (MUXO3_out, MUXO2_out, TQr);
  or MUXO4 (MUXO4_out, MUXO3_out, TQt);
  or MUXO5 (MUXO5_out, MUXO4_out, TQv);
  or MUXO6 (MUXO6_out, MUXO5_out, TQx);
  or MUXO7 (Y, MUXO6_out, MUX7D_out);
  not MUXN1 (TQf, S0);
  not MUXN2 (TQc, S1);
  not MUXN3 (TQ8, S2);

  // Other names for the same wires on the sheet: TQ0 = Y; TQh = S0; TQi = S1; TQj = S2; TQk = D0; TQm = D1; TQo = D2;
  //   TQq = D3; TQs = D4; TQu = D5; TQw = D6; TQy = D7
endmodule
