// Logisim project nine_complement.circ as structural Verilog
module nine_complement (
  input  D1,
  input  D2,
  input  D4,
  input  D8,
  output C1,
  output C2,
  output C4,
  output C8
);

  wire O1_out, X3_out;

  not N1 (C1, D1);
  xor X2 (C4, D4, D2);
  or O1 (O1_out, D4, D2);
  xor X3 (X3_out, D8, O1_out);
  not N2 (C8, X3_out);

  assign C2 = D2;
endmodule
