// Logisim project parity_4bit.circ as structural Verilog
module parity_4bit (
  input  D0,
  input  D1,
  input  D2,
  input  D3,
  output P
);

  wire PAR1_out, PAR2_out;

  xor PAR1 (PAR1_out, D0, D1);
  xor PAR2 (PAR2_out, PAR1_out, D2);
  xor PAR3 (P, PAR2_out, D3);
endmodule
