// Logisim project piso_4bit.circ as structural Verilog
module piso_4bit (
  input  CLK,
  input  LOAD,
  input  RST,
  input  SI,
  input  D0,
  input  D1,
  input  D2,
  input  D3,
  output SO,
  output Q0,
  output Q1,
  output Q2,
  output Q3
);

  wire TQ1, TQ2, TQ3, TQ5, TQ6, TQ7, TQa, TQb, TQc, TQg, TQi, TQj, TQk;

  not PISOL (TQg, LOAD);
  D_Flip_Flop PISO3 (.D(TQc), .clk(CLK), .Q(Q2), .reset(RST));  // open: Qn, preset
  and PISOA0 (TQ1, LOAD, D0);
  and PISOB0 (TQ2, TQg, Q1);
  and PISOA3 (TQi, LOAD, D3);
  and PISOB3 (TQj, TQg, SI);
  or PISOM0 (TQ3, TQ1, TQ2);
  D_Flip_Flop PISO1 (.D(TQ3), .clk(CLK), .Q(Q0), .reset(RST));  // open: Qn, preset
  or PISOM3 (TQk, TQi, TQj);
  D_Flip_Flop PISO4 (.D(TQk), .clk(CLK), .Q(Q3), .reset(RST));  // open: Qn, preset
  and PISOA1 (TQ5, LOAD, D1);
  and PISOB1 (TQ6, TQg, Q2);
  or PISOM1 (TQ7, TQ5, TQ6);
  D_Flip_Flop PISO2 (.D(TQ7), .clk(CLK), .Q(Q1), .reset(RST));  // open: Qn, preset
  and PISOA2 (TQa, LOAD, D2);
  and PISOB2 (TQb, TQg, Q3);
  or PISOM2 (TQc, TQa, TQb);

  assign SO = Q0;

  // Other names for the same wires on the sheet: TQ0 = D0; TQ4 = D1; TQ8 = Q1; TQ9 = D2; TQd = Q2; TQe = LOAD;
  //   TQf = D3; TQh = SI; TQl = CLK; TQm = RST; TQn = Q3; TQo = Q0
endmodule
