// Logisim project register_4bit.circ as structural Verilog
module register_4bit (
  input  RST,
  input  D0,
  input  D1,
  input  D2,
  input  D3,
  output Q0,
  output Q1,
  output Q2,
  output Q3
);

  wire CLK_out;

  Clock CLK (.out(CLK_out));
  D_Flip_Flop U1 (.D(D0), .clk(CLK_out), .Q(Q0), .preset(RST), .reset(RST));  // open: Qn
  D_Flip_Flop U2 (.D(D1), .clk(CLK_out), .Q(Q1), .preset(RST), .reset(RST));  // open: Qn
  D_Flip_Flop U3 (.D(D2), .clk(CLK_out), .Q(Q2), .preset(RST), .reset(RST));  // open: Qn
  D_Flip_Flop U4 (.D(D3), .clk(CLK_out), .Q(Q3), .preset(RST), .reset(RST));  // open: Qn
endmodule
