// Logisim project sar_4bit.circ as structural Verilog
module sar_4bit (
  input  D0,
  input  D1,
  input  D2,
  input  D3,
  input  SH0,
  input  SH1,
  output Y0,
  output Y1,
  output Y2,
  output Y3
);

  wire TQ1, TQ1a, TQ1b, TQ1c, TQ1d, TQ1e, TQ2, TQ3, TQ4, TQ5, TQ6, TQ7, TQ8, TQ9, TQ10, TQ11, TQ12, TQ13,
       TQ14, TQ17, TQ19, TQa, TQd, TQe, TQf, TQg, TQh, TQi, TQj, TQk, TQl, TQm, TQp, TQq, TQr, TQs, TQt, TQu,
       TQv, TQw, TQx, TQy;

  not NS1 (TQ13, SH0);
  or MO11 (Y0, TQ9, TQa);
  and SA23 (TQp, D2, TQ13);
  and SB35 (TQ19, TQ10, TQ12);
  not NS2 (TQ12, SH1);
  and SA12 (TQd, D1, TQ13);
  and SB24 (TQt, TQp, TQ12);
  and SA36 (TQ11, D3, SH0);
  and SA1 (TQ1, D0, TQ13);
  and SB13 (TQh, TQd, TQ12);
  and SA25 (TQq, D3, SH0);
  and SB37 (TQ1a, TQ11, TQ12);
  and SB2 (TQ5, TQ1, TQ12);
  and SA14 (TQe, D2, SH0);
  and SB26 (TQu, TQq, TQ12);
  and SA38 (TQ14, D3, TQ13);
  and SA3 (TQ2, D1, SH0);
  and SB15 (TQi, TQe, TQ12);
  and SA27 (TQr, D3, TQ13);
  and SB39 (TQ1c, TQ14, SH1);
  and SB4 (TQ6, TQ2, TQ12);
  and SA16 (TQf, D3, TQ13);
  and SB28 (TQw, TQr, SH1);
  and SA40 (TQ17, D3, SH0);
  and SA5 (TQ3, D2, TQ13);
  and SB17 (TQk, TQf, SH1);
  and SA29 (TQs, D3, SH0);
  and SB41 (TQ1e, TQ17, SH1);
  and SB6 (TQ8, TQ3, SH1);
  and SA18 (TQg, D3, SH0);
  and SB30 (TQy, TQs, SH1);
  or MO42 (TQ1b, TQ19, TQ1a);
  and SA7 (TQ4, D3, SH0);
  and SB19 (TQm, TQg, SH1);
  or MO31 (TQv, TQt, TQu);
  or MO43 (TQ1d, TQ1b, TQ1c);
  and SB8 (TQa, TQ4, SH1);
  or MO20 (TQj, TQh, TQi);
  or MO32 (TQx, TQv, TQw);
  or MO44 (Y3, TQ1d, TQ1e);
  or MO9 (TQ7, TQ5, TQ6);
  or MO21 (TQl, TQj, TQk);
  or MO33 (Y2, TQx, TQy);
  or MO10 (TQ9, TQ7, TQ8);
  or MO22 (Y1, TQl, TQm);
  and SA34 (TQ10, D3, TQ13);

  // Other names for the same wires on the sheet: TQ0 = D0; TQ1f = Y3; TQ15 = D3; TQ16 = SH0; TQ18 = SH1; TQb = Y0;
  //   TQc = D1; TQn = Y1; TQo = D2; TQz = Y2
endmodule
