// Logisim project satadd_4bit.circ as structural Verilog
module satadd_4bit (
  input  A0,
  input  B0,
  input  A1,
  input  B1,
  input  A2,
  input  B2,
  input  A3,
  input  B3,
  input  GND,
  output S0,
  output S1,
  output S2,
  output S3
);

  wire SAA1_out, SAA2_out, SAA3_out, SAA4_out, SAB1_out, SAB2_out, SAB3_out, SAB4_out, SAG1_out, SAG2_out,
       SAG3_out, SAG4_out, SAO1_out, SAO2_out, SAO3_out, SAO4_out, SAS1_out, SAS2_out, SAS3_out, SAS4_out,
       SAX1_out, SAX2_out, SAX3_out, SAX4_out;

  xor SAX1 (SAX1_out, A0, B0);
  xor SAS1 (SAS1_out, SAX1_out, GND);
  and SAA1 (SAA1_out, A0, B0);
  and SAB1 (SAB1_out, GND, SAX1_out);
  or SAO1 (SAO1_out, SAA1_out, SAB1_out);
  or SAG1 (SAG1_out, SAO1_out, GND);
  xor SAX2 (SAX2_out, A1, B1);
  xor SAS2 (SAS2_out, SAX2_out, SAG1_out);
  and SAA2 (SAA2_out, A1, B1);
  and SAB2 (SAB2_out, SAG1_out, SAX2_out);
  or SAO2 (SAO2_out, SAA2_out, SAB2_out);
  or SAG2 (SAG2_out, SAO2_out, GND);
  xor SAX3 (SAX3_out, A2, B2);
  xor SAS3 (SAS3_out, SAX3_out, SAG2_out);
  and SAA3 (SAA3_out, A2, B2);
  and SAB3 (SAB3_out, SAG2_out, SAX3_out);
  or SAO3 (SAO3_out, SAA3_out, SAB3_out);
  or SAG3 (SAG3_out, SAO3_out, GND);
  xor SAX4 (SAX4_out, A3, B3);
  xor SAS4 (SAS4_out, SAX4_out, SAG3_out);
  and SAA4 (SAA4_out, A3, B3);
  and SAB4 (SAB4_out, SAG3_out, SAX4_out);
  or SAO4 (SAO4_out, SAA4_out, SAB4_out);
  or SAG4 (SAG4_out, SAO4_out, GND);
  or SAU5 (S0, SAS1_out, SAG4_out);
  or SAU6 (S1, SAS2_out, SAG4_out);
  or SAU7 (S2, SAS3_out, SAG4_out);
  or SAU8 (S3, SAS4_out, SAG4_out);
endmodule
