// Logisim project seqdet_101.circ as structural Verilog
module seqdet_101 (
  input  X,
  input  RST,
  output F
);

  wire A1_out, A2_out, A3_out, CLK_out, N1_out, N2_out, O1_out, U1_q, U2_q;

  Clock CLK (.out(CLK_out));
  D_Flip_Flop U1 (.D(X), .clk(CLK_out), .Q(U1_q), .preset(RST), .reset(RST));  // open: Qn
  D_Flip_Flop U2 (.D(O1_out), .clk(CLK_out), .Q(U2_q), .preset(RST), .reset(RST));  // open: Qn
  not N1 (N1_out, X);
  not N2 (N2_out, U1_q);
  and A1 (A1_out, U1_q, N1_out);
  and A2 (A2_out, N2_out, X);
  and A3 (A3_out, U2_q, A2_out);
  or O1 (O1_out, A1_out, A3_out);
  and A4 (F, U2_q, U1_q);
endmodule
