// Logisim project squarer_4bit.circ as structural Verilog
module squarer_4bit (
  input  A0,
  input  A1,
  input  A2,
  input  A3,
  input  GND,
  output P0,
  output P1,
  output P2,
  output P3,
  output P4,
  output P5,
  output P6,
  output P7
);

  wire TQ1a, TQ1b, TQ1c, TQ1d, TQ1e, TQ1f, TQ1g, TQ1h, TQ1i, TQ1j, TQ1k, TQ1l, TQ1m, TQ1n, TQ1o, TQ1p, TQ1q,
       TQ1r, TQ1s, TQ1t, TQ1u, TQ1v, TQ1w, TQ1x, TQ1y, TQ1z, TQ2a, TQ2b, TQ2c, TQ2d, TQ2e, TQ2f, TQ2g, TQ2h,
       TQ2i, TQ2j, TQ2k, TQ2l, TQ2m, TQ2n, TQ2o, TQ2p, TQ2q, TQ2r, TQ2s, TQ2t, TQ2u, TQ2v, TQ2w, TQ2x, TQ2y,
       TQ2z, TQ4, TQ5, TQ6, TQ7, TQ8, TQ9, TQ10, TQ11, TQ12, TQ13, TQ14, TQ15, TQ16, TQ17, TQ18, TQ19, TQ20,
       TQ21, TQ22, TQ23, TQ24, TQ25, TQ26, TQ27, TQ28, TQ29, TQ30, TQ31, TQ32, TQ33, TQ34, TQ35, TQ36, TQa,
       TQb, TQc, TQd, TQe, TQf, TQg, TQh, TQi, TQj, TQk, TQl, TQm, TQn, TQo, TQp, TQq, TQr, TQs, TQt, TQu,
       TQv, TQw, TQx, TQy, TQz;

  and SQP1 (P0, A0, A0);
  and SQP13 (TQ21, A0, A3);
  and SQA18 (TQe, TQa, TQb);
  and SQA20 (TQr, GND, TQo);
  and SQA22 (TQ12, TQz, TQ10);
  and SQA24 (TQ1g, TQ1c, TQ1d);
  and SQA26 (TQ1s, GND, GND);
  and SQA28 (TQ23, TQ20, TQ21);
  and SQA30 (TQ2h, TQ2d, TQ2e);
  and SQA32 (TQ2u, TQ2r, GND);
  and SQA34 (TQ34, GND, GND);
  and SQP2 (TQ4, A1, A0);
  and SQP14 (TQ27, A1, A3);
  and SQB18 (TQf, TQc, TQd);
  and SQB20 (TQs, TQp, TQq);
  and SQB22 (TQ13, GND, TQ11);
  and SQB24 (TQ1h, TQ1e, TQ1f);
  and SQB26 (TQ1t, TQ1q, TQ1r);
  and SQB28 (TQ24, GND, TQ22);
  and SQB30 (TQ2i, TQ2f, TQ2g);
  and SQB32 (TQ2v, TQ2s, TQ2t);
  and SQB34 (TQ35, TQ32, TQ33);
  and SQP3 (TQa, A2, A0);
  and SQP15 (TQ2e, A2, A3);
  or SQO18 (TQg, TQe, TQf);
  or SQO20 (TQt, TQr, TQs);
  or SQO22 (TQ14, TQ12, TQ13);
  or SQO24 (TQ1i, TQ1g, TQ1h);
  or SQO26 (TQ1u, TQ1s, TQ1t);
  or SQO28 (TQ25, TQ23, TQ24);
  or SQO30 (TQ2j, TQ2h, TQ2i);
  or SQO32 (TQ2w, TQ2u, TQ2v);
  or SQO34 (TQ36, TQ34, TQ35);
  and SQP4 (TQh, A3, A0);
  and SQP16 (TQ2l, A3, A3);
  or SQG18 (TQj, TQg, GND);
  or SQG20 (TQu, TQt, GND);
  or SQG22 (TQ17, TQ14, GND);
  or SQG24 (TQ1l, TQ1i, GND);
  or SQG26 (TQ1v, TQ1u, GND);
  or SQG28 (TQ28, TQ25, GND);
  or SQG30 (TQ2m, TQ2j, GND);
  or SQG32 (TQ2x, TQ2w, GND);
  // OR_Gate SQG34 has open pins: in0=TQ36, in1=GND, out=open
  and SQP5 (TQ5, A0, A1);
  xor SQX17 (TQ6, TQ4, TQ5);
  xor SQX19 (TQk, TQh, TQi);
  xor SQX21 (TQv, GND, GND);
  xor SQX23 (TQ18, TQ15, TQ16);
  xor SQX25 (TQ1m, TQ1j, TQ1k);
  xor SQX27 (TQ1w, GND, GND);
  xor SQX29 (TQ29, TQ26, TQ27);
  xor SQX31 (TQ2n, TQ2k, TQ2l);
  xor SQX33 (TQ2y, GND, GND);
  and SQP6 (TQb, A1, A1);
  xor SQS17 (P1, TQ6, GND);
  xor SQS19 (TQ15, TQk, TQj);
  xor SQS21 (TQ1j, TQv, TQu);
  xor SQS23 (TQ20, TQ18, TQ17);
  xor SQS25 (TQ2d, TQ1m, TQ1l);
  xor SQS27 (TQ2r, TQ1w, TQ1v);
  xor SQS29 (P4, TQ29, TQ28);
  xor SQS31 (P6, TQ2n, TQ2m);
  // XOR_Gate SQS33 has open pins: in0=TQ2y, in1=TQ2x, out=open
  and SQP7 (TQi, A2, A1);
  and SQA17 (TQ7, TQ4, TQ5);
  and SQA19 (TQl, TQh, TQi);
  and SQA21 (TQw, GND, GND);
  and SQA23 (TQ19, TQ15, TQ16);
  and SQA25 (TQ1n, TQ1j, TQ1k);
  and SQA27 (TQ1x, GND, GND);
  and SQA29 (TQ2a, TQ26, TQ27);
  and SQA31 (TQ2o, TQ2k, TQ2l);
  and SQA33 (TQ2z, GND, GND);
  and SQP8 (TQo, A3, A1);
  and SQB17 (TQ8, GND, TQ6);
  and SQB19 (TQm, TQj, TQk);
  and SQB21 (TQx, TQu, TQv);
  and SQB23 (TQ1a, TQ17, TQ18);
  and SQB25 (TQ1o, TQ1l, TQ1m);
  and SQB27 (TQ1y, TQ1v, TQ1w);
  and SQB29 (TQ2b, TQ28, TQ29);
  and SQB31 (TQ2p, TQ2m, TQ2n);
  and SQB33 (TQ30, TQ2x, TQ2y);
  and SQP9 (TQ10, A0, A2);
  or SQO17 (TQ9, TQ7, TQ8);
  or SQO19 (TQn, TQl, TQm);
  or SQO21 (TQy, TQw, TQx);
  or SQO23 (TQ1b, TQ19, TQ1a);
  or SQO25 (TQ1p, TQ1n, TQ1o);
  or SQO27 (TQ1z, TQ1x, TQ1y);
  or SQO29 (TQ2c, TQ2a, TQ2b);
  or SQO31 (TQ2q, TQ2o, TQ2p);
  or SQO33 (TQ31, TQ2z, TQ30);
  and SQP10 (TQ16, A1, A2);
  or SQG17 (TQc, TQ9, GND);
  or SQG19 (TQp, TQn, GND);
  // OR_Gate SQG21 has open pins: in0=TQy, in1=GND, out=open
  or SQG23 (TQ1e, TQ1b, GND);
  or SQG25 (TQ1q, TQ1p, GND);
  // OR_Gate SQG27 has open pins: in0=TQ1z, in1=GND, out=open
  or SQG29 (TQ2f, TQ2c, GND);
  or SQG31 (TQ2s, TQ2q, GND);
  or SQG33 (TQ32, TQ31, GND);
  and SQP11 (TQ1d, A2, A2);
  xor SQX18 (TQd, TQa, TQb);
  xor SQX20 (TQq, GND, TQo);
  xor SQX22 (TQ11, TQz, TQ10);
  xor SQX24 (TQ1f, TQ1c, TQ1d);
  xor SQX26 (TQ1r, GND, GND);
  xor SQX28 (TQ22, TQ20, TQ21);
  xor SQX30 (TQ2g, TQ2d, TQ2e);
  xor SQX32 (TQ2t, TQ2r, GND);
  xor SQX34 (TQ33, GND, GND);
  and SQP12 (TQ1k, A3, A2);
  xor SQS18 (TQz, TQd, TQc);
  xor SQS20 (TQ1c, TQq, TQp);
  xor SQS22 (P2, TQ11, GND);
  xor SQS24 (TQ26, TQ1f, TQ1e);
  xor SQS26 (TQ2k, TQ1r, TQ1q);
  xor SQS28 (P3, TQ22, GND);
  xor SQS30 (P5, TQ2g, TQ2f);
  xor SQS32 (P7, TQ2t, TQ2s);
  // XOR_Gate SQS34 has open pins: in0=TQ33, in1=TQ32, out=open

  // Other names for the same wires on the sheet: TQ0 = A0; TQ1 = A1; TQ2 = A2; TQ3 = A3; TQ3a = P2; TQ3b = P3;
  //   TQ3c = P4; TQ3d = P5; TQ3e = P6; TQ3f = P7; TQ37 = GND; TQ38 = P0; TQ39 = P1
endmodule
