// Logisim project stopwatch.circ as structural Verilog
module stopwatch (
  input  CLK,
  input  RUN,
  input  RST,
  output Q0,
  output Q1,
  output Q2,
  output Q3,
  output Q4,
  output Q5,
  output Q6
);

  wire SWNR3_out, SWNT_out, SWTA1_out, SWTA2_out, SWTC_out, SWTM2_out, SWTN1_out, SWTNR2_out, SWTW_out,
       SWUM3_out, TQ1, TQ3, TQ4, TQ5, TQ9, TQb, TQc, TQd, TQe, TQf, TQg, TQh, TQj, TQk, TQl, TQm;

  // NOT_Gate SWRN has open pins: in=RUN, out=open
  T_Flip_Flop SWUF0 (.T(TQb), .clk(CLK), .Q(Q0), .reset(RST));  // open: Qn, preset
  T_Flip_Flop SWUF1 (.T(TQc), .clk(CLK), .Q(Q1), .reset(RST));  // open: Qn, preset
  T_Flip_Flop SWUF2 (.T(TQd), .clk(CLK), .Q(Q2), .reset(RST));  // open: Qn, preset
  T_Flip_Flop SWUF3 (.T(TQh), .clk(CLK), .Q(Q3), .reset(RST));  // open: Qn, preset
  T_Flip_Flop SWTF0 (.T(TQk), .clk(CLK), .Q(Q4), .reset(RST));  // open: Qn, preset
  T_Flip_Flop SWTF1 (.T(TQl), .clk(CLK), .Q(Q5), .reset(RST));  // open: Qn, preset
  T_Flip_Flop SWTF2 (.T(TQm), .clk(CLK), .Q(Q6), .reset(RST));  // open: Qn, preset
  not SWUN1 (TQ1, Q1);
  and SWUA1 (TQ3, Q0, TQ1);
  not SWUN2 (TQ4, Q2);
  and SWUA2 (TQ5, TQ3, TQ4);
  and SWUA3 (TQj, TQ5, Q3);
  not SWNA (TQ9, TQj);
  and SWUC (TQf, TQ9, RUN);
  and SWUW (TQg, TQj, RUN);
  or SWT0 (TQb, TQf, TQg);
  and SWUM1 (TQc, Q0, TQf);
  and SWNR2 (TQe, Q0, Q1);
  and SWUM2 (TQd, TQe, TQf);
  and SWNR3 (SWNR3_out, TQe, Q2);
  and SWUM3 (SWUM3_out, SWNR3_out, TQf);
  or SWUO3 (TQh, SWUM3_out, TQg);
  and SWTE (TQk, RUN, TQj);
  not SWTN1 (SWTN1_out, Q5);
  and SWTA1 (SWTA1_out, Q4, SWTN1_out);
  and SWTA2 (SWTA2_out, SWTA1_out, Q6);
  not SWNT (SWNT_out, SWTA2_out);
  and SWTW (SWTW_out, TQk, SWTA2_out);
  and SWTC (SWTC_out, TQk, SWNT_out);
  and SWTM1 (TQl, Q4, SWTC_out);
  and SWTNR2 (SWTNR2_out, Q4, Q5);
  and SWTM2 (SWTM2_out, SWTNR2_out, SWTC_out);
  or SWTO2 (TQm, SWTM2_out, SWTW_out);

  // Other names for the same wires on the sheet: TQ0 = Q3; TQ2 = Q4; TQ6 = Q5; TQ7 = CLK; TQ8 = RST; TQa = Q6;
  //   TQi = RUN; TQn = Q0; TQo = Q1; TQp = Q2
endmodule
