// Logisim project subtractor_4bit.circ as structural Verilog
module subtractor_4bit (
  input  A0,
  input  B0,
  input  A1,
  input  B1,
  input  A2,
  input  B2,
  input  A3,
  input  B3,
  input  Bin,
  output D0,
  output D1,
  output D2,
  output D3,
  output Bout
);

  wire SUB1C_out, SUB2A_out, SUB2B_out, SUB2C_out, SUB2N_out, SUB2O_out, SUB2X_out, SUB3A_out, SUB3B_out,
       SUB3N_out, SUB3O_out, SUB3X_out, TQ8, TQa, TQb, TQd, TQe, TQf, TQh, TQi, TQj, TQk, TQl;

  xor SUB0X (TQ8, A0, B0);
  xor SUB0D (D0, TQ8, Bin);
  not SUB0N (TQa, A0);
  or SUB0O (TQb, B0, Bin);
  and SUB0A (TQd, TQa, TQb);
  and SUB0B (TQe, B0, Bin);
  or SUB0C (TQj, TQd, TQe);
  xor SUB1X (TQf, A1, B1);
  xor SUB1D (D1, TQf, TQj);
  not SUB1N (TQh, A1);
  or SUB1O (TQi, B1, TQj);
  and SUB1A (TQk, TQh, TQi);
  and SUB1B (TQl, B1, TQj);
  or SUB1C (SUB1C_out, TQk, TQl);
  xor SUB2X (SUB2X_out, A2, B2);
  xor SUB2D (D2, SUB2X_out, SUB1C_out);
  not SUB2N (SUB2N_out, A2);
  or SUB2O (SUB2O_out, B2, SUB1C_out);
  and SUB2A (SUB2A_out, SUB2N_out, SUB2O_out);
  and SUB2B (SUB2B_out, B2, SUB1C_out);
  or SUB2C (SUB2C_out, SUB2A_out, SUB2B_out);
  xor SUB3X (SUB3X_out, A3, B3);
  xor SUB3D (D3, SUB3X_out, SUB2C_out);
  not SUB3N (SUB3N_out, A3);
  or SUB3O (SUB3O_out, B3, SUB2C_out);
  and SUB3A (SUB3A_out, SUB3N_out, SUB3O_out);
  and SUB3B (SUB3B_out, B3, SUB2C_out);
  or SUB3C (Bout, SUB3A_out, SUB3B_out);

  // Other names for the same wires on the sheet: TQ0 = A0; TQ1 = B0; TQ2 = A1; TQ3 = B1; TQ4 = A2; TQ5 = B2; TQ6 = A3;
  //   TQ7 = B3; TQ9 = D0; TQc = Bin; TQg = D1; TQm = D2; TQn = D3; TQo = Bout
endmodule
