// Logisim project subtractor_8bit.circ as structural Verilog
module subtractor_8bit (
  input  A0,
  input  B0,
  input  A1,
  input  B1,
  input  A2,
  input  B2,
  input  A3,
  input  B3,
  input  A4,
  input  B4,
  input  A5,
  input  B5,
  input  A6,
  input  B6,
  input  A7,
  input  B7,
  input  Bin,
  output D0,
  output D1,
  output D2,
  output D3,
  output D4,
  output D5,
  output D6,
  output D7,
  output Bout
);

  wire SUB5C_out, SUB6A_out, SUB6B_out, SUB6C_out, SUB6N_out, SUB6O_out, SUB6X_out, SUB7A_out, SUB7B_out,
       SUB7N_out, SUB7O_out, SUB7X_out, TQ1a, TQ1b, TQ1c, TQ1d, TQ1e, TQ1f, TQ1h, TQ1i, TQ1j, TQ1k, TQ1l,
       TQ10, TQ11, TQ13, TQ14, TQ15, TQ16, TQ17, TQ18, TQg, TQi, TQj, TQl, TQm, TQn, TQp, TQq, TQr, TQs, TQt,
       TQu, TQw, TQx, TQy, TQz;

  xor SUB0X (TQg, A0, B0);
  xor SUB0D (D0, TQg, Bin);
  not SUB0N (TQi, A0);
  or SUB0O (TQj, B0, Bin);
  and SUB0A (TQl, TQi, TQj);
  and SUB0B (TQm, B0, Bin);
  or SUB0C (TQr, TQl, TQm);
  xor SUB1X (TQn, A1, B1);
  xor SUB1D (D1, TQn, TQr);
  not SUB1N (TQp, A1);
  or SUB1O (TQq, B1, TQr);
  and SUB1A (TQs, TQp, TQq);
  and SUB1B (TQt, B1, TQr);
  or SUB1C (TQy, TQs, TQt);
  xor SUB2X (TQu, A2, B2);
  xor SUB2D (D2, TQu, TQy);
  not SUB2N (TQw, A2);
  or SUB2O (TQx, B2, TQy);
  and SUB2A (TQz, TQw, TQx);
  and SUB2B (TQ10, B2, TQy);
  or SUB2C (TQ15, TQz, TQ10);
  xor SUB3X (TQ11, A3, B3);
  xor SUB3D (D3, TQ11, TQ15);
  not SUB3N (TQ13, A3);
  or SUB3O (TQ14, B3, TQ15);
  and SUB3A (TQ16, TQ13, TQ14);
  and SUB3B (TQ17, B3, TQ15);
  or SUB3C (TQ1c, TQ16, TQ17);
  xor SUB4X (TQ18, A4, B4);
  xor SUB4D (D4, TQ18, TQ1c);
  not SUB4N (TQ1a, A4);
  or SUB4O (TQ1b, B4, TQ1c);
  and SUB4A (TQ1d, TQ1a, TQ1b);
  and SUB4B (TQ1e, B4, TQ1c);
  or SUB4C (TQ1j, TQ1d, TQ1e);
  xor SUB5X (TQ1f, A5, B5);
  xor SUB5D (D5, TQ1f, TQ1j);
  not SUB5N (TQ1h, A5);
  or SUB5O (TQ1i, B5, TQ1j);
  and SUB5A (TQ1k, TQ1h, TQ1i);
  and SUB5B (TQ1l, B5, TQ1j);
  or SUB5C (SUB5C_out, TQ1k, TQ1l);
  xor SUB6X (SUB6X_out, A6, B6);
  xor SUB6D (D6, SUB6X_out, SUB5C_out);
  not SUB6N (SUB6N_out, A6);
  or SUB6O (SUB6O_out, B6, SUB5C_out);
  and SUB6A (SUB6A_out, SUB6N_out, SUB6O_out);
  and SUB6B (SUB6B_out, B6, SUB5C_out);
  or SUB6C (SUB6C_out, SUB6A_out, SUB6B_out);
  xor SUB7X (SUB7X_out, A7, B7);
  xor SUB7D (D7, SUB7X_out, SUB6C_out);
  not SUB7N (SUB7N_out, A7);
  or SUB7O (SUB7O_out, B7, SUB6C_out);
  and SUB7A (SUB7A_out, SUB7N_out, SUB7O_out);
  and SUB7B (SUB7B_out, B7, SUB6C_out);
  or SUB7C (Bout, SUB7A_out, SUB7B_out);

  // Other names for the same wires on the sheet: TQ0 = A0; TQ1 = B0; TQ1g = D5; TQ1m = D6; TQ1n = D7; TQ1o = Bout;
  //   TQ2 = A1; TQ3 = B1; TQ4 = A2; TQ5 = B2; TQ6 = A3; TQ7 = B3; TQ8 = A4; TQ9 = B4; TQ12 = D3; TQ19 = D4; TQa = A5;
  //   TQb = B5; TQc = A6; TQd = B6; TQe = A7; TQf = B7; TQh = D0; TQk = Bin; TQo = D1; TQv = D2
endmodule
