// Logisim project traffic_light.circ as structural Verilog
module traffic_light (
  input  CLK,
  input  EN,
  input  RST,
  output RED,
  output YELLOW,
  output GREEN
);

  wire N2_out, U1_q, U2_q;

  T_Flip_Flop U1 (.T(EN), .clk(CLK), .Q(U1_q), .reset(RST), .preset(RST));  // open: Qn
  T_Flip_Flop U2 (.T(U1_q), .clk(CLK), .Q(U2_q), .reset(RST), .preset(RST));  // open: Qn
  not N1 (GREEN, U2_q);
  not N2 (N2_out, U1_q);
  and R1 (RED, U2_q, U1_q);
  and Y1 (YELLOW, U2_q, N2_out);
endmodule
