// Logisim project tristate_buffer.circ as structural Verilog
module tristate_buffer (
  input  A,
  input  nG,
  output Y
);

  _74125 U1 (.pin1(nG), .pin2(A), .pin3(Y), .pin13(A), .pin12(Y));  // open: pin4, pin5, pin6, pin11, pin10, pin9, pin8
endmodule
