// Logisim project ttl_74138.circ as structural Verilog
module ttl_74138 (
  input  A,
  input  B,
  input  C,
  input  nG2A_Enable,
  input  nG2B_Enable,
  input  G1_Enable,
  output nY7,
  output nY6,
  output nY5,
  output nY4,
  output nY3,
  output nY2,
  output nY1,
  output nY0
);

  _74138 u_74138_1 (
    .pin1(A), .pin2(B), .pin3(B), .pin4(B), .pin5(nG2B_Enable), .pin6(B), .pin7(nY5), .pin15(B), .pin14(B),
    .pin13(B), .pin12(nG2B_Enable), .pin11(B), .pin10(nY5), .pin9(A));

  assign C = B;
  assign G1_Enable = B;
  assign nG2A_Enable = B;
  assign nY0 = B;
  assign nY1 = B;
  assign nY2 = B;
  assign nY3 = nG2B_Enable;
  assign nY4 = B;
  assign nY6 = A;
  assign nY7 = nY5;
endmodule
