// Logisim project ttl_74151_macro.circ as structural Verilog: 1 circuit, main circuit main
module main (
  input  D0,
  input  D1,
  input  D2,
  input  D3,
  input  D4,
  input  D5,
  input  D6,
  input  D7,
  input  S0,
  input  S1,
  input  S2,
  input  nG,
  output Y,
  output nW
);

  wire EN, nS0, nS1, nS2, O01, O03, O23, O45, O47, O67, P0_A, P0_B, P0_C, P1_A, P1_B, P1_C, P2_A, P2_B, P2_C,
       P3_A, P3_B, P3_C, P4_A, P4_B, P4_C, P5_A, P5_B, P5_C, P6_A, P6_B, P6_C, P7_A, P7_B, P7_C, T0, T1, T2,
       T3, T4, T5, T6, T7;

  not not_1 (nS0, S0);
  not not_2 (nS1, S1);
  not not_3 (nS2, S2);
  not not_4 (EN, nG);
  and and_1 (P0_A, EN, D0);
  and and_2 (P1_A, EN, D1);
  and and_3 (P2_A, EN, D2);
  and and_4 (P3_A, EN, D3);
  and and_5 (P4_A, EN, D4);
  and and_6 (P5_A, EN, D5);
  and and_7 (P6_A, EN, D6);
  and and_8 (P7_A, EN, D7);
  and and_9 (P0_B, P0_A, nS0);
  and and_10 (P1_B, P1_A, S0);
  and and_11 (P2_B, P2_A, nS0);
  and and_12 (P3_B, P3_A, S0);
  and and_13 (P4_B, P4_A, nS0);
  and and_14 (P5_B, P5_A, S0);
  and and_15 (P6_B, P6_A, nS0);
  and and_16 (P7_B, P7_A, S0);
  and and_17 (P0_C, P0_B, nS1);
  and and_18 (P1_C, P1_B, nS1);
  and and_19 (P2_C, P2_B, S1);
  and and_20 (P3_C, P3_B, S1);
  and and_21 (P4_C, P4_B, nS1);
  and and_22 (P5_C, P5_B, nS1);
  and and_23 (P6_C, P6_B, S1);
  and and_24 (P7_C, P7_B, S1);
  and and_25 (T0, P0_C, nS2);
  and and_26 (T1, P1_C, nS2);
  and and_27 (T2, P2_C, nS2);
  and and_28 (T3, P3_C, nS2);
  not not_5 (nW, Y);
  and and_29 (T4, P4_C, S2);
  and and_30 (T5, P5_C, S2);
  and and_31 (T6, P6_C, S2);
  and and_32 (T7, P7_C, S2);
  or or_1 (O01, T0, T1);
  or or_2 (O23, T2, T3);
  or or_3 (O45, T4, T5);
  or or_4 (O67, T6, T7);
  or or_5 (O03, O01, O23);
  or or_6 (O47, O45, O67);
  or or_7 (Y, O03, O47);
endmodule
