// Logisim project ttl_74161.circ as structural Verilog
module ttl_74161 (
  input  MR_CLR,
  input  CP_CLK,
  input  D0_A,
  input  D1_B,
  input  D2_C,
  input  D3_D,
  input  CE_ENP,
  input  PE_LOAD,
  input  CET_ENT,
  output Q3_QD,
  output Q2_QC,
  output A1_QB,
  output A0_QA,
  output TC_RC0
);

  _74161 u_74161_1 (
    .pin1(CE_ENP), .pin2(CP_CLK), .pin3(CP_CLK), .pin4(CP_CLK), .pin5(D2_C), .pin6(CP_CLK), .pin7(CE_ENP),
    .pin15(CP_CLK), .pin14(CP_CLK), .pin13(CP_CLK), .pin12(D2_C), .pin11(CP_CLK), .pin10(CE_ENP),
    .pin9(CE_ENP));

  assign A0_QA = CP_CLK;
  assign A1_QB = CP_CLK;
  assign CET_ENT = CE_ENP;
  assign D0_A = CP_CLK;
  assign D1_B = CP_CLK;
  assign D3_D = CP_CLK;
  assign MR_CLR = CE_ENP;
  assign PE_LOAD = CE_ENP;
  assign Q2_QC = D2_C;
  assign Q3_QD = CP_CLK;
  assign TC_RC0 = CP_CLK;
endmodule
