// Logisim project ttl_7464.circ as structural Verilog
module ttl_7464 (
  input  A,
  input  E,
  input  F,
  input  G,
  input  H,
  input  I,
  input  J,
  input  K,
  input  B,
  input  C,
  input  D,
  output Y
);

  // _7464 7464_1: pin names not known; wires that end beside it: A, A, A, H, A, Y

  assign B = A;
  assign C = A;
  assign D = A;
  assign E = A;
  assign F = A;
  assign G = A;
  assign I = A;
  assign J = A;
  assign K = H;
endmodule
