// Logisim project two_bit_ripple_adder.circ as structural Verilog
module two_bit_ripple_adder (
  input  [1:0] A_1_0,
  input  [1:0] B_1_0,
  input  Cin,
  output [1:0] S_1_0,
  output Cout
);

  Adder #(.width(2)) adder_1 (.a(A_1_0), .b(B_1_0), .out(S_1_0), .cin(Cin), .cout(Cout));
endmodule
