// Logisim project updown_counter_4bit.circ as structural Verilog
module updown_counter_4bit (
  input  UD,
  input  EN,
  input  RST,
  output Q0,
  output Q1,
  output Q2,
  output Q3
);

  wire AD2_out, AD3_out, AU2_out, AU3_out, CLK_out, N1_out, N2_out, N3_out, N4_out, TD2_out, TD3_out,
       TO2_out, TO3_out, TU2_out, TU3_out, X1_out;

  Clock CLK (.out(CLK_out));
  not N1 (N1_out, UD);
  T_Flip_Flop U1 (.T(EN), .clk(CLK_out), .Q(Q0), .reset(RST), .preset(RST));  // open: Qn
  not N2 (N2_out, Q0);
  T_Flip_Flop U2 (.T(X1_out), .clk(CLK_out), .Q(Q1), .reset(RST), .preset(RST));  // open: Qn
  not N3 (N3_out, Q1);
  T_Flip_Flop U3 (.T(TO2_out), .clk(CLK_out), .Q(Q2), .reset(RST), .preset(RST));  // open: Qn
  not N4 (N4_out, Q2);
  T_Flip_Flop U4 (.T(TO3_out), .clk(CLK_out), .Q(Q3), .reset(RST), .preset(RST));  // open: Qn
  xor X1 (X1_out, Q0, UD);
  and AU2 (AU2_out, Q0, Q1);
  and AD2 (AD2_out, N2_out, N3_out);
  and TU2 (TU2_out, N1_out, AU2_out);
  and TD2 (TD2_out, UD, AD2_out);
  or TO2 (TO2_out, TU2_out, TD2_out);
  and AU3 (AU3_out, AU2_out, Q2);
  and AD3 (AD3_out, AD2_out, N4_out);
  and TU3 (TU3_out, N1_out, AU3_out);
  and TD3 (TD3_out, UD, AD3_out);
  or TO3 (TO3_out, TU3_out, TD3_out);
endmodule
