// Logisim project vending_machine.circ as structural Verilog
module vending_machine (
  input  RST,
  input  A,
  input  B,
  output DONE
);

  wire AH2_out, NC2_out, O114_out, O115_out, O116_out, O117_out, O118_out, O119_out, O120_out, O121_out,
       O122_out, O123_out, O124_out, TQ0, TQ1, TQ1a, TQ1b, TQ1c, TQ1d, TQ1e, TQ1f, TQ1g, TQ1h, TQ1i, TQ1j,
       TQ1k, TQ1l, TQ1m, TQ1n, TQ1o, TQ1p, TQ1q, TQ1r, TQ1s, TQ1t, TQ1u, TQ1v, TQ1w, TQ1x, TQ1y, TQ1z, TQ2,
       TQ2a, TQ2b, TQ2c, TQ2d, TQ2e, TQ2f, TQ2g, TQ2h, TQ2i, TQ2j, TQ2k, TQ2l, TQ2m, TQ2n, TQ2o, TQ2p, TQ2q,
       TQ2r, TQ2s, TQ2t, TQ2u, TQ2v, TQ2w, TQ2x, TQ2y, TQ2z, TQ3, TQ3a, TQ3b, TQ3c, TQ3d, TQ3e, TQ3f, TQ3g,
       TQ3h, TQ3i, TQ3j, TQ3k, TQ5, TQ6, TQ7, TQ8, TQ9, TQ10, TQ11, TQ12, TQ13, TQ14, TQ15, TQ16, TQ17, TQ18,
       TQ19, TQ20, TQ21, TQ22, TQ24, TQ26, TQ27, TQ28, TQ29, TQ30, TQ31, TQ32, TQ33, TQ34, TQ35, TQ36, TQ37,
       TQ38, TQ39, TQa, TQb, TQc, TQd, TQe, TQf, TQg, TQi, TQj, TQk, TQl, TQm, TQn, TQo, TQp, TQq, TQr, TQs,
       TQt, TQu, TQv, TQw, TQx, TQy, TQz;

  Clock CLK (.out(TQ3));
  D_Flip_Flop U1 (.D(TQ2o), .clk(TQ3), .Q(TQ2k), .reset(RST));  // open: Qn, preset
  D_Flip_Flop U2 (.D(TQ37), .clk(TQ3), .Q(TQ33), .reset(RST));  // open: Qn, preset
  D_Flip_Flop U3 (.D(TQd), .clk(TQ3), .Q(TQa), .reset(RST));  // open: Qn, preset
  not N1 (TQ1z, TQ2k);
  not N2 (TQ20, TQ33);
  not N3 (TQ1k, TQa);
  not NIa (TQ1y, A);
  not NIb (TQ1t, B);
  and M0 (TQ9, TQ1z, TQ20);
  // AND_Gate M1 has open pins: in0=TQ9, in1=TQ1k, out=open
  and A2 (TQc, TQ1z, TQ20);
  and A3 (TQf, TQc, TQ1k);
  and A4 (TQi, TQf, TQ1t);
  and A5 (TQ3a, TQi, A);
  and A6 (TQj, TQ1z, TQ20);
  and A7 (TQk, TQj, TQ1k);
  and A8 (TQl, TQk, B);
  and A9 (TQ3b, TQl, TQ1y);
  and A10 (TQm, TQ1z, TQ20);
  and A11 (TQn, TQm, TQ1k);
  and A12 (TQo, TQn, B);
  and A13 (TQ3d, TQo, A);
  and M14 (TQp, TQ2k, TQ20);
  // AND_Gate M15 has open pins: in0=TQp, in1=TQ1k, out=open
  and A16 (TQq, TQ2k, TQ20);
  and A17 (TQr, TQq, TQ1k);
  and A18 (TQs, TQr, TQ1t);
  and A19 (TQ3f, TQs, A);
  and A20 (TQt, TQ2k, TQ20);
  and A21 (TQu, TQt, TQ1k);
  and A22 (TQv, TQu, B);
  and A23 (TQ3h, TQv, TQ1y);
  and A24 (TQw, TQ2k, TQ20);
  and A25 (TQx, TQw, TQ1k);
  and A26 (TQy, TQx, B);
  and A27 (TQ3i, TQy, A);
  and M28 (TQz, TQ1z, TQ33);
  // AND_Gate M29 has open pins: in0=TQz, in1=TQ1k, out=open
  and A30 (TQ10, TQ1z, TQ33);
  and A31 (TQ11, TQ10, TQ1k);
  and A32 (TQ12, TQ11, TQ1t);
  and A33 (TQ3j, TQ12, A);
  and A34 (TQ13, TQ1z, TQ33);
  and A35 (TQ14, TQ13, TQ1k);
  and A36 (TQ15, TQ14, B);
  and A37 (TQ38, TQ15, TQ1y);
  and A38 (TQ16, TQ1z, TQ33);
  and A39 (TQ17, TQ16, TQ1k);
  and A40 (TQ18, TQ17, B);
  and A41 (TQ39, TQ18, A);
  and M42 (TQ19, TQ2k, TQ33);
  and M43 (TQe, TQ19, TQ1k);
  and A44 (TQ1a, TQ2k, TQ33);
  and A45 (TQ1b, TQ1a, TQ1k);
  and A46 (TQ1c, TQ1b, TQ1t);
  and A47 (TQ3k, TQ1c, TQ1y);
  and A48 (TQ1d, TQ2k, TQ33);
  and A49 (TQ1e, TQ1d, TQ1k);
  and A50 (TQ1f, TQ1e, TQ1t);
  and A51 (TQ0, TQ1f, A);
  and A52 (TQ1g, TQ2k, TQ33);
  and A53 (TQ1h, TQ1g, TQ1k);
  and A54 (TQ1i, TQ1h, B);
  and A55 (TQ1, TQ1i, TQ1y);
  and A56 (TQ1j, TQ2k, TQ33);
  and A57 (TQ1l, TQ1j, TQ1k);
  and A58 (TQ1m, TQ1l, B);
  and A59 (TQ2, TQ1m, A);
  and M60 (TQ1n, TQ1z, TQ20);
  and M61 (TQg, TQ1n, TQa);
  and A62 (TQ1o, TQ1z, TQ20);
  and A63 (TQ1p, TQ1o, TQa);
  and A64 (TQ1q, TQ1p, TQ1t);
  and A65 (TQ5, TQ1q, TQ1y);
  and A66 (TQ1r, TQ1z, TQ20);
  and A67 (TQ1s, TQ1r, TQa);
  and A68 (TQ1u, TQ1s, TQ1t);
  and A69 (TQ6, TQ1u, A);
  and A70 (TQ1v, TQ1z, TQ20);
  and A71 (TQ1w, TQ1v, TQa);
  and A72 (TQ1x, TQ1w, B);
  and A73 (TQ7, TQ1x, TQ1y);
  and A74 (TQ21, TQ1z, TQ20);
  and A75 (TQ22, TQ21, TQa);
  and A76 (TQ24, TQ22, B);
  and A77 (TQ8, TQ24, A);
  or O78 (TQ26, TQ3a, TQ3h);
  or O79 (TQ27, TQ26, TQ3i);
  or O80 (TQ2m, TQ27, TQ3j);
  or O81 (TQ28, TQ3b, TQ3d);
  or O82 (TQ29, TQ28, TQ3f);
  or O83 (TQ2a, TQ29, TQ38);
  or O84 (TQ2b, TQ2a, TQ39);
  or O85 (TQ2c, TQ2b, TQ3k);
  or O86 (TQ2d, TQ2c, TQ0);
  or O87 (TQ2e, TQ2d, TQ1);
  or O88 (TQ2f, TQ2e, TQ2);
  or O89 (TQ2g, TQ2f, TQ5);
  or O90 (TQ2h, TQ2g, TQ6);
  or O91 (TQ2i, TQ2h, TQ7);
  or O92 (TQ2j, TQ2i, TQ8);
  not NC0 (TQ2l, TQ2j);
  and AH0 (TQ2n, TQ2k, TQ2l);
  or O93 (TQ2o, TQ2m, TQ2n);
  or O94 (TQ2p, TQ3b, TQ3d);
  or O95 (TQ2q, TQ2p, TQ3f);
  or O96 (TQ2r, TQ2q, TQ3h);
  or O97 (TQ2s, TQ2r, TQ3i);
  or O98 (TQ35, TQ2s, TQ3j);
  or O99 (TQ2t, TQ3a, TQ38);
  or O100 (TQ2u, TQ2t, TQ39);
  or O101 (TQ2v, TQ2u, TQ3k);
  or O102 (TQ2w, TQ2v, TQ0);
  or O103 (TQ2x, TQ2w, TQ1);
  or O104 (TQ2y, TQ2x, TQ2);
  or O105 (TQ2z, TQ2y, TQ5);
  or O106 (TQ30, TQ2z, TQ6);
  or O107 (TQ31, TQ30, TQ7);
  or O108 (TQ32, TQ31, TQ8);
  not NC1 (TQ34, TQ32);
  and AH1 (TQ36, TQ33, TQ34);
  or O109 (TQ37, TQ35, TQ36);
  or O110 (TQb, TQ38, TQ39);
  or O111 (TQ3c, TQ3a, TQ3b);
  or O112 (TQ3e, TQ3c, TQ3d);
  or O113 (TQ3g, TQ3e, TQ3f);
  or O114 (O114_out, TQ3g, TQ3h);
  or O115 (O115_out, O114_out, TQ3i);
  or O116 (O116_out, O115_out, TQ3j);
  or O117 (O117_out, O116_out, TQ3k);
  or O118 (O118_out, O117_out, TQ0);
  or O119 (O119_out, O118_out, TQ1);
  or O120 (O120_out, O119_out, TQ2);
  or O121 (O121_out, O120_out, TQ5);
  or O122 (O122_out, O121_out, TQ6);
  or O123 (O123_out, O122_out, TQ7);
  or O124 (O124_out, O123_out, TQ8);
  not NC2 (NC2_out, O124_out);
  and AH2 (AH2_out, TQa, NC2_out);
  or O125 (TQd, TQb, AH2_out);
  or Ofo126 (DONE, TQe, TQg);

  // Other names for the same wires on the sheet: TQ4 = RST; TQ23 = B; TQ25 = A; TQh = DONE
endmodule
