// Logisim project washing_machine.circ as structural Verilog
module washing_machine (
  input  RST,
  input  START,
  input  FILL,
  input  EMPTY,
  input  AG4,
  input  SP4,
  output FILLV,
  output AGIT,
  output DRAINV,
  output SPIN
);

  wire AH0_out, AH1_out, AH2_out, NC1_out, NC2_out, O49_out, O50_out, O51_out, O53_out, O54_out, O55_out,
       TQ0, TQ1, TQ1a, TQ1b, TQ1c, TQ1d, TQ1e, TQ1f, TQ1g, TQ1h, TQ1i, TQ1j, TQ1l, TQ1m, TQ1n, TQ1o, TQ1p,
       TQ1q, TQ1r, TQ1s, TQ1t, TQ1u, TQ1v, TQ1w, TQ2, TQ3, TQ4, TQ6, TQ7, TQ8, TQ10, TQ11, TQ12, TQ13, TQ14,
       TQ15, TQ16, TQ17, TQ18, TQd, TQe, TQf, TQg, TQh, TQi, TQj, TQl, TQm, TQn, TQp, TQq, TQr, TQs, TQt,
       TQu, TQv, TQw, TQy, TQz;

  Clock CLK (.out(TQ3));
  D_Flip_Flop U1 (.D(TQ1u), .clk(TQ3), .Q(TQ1r), .reset(RST));  // open: Qn, preset
  D_Flip_Flop U2 (.D(TQ1w), .clk(TQ3), .Q(TQ1v), .reset(RST));  // open: Qn, preset
  D_Flip_Flop U3 (.D(TQ8), .clk(TQ3), .Q(TQ6), .reset(RST));  // open: Qn, preset
  not N1 (TQ1c, TQ1r);
  not N2 (TQ1d, TQ1v);
  not N3 (TQ13, TQ6);
  not NIstart (TQ1o, START);
  not NIfill (TQ1g, FILL);
  not NIempty (TQ1m, EMPTY);
  not NIag4 (TQ1i, AG4);
  not NIsp4 (TQ17, SP4);
  and M0 (TQd, TQ1c, TQ1d);
  // AND_Gate M1 has open pins: in0=TQd, in1=TQ13, out=open
  and A2 (TQe, TQ1c, TQ1d);
  and A3 (TQf, TQe, TQ13);
  and A4 (TQg, TQf, TQ1g);
  and A5 (TQh, TQg, TQ1i);
  and A6 (TQi, TQh, TQ17);
  and A7 (TQj, TQi, TQ1m);
  and A8 (TQ0, TQj, START);
  and M9 (TQl, TQ1r, TQ1d);
  and M10 (FILLV, TQl, TQ13);
  and A11 (TQm, TQ1r, TQ1d);
  and A12 (TQn, TQm, TQ13);
  and A13 (TQp, TQn, FILL);
  and A14 (TQq, TQp, TQ1i);
  and A15 (TQr, TQq, TQ17);
  and A16 (TQs, TQr, TQ1m);
  and A17 (TQ1, TQs, TQ1o);
  and M18 (TQt, TQ1c, TQ1v);
  and M19 (AGIT, TQt, TQ13);
  and A20 (TQu, TQ1c, TQ1v);
  and A21 (TQv, TQu, TQ13);
  and A22 (TQw, TQv, TQ1g);
  and A23 (TQy, TQw, AG4);
  and A24 (TQz, TQy, TQ17);
  and A25 (TQ10, TQz, TQ1m);
  and A26 (TQ2, TQ10, TQ1o);
  and M27 (TQ11, TQ1r, TQ1v);
  and M28 (DRAINV, TQ11, TQ13);
  and A29 (TQ12, TQ1r, TQ1v);
  and A30 (TQ14, TQ12, TQ13);
  and A31 (TQ15, TQ14, TQ1g);
  and A32 (TQ16, TQ15, TQ1i);
  and A33 (TQ18, TQ16, TQ17);
  and A34 (TQ1a, TQ18, EMPTY);
  and A35 (TQ7, TQ1a, TQ1o);
  and M36 (TQ1b, TQ1c, TQ1d);
  and M37 (SPIN, TQ1b, TQ6);
  and A38 (TQ1e, TQ1c, TQ1d);
  and A39 (TQ1f, TQ1e, TQ6);
  and A40 (TQ1h, TQ1f, TQ1g);
  and A41 (TQ1j, TQ1h, TQ1i);
  and A42 (TQ1l, TQ1j, SP4);
  and A43 (TQ1n, TQ1l, TQ1m);
  and A44 (TQ4, TQ1n, TQ1o);
  or O45 (TQ1t, TQ0, TQ2);
  or O46 (TQ1p, TQ1, TQ7);
  or O47 (TQ1q, TQ1p, TQ4);
  not NC0 (TQ1s, TQ1q);
  and AH0 (AH0_out, TQ1r, TQ1s);
  or O48 (TQ1u, TQ1t, AH0_out);
  or O49 (O49_out, TQ1, TQ2);
  or O50 (O50_out, TQ0, TQ7);
  or O51 (O51_out, O50_out, TQ4);
  not NC1 (NC1_out, O51_out);
  and AH1 (AH1_out, TQ1v, NC1_out);
  or O52 (TQ1w, O49_out, AH1_out);
  or O53 (O53_out, TQ0, TQ1);
  or O54 (O54_out, O53_out, TQ2);
  or O55 (O55_out, O54_out, TQ4);
  not NC2 (NC2_out, O55_out);
  and AH2 (AH2_out, TQ6, NC2_out);
  or O56 (TQ8, TQ7, AH2_out);

  // Other names for the same wires on the sheet: TQ1k = SP4; TQ5 = RST; TQ9 = FILLV; TQ19 = EMPTY; TQa = AGIT;
  //   TQb = DRAINV; TQc = SPIN; TQk = START; TQo = FILL; TQx = AG4
endmodule
